// Logisim project Lab_4_cybernetica.circ as structural Verilog: 13 circuits, main circuit Полусумматор
module Lab_4 (
  input  in_1,
  input  in_2,
  input  in_3,
  input  in_4,
  input  [7:0] in_5,
  input  [7:0] in_6,
  input  [7:0] in_7,
  input  [7:0] in_8,
  input  in_9,
  input  [3:0] in_10,
  input  [3:0] in_11,
  input  [3:0] in_12,
  input  [3:0] in_13,
  output out_14,
  output out_15,
  output out_16,
  output out_17,
  output out_18,
  output [7:0] out_19,
  output [7:0] out_20,
  output out_21,
  output [3:0] out_22,
  output [7:0] out_23
);

  \Сумматор_2_бит  \u_сумматор_2_бит_1  (
    .in_1(in_1), .in_2(in_2), .in_3(in_3), .in_4(in_4), .out_5(out_15), .out_7(out_14), .out_6(out_16));
  // Probe on in_10
  // Probe on out_22
  // Probe on in_11
  \Сумматор_4_бит  \u_сумматор_4_бит_1  (.A(in_10), .B(in_11), .out_5(out_22), .in_3(1'b0), .out_4(out_21));
  // Probe on in_5
  \Сумматор_8_бит  \u_сумматор_8_бит_1  (.A(in_5), .B(in_6), .out_5(out_19), .in_3(1'b0), .out_4(out_17));
  // Probe on out_19
  // Probe on in_6
  // Probe on in_12
  \Умножатор_Ам_Ням  \u_умножатор_ам_ням_1  (.A(in_12), .B(in_13), .out_3(out_23));
  // Probe on in_7
  \Вычитатор_Добрый  \u_вычитатор_добрый_1  (.in_3(in_9), .in_1(in_7), .in_2(in_8), .out_4(out_18), .out_5(out_20));
  // Probe on in_13
  // Probe on out_23
  // Probe on in_8
  // Probe on out_20
  // Probe on out_20
endmodule

module \Полусумматор  (
  input  A,
  input  B,
  output Sum,
  output Carry
);

  xor xor_1 (Sum, A, B);
  and and_1 (Carry, A, B);
endmodule

module \Сумматор  (
  input  CI,
  input  A,
  input  B,
  output Sum,
  output CO
);

  wire \полусумматор_1_carry , \полусумматор_1_sum , \полусумматор_2_carry ;

  \Полусумматор  \u_полусумматор_1  (.A(A), .B(B), .Sum(\полусумматор_1_sum ), .Carry(\полусумматор_1_carry ));
  \Полусумматор  \u_полусумматор_2  (.A(CI), .B(\полусумматор_1_sum ), .Sum(Sum), .Carry(\полусумматор_2_carry ));
  or or_1 (CO, \полусумматор_2_carry , \полусумматор_1_carry );
endmodule

module \Сумматор_8_бит  (
  input  [7:0] A,
  input  [7:0] B,
  input  in_3,
  output out_4,
  output [7:0] out_5
);

  wire \сумматор_2_co , \сумматор_3_co , \сумматор_4_co , \сумматор_5_co , \сумматор_6_co , \сумматор_7_co ,
       \сумматор_8_co ;

  // Probe on A
  // Probe on B
  // Probe on out_5
  \Сумматор  \u_сумматор_1  (.CI(\сумматор_2_co ), .A(A[7]), .B(B[7]), .Sum(out_5[7]), .CO(out_4));
  \Сумматор  \u_сумматор_2  (.CI(\сумматор_3_co ), .A(A[6]), .B(B[6]), .Sum(out_5[6]), .CO(\сумматор_2_co ));
  \Сумматор  \u_сумматор_3  (.CI(\сумматор_4_co ), .A(A[5]), .B(B[5]), .Sum(out_5[5]), .CO(\сумматор_3_co ));
  \Сумматор  \u_сумматор_4  (.CI(\сумматор_5_co ), .A(A[4]), .B(B[4]), .Sum(out_5[4]), .CO(\сумматор_4_co ));
  \Сумматор  \u_сумматор_5  (.CI(\сумматор_6_co ), .A(A[3]), .B(B[3]), .Sum(out_5[3]), .CO(\сумматор_5_co ));
  \Сумматор  \u_сумматор_6  (.CI(\сумматор_7_co ), .A(A[2]), .B(B[2]), .Sum(out_5[2]), .CO(\сумматор_6_co ));
  \Сумматор  \u_сумматор_7  (.CI(\сумматор_8_co ), .A(A[1]), .B(B[1]), .Sum(out_5[1]), .CO(\сумматор_7_co ));
  \Сумматор  \u_сумматор_8  (.CI(in_3), .A(A[0]), .B(B[0]), .Sum(out_5[0]), .CO(\сумматор_8_co ));

  // Notes on the sheet:
  //   +
endmodule

module \Сумматор_2_бит  (
  input  in_1,
  input  in_2,
  input  in_3,
  input  in_4,
  output out_5,
  output out_6,
  output out_7
);

  F0 f0_1 (.A(in_1), .B(in_2), .C(in_3), .D(in_4), .out_5(out_6));
  F1 f1_1 (.A(in_1), .B(in_2), .C(in_3), .D(in_4), .out_5(out_5));
  F2 f2_1 (.A(in_1), .B(in_2), .C(in_3), .D(in_4), .out_5(out_7));
endmodule

module F0 (
  input  A,
  input  B,
  input  C,
  input  D,
  output out_5
);

  wire and_1_out, and_2_out, and_3_out, and_4_out, not_1_out, not_2_out, not_3_out, not_4_out, not_5_out,
       not_6_out;

  not not_1 (not_1_out, C);
  not not_2 (not_2_out, D);
  not not_3 (not_3_out, D);
  not not_4 (not_4_out, A);
  not not_5 (not_5_out, B);
  not not_6 (not_6_out, B);
  and and_1 (and_1_out, B, not_1_out, not_2_out);
  and and_2 (and_2_out, B, C, not_3_out);
  and and_3 (and_3_out, not_4_out, not_5_out, D);
  and and_4 (and_4_out, A, not_6_out, D);
  or or_1 (out_5, and_1_out, and_2_out, and_3_out, and_4_out);
endmodule

module F1 (
  input  A,
  input  B,
  input  C,
  input  D,
  output out_5
);

  wire and_1_out, and_2_out, and_3_out, and_4_out, and_5_out, and_6_out, not_1_out, not_2_out, not_3_out,
       not_4_out, not_5_out, not_6_out, not_7_out, not_8_out, not_9_out, not_10_out;

  not not_1 (not_1_out, A);
  not not_2 (not_2_out, B);
  and and_1 (and_1_out, not_1_out, not_2_out, C);
  not not_3 (not_3_out, A);
  and and_2 (and_2_out, not_3_out, C, not_4_out);
  not not_4 (not_4_out, D);
  not not_5 (not_5_out, C);
  and and_3 (and_3_out, A, not_5_out, not_6_out);
  not not_6 (not_6_out, D);
  not not_7 (not_7_out, B);
  and and_4 (and_4_out, A, not_7_out, not_8_out);
  not not_8 (not_8_out, C);
  not not_9 (not_9_out, A);
  and and_5 (and_5_out, not_9_out, B, not_10_out, D);
  not not_10 (not_10_out, C);
  and and_6 (and_6_out, A, B, C, D);
  or or_1 (out_5, and_1_out, and_2_out, and_3_out, and_4_out, and_5_out, and_6_out);
endmodule

module F2 (
  input  A,
  input  B,
  input  C,
  input  D,
  output out_5
);

  wire and_1_out, and_2_out, and_3_out, and_4_out, and_5_out;

  and and_1 (and_1_out, A, C);
  and and_2 (and_2_out, A, B, D);
  and and_3 (and_3_out, B, C, D);
  and and_4 (and_4_out, A, B, C);
  and and_5 (and_5_out, A, C, D);
  or or_1 (out_5, and_1_out, and_2_out, and_3_out, and_4_out, and_5_out);
endmodule

module \Вычитатор_Добрый  (
  input  [7:0] in_1,
  input  [7:0] in_2,
  input  in_3,
  output out_4,
  output [7:0] out_5
);

  wire \сумматор_8_бит_1_out_4 ;
  wire [7:0] \инвертер_для_вычитатора_1_out_3 ;

  xor xor_1 (out_4, in_3, \сумматор_8_бит_1_out_4 );
  // Probe on in_1
  // Probe on in_1
  \Сумматор_8_бит  \u_сумматор_8_бит_1  (
    .A(in_1), .B(\инвертер_для_вычитатора_1_out_3 ), .out_5(out_5), .in_3(in_3),
    .out_4(\сумматор_8_бит_1_out_4 ));
  // Probe on out_5
  // Probe on out_5
  // Probe on \инвертер_для_вычитатора_1_out_3 
  // Probe on \инвертер_для_вычитатора_1_out_3 
  \Инвертер_для_вычитатора  \u_инвертер_для_вычитатора_1  (
    .in_1(in_2), .out_3(\инвертер_для_вычитатора_1_out_3 ), .in_2(in_3));
endmodule

module \Инвертер_для_вычитатора  (
  input  [7:0] in_1,
  input  in_2,
  output [7:0] out_3
);

  xor xor_1 (out_3[0], in_2, in_1[0]);
  xor xor_2 (out_3[1], in_2, in_1[1]);
  xor xor_3 (out_3[2], in_2, in_1[2]);
  xor xor_4 (out_3[3], in_2, in_1[3]);
  xor xor_5 (out_3[4], in_2, in_1[4]);
  xor xor_6 (out_3[5], in_2, in_1[5]);
  xor xor_7 (out_3[6], in_2, in_1[6]);
  xor xor_8 (out_3[7], in_2, in_1[7]);
endmodule

module \Сумматор_4_бит  (
  input  [3:0] A,
  input  [3:0] B,
  input  in_3,
  output out_4,
  output [3:0] out_5
);

  wire \сумматор_2_co , \сумматор_3_co , \сумматор_4_co ;

  // Probe on A
  // Probe on B
  // Probe on out_5
  \Сумматор  \u_сумматор_1  (.CI(\сумматор_2_co ), .A(A[3]), .B(B[3]), .Sum(out_5[3]), .CO(out_4));
  \Сумматор  \u_сумматор_2  (.CI(\сумматор_3_co ), .A(A[2]), .B(B[2]), .Sum(out_5[2]), .CO(\сумматор_2_co ));
  \Сумматор  \u_сумматор_3  (.CI(\сумматор_4_co ), .A(A[1]), .B(B[1]), .Sum(out_5[1]), .CO(\сумматор_3_co ));
  \Сумматор  \u_сумматор_4  (.CI(in_3), .A(A[0]), .B(B[0]), .Sum(out_5[0]), .CO(\сумматор_4_co ));

  // Notes on the sheet:
  //   +
endmodule

module \Умножатор_Ам_Ням  (
  input  [3:0] A,
  input  [3:0] B,
  output [7:0] out_3
);

  wire [2:0] \умножатор_4_out_3 ;
  wire [3:0] \сумматор_4_бит_1_out_5 , \сумматор_4_бит_3_out_5 , \умножатор_1_out_3 , \умножатор_2_out_3 ,
       \умножатор_3_out_3 ;

  // Probe on A
  // Probe on B
  \Умножатор  \u_умножатор_1  (.in_2(B[2]), .in_1(A), .out_3(\умножатор_1_out_3 ));
  \Умножатор  \u_умножатор_2  (.in_2(B[3]), .in_1(A), .out_3(\умножатор_2_out_3 ));
  \Умножатор  \u_умножатор_3  (.in_2(B[1]), .in_1(A), .out_3(\умножатор_3_out_3 ));
  \Сумматор_4_бит  \u_сумматор_4_бит_1  (
    .A(\умножатор_1_out_3 ), .B(\сумматор_4_бит_3_out_5 ), .out_5({\сумматор_4_бит_1_out_5 [2:0], out_3[2]}),
    .in_3(1'b0), .out_4(\сумматор_4_бит_1_out_5 [3]));
  \Сумматор_4_бит  \u_сумматор_4_бит_2  (
    .A(\умножатор_2_out_3 ), .B(\сумматор_4_бит_1_out_5 ), .out_5(out_3[6:3]), .in_3(1'b0), .out_4(out_3[7]));
  \Умножатор  \u_умножатор_4  (.in_2(B[0]), .in_1(A), .out_3({\умножатор_4_out_3 , out_3[0]}));
  \Сумматор_4_бит  \u_сумматор_4_бит_3  (
    .A(\умножатор_3_out_3 ), .B({1'b0, \умножатор_4_out_3 }),
    .out_5({\сумматор_4_бит_3_out_5 [2:0], out_3[1]}), .in_3(1'b0), .out_4(\сумматор_4_бит_3_out_5 [3]));
  // Probe on out_3
endmodule

module \Умножатор  (
  input  [3:0] in_1,
  input  in_2,
  output [3:0] out_3
);

  and and_1 (out_3[3], in_1[3], in_2);
  and and_2 (out_3[2], in_1[2], in_2);
  and and_3 (out_3[0], in_1[0], in_2);
  and and_4 (out_3[1], in_1[1], in_2);
endmodule
