// Logisim project Lab_5_cybernetica_+.circ as structural Verilog: 8 circuits, main circuit Lab_5
module Lab_5 (
  input  _0,
  input  _1,
  input  _2,
  input  _3,
  input  _4,
  input  _5,
  input  _6,
  input  _7,
  input  _8,
  input  _9,
  input  A,
  input  B,
  input  C,
  input  D,
  input  in_15,
  input  E,
  input  F
);

  wire not_1_out, \перевод_в_16_ричную_1_out_18 ;
  wire [3:0] \память_4_бит_1_out_4 , \память_4_бит_2_out_4 , \память_4_бит_3_out_4 , \память_4_бит_4_out_4 ,
       \память_4_бит_5_out_4 , \память_4_бит_6_out_4 , \память_4_бит_7_out_4 , \память_4_бит_8_out_4 ,
       \перевод_в_16_ричную_1_out_17 , \перевод_из_16_ричной_в_7_сегментов_1_out_2 ,
       \перевод_из_16_ричной_в_7_сегментов_1_out_2_2 , \перевод_из_16_ричной_в_7_сегментов_2_out_2 ,
       \перевод_из_16_ричной_в_7_сегментов_2_out_2_2 , \перевод_из_16_ричной_в_7_сегментов_3_out_2 ,
       \перевод_из_16_ричной_в_7_сегментов_3_out_2_2 , \перевод_из_16_ричной_в_7_сегментов_4_out_2 ,
       \перевод_из_16_ричной_в_7_сегментов_4_out_2_2 , \перевод_из_16_ричной_в_7_сегментов_5_out_2 ,
       \перевод_из_16_ричной_в_7_сегментов_5_out_2_2 , \перевод_из_16_ричной_в_7_сегментов_6_out_2 ,
       \перевод_из_16_ричной_в_7_сегментов_6_out_2_2 , \перевод_из_16_ричной_в_7_сегментов_7_out_2 ,
       \перевод_из_16_ричной_в_7_сегментов_7_out_2_2 , \перевод_из_16_ричной_в_7_сегментов_8_out_2 ,
       \перевод_из_16_ричной_в_7_сегментов_8_out_2_2 ;

  \Перевод_в_16_ричную  \u_перевод_в_16_ричную_1  (
    ._0(_0), ._1(_1), ._2(_2), ._3(_3), ._4(_4), ._5(_5), ._6(_6), ._7(_7), ._8(_8), ._9(_9), .A(A), .B(B),
    .C(C), .D(D), .E(E), .F(F), .out_17(\перевод_в_16_ричную_1_out_17 ),
    .out_18(\перевод_в_16_ричную_1_out_18 ));
  not not_1 (not_1_out, \перевод_в_16_ричную_1_out_18 );
  _7_Segment_Display u_7_segment_display_1 (
    .g(\перевод_из_16_ричной_в_7_сегментов_1_out_2_2 [3]),
    .f(\перевод_из_16_ричной_в_7_сегментов_1_out_2_2 [2]),
    .a(\перевод_из_16_ричной_в_7_сегментов_1_out_2_2 [1]),
    .b(\перевод_из_16_ричной_в_7_сегментов_1_out_2_2 [0]),
    .e(\перевод_из_16_ричной_в_7_сегментов_1_out_2 [3]), .d(\перевод_из_16_ричной_в_7_сегментов_1_out_2 [2]),
    .c(\перевод_из_16_ричной_в_7_сегментов_1_out_2 [1]), .dp(\перевод_из_16_ричной_в_7_сегментов_1_out_2 [0]));
  \Перевод_из_16_ричной_в_7_сегментов  \u_перевод_из_16_ричной_в_7_сегментов_1  (
    .in_1(\память_4_бит_1_out_4 ),
    .out_2({\перевод_из_16_ричной_в_7_сегментов_1_out_2 , \перевод_из_16_ричной_в_7_сегментов_1_out_2_2 }));
  // Probe on \память_4_бит_1_out_4 
  \Память_4_бит  \u_память_4_бит_1  (
    .in_1(\память_4_бит_2_out_4 ), .out_4(\память_4_бит_1_out_4 ), .in_2(not_1_out), .in_3(in_15));
  _7_Segment_Display u_7_segment_display_2 (
    .g(\перевод_из_16_ричной_в_7_сегментов_2_out_2_2 [3]),
    .f(\перевод_из_16_ричной_в_7_сегментов_2_out_2_2 [2]),
    .a(\перевод_из_16_ричной_в_7_сегментов_2_out_2_2 [1]),
    .b(\перевод_из_16_ричной_в_7_сегментов_2_out_2_2 [0]),
    .e(\перевод_из_16_ричной_в_7_сегментов_2_out_2 [3]), .d(\перевод_из_16_ричной_в_7_сегментов_2_out_2 [2]),
    .c(\перевод_из_16_ричной_в_7_сегментов_2_out_2 [1]), .dp(\перевод_из_16_ричной_в_7_сегментов_2_out_2 [0]));
  \Перевод_из_16_ричной_в_7_сегментов  \u_перевод_из_16_ричной_в_7_сегментов_2  (
    .in_1(\память_4_бит_2_out_4 ),
    .out_2({\перевод_из_16_ричной_в_7_сегментов_2_out_2 , \перевод_из_16_ричной_в_7_сегментов_2_out_2_2 }));
  // Probe on \память_4_бит_2_out_4 
  \Память_4_бит  \u_память_4_бит_2  (
    .in_1(\память_4_бит_3_out_4 ), .out_4(\память_4_бит_2_out_4 ), .in_2(not_1_out), .in_3(in_15));
  _7_Segment_Display u_7_segment_display_3 (
    .g(\перевод_из_16_ричной_в_7_сегментов_3_out_2_2 [3]),
    .f(\перевод_из_16_ричной_в_7_сегментов_3_out_2_2 [2]),
    .a(\перевод_из_16_ричной_в_7_сегментов_3_out_2_2 [1]),
    .b(\перевод_из_16_ричной_в_7_сегментов_3_out_2_2 [0]),
    .e(\перевод_из_16_ричной_в_7_сегментов_3_out_2 [3]), .d(\перевод_из_16_ричной_в_7_сегментов_3_out_2 [2]),
    .c(\перевод_из_16_ричной_в_7_сегментов_3_out_2 [1]), .dp(\перевод_из_16_ричной_в_7_сегментов_3_out_2 [0]));
  \Перевод_из_16_ричной_в_7_сегментов  \u_перевод_из_16_ричной_в_7_сегментов_3  (
    .in_1(\память_4_бит_3_out_4 ),
    .out_2({\перевод_из_16_ричной_в_7_сегментов_3_out_2 , \перевод_из_16_ричной_в_7_сегментов_3_out_2_2 }));
  // Probe on \память_4_бит_3_out_4 
  \Память_4_бит  \u_память_4_бит_3  (
    .in_1(\память_4_бит_5_out_4 ), .out_4(\память_4_бит_3_out_4 ), .in_2(not_1_out), .in_3(in_15));
  _7_Segment_Display u_7_segment_display_4 (
    .g(\перевод_из_16_ричной_в_7_сегментов_4_out_2_2 [3]),
    .f(\перевод_из_16_ричной_в_7_сегментов_4_out_2_2 [2]),
    .a(\перевод_из_16_ричной_в_7_сегментов_4_out_2_2 [1]),
    .b(\перевод_из_16_ричной_в_7_сегментов_4_out_2_2 [0]),
    .e(\перевод_из_16_ричной_в_7_сегментов_4_out_2 [3]), .d(\перевод_из_16_ричной_в_7_сегментов_4_out_2 [2]),
    .c(\перевод_из_16_ричной_в_7_сегментов_4_out_2 [1]), .dp(\перевод_из_16_ричной_в_7_сегментов_4_out_2 [0]));
  \Перевод_из_16_ричной_в_7_сегментов  \u_перевод_из_16_ричной_в_7_сегментов_4  (
    .in_1(\память_4_бит_5_out_4 ),
    .out_2({\перевод_из_16_ричной_в_7_сегментов_4_out_2 , \перевод_из_16_ричной_в_7_сегментов_4_out_2_2 }));
  // Probe on \память_4_бит_5_out_4 
  _7_Segment_Display u_7_segment_display_5 (
    .g(\перевод_из_16_ричной_в_7_сегментов_5_out_2_2 [3]),
    .f(\перевод_из_16_ричной_в_7_сегментов_5_out_2_2 [2]),
    .a(\перевод_из_16_ричной_в_7_сегментов_5_out_2_2 [1]),
    .b(\перевод_из_16_ричной_в_7_сегментов_5_out_2_2 [0]),
    .e(\перевод_из_16_ричной_в_7_сегментов_5_out_2 [3]), .d(\перевод_из_16_ричной_в_7_сегментов_5_out_2 [2]),
    .c(\перевод_из_16_ричной_в_7_сегментов_5_out_2 [1]), .dp(\перевод_из_16_ричной_в_7_сегментов_5_out_2 [0]));
  \Перевод_из_16_ричной_в_7_сегментов  \u_перевод_из_16_ричной_в_7_сегментов_5  (
    .in_1(\память_4_бит_4_out_4 ),
    .out_2({\перевод_из_16_ричной_в_7_сегментов_5_out_2 , \перевод_из_16_ричной_в_7_сегментов_5_out_2_2 }));
  // Probe on \память_4_бит_4_out_4 
  \Память_4_бит  \u_память_4_бит_4  (
    .in_1(\память_4_бит_6_out_4 ), .out_4(\память_4_бит_4_out_4 ), .in_2(not_1_out), .in_3(in_15));
  \Память_4_бит  \u_память_4_бит_5  (
    .in_1(\память_4_бит_4_out_4 ), .out_4(\память_4_бит_5_out_4 ), .in_2(not_1_out), .in_3(in_15));
  _7_Segment_Display u_7_segment_display_6 (
    .g(\перевод_из_16_ричной_в_7_сегментов_6_out_2_2 [3]),
    .f(\перевод_из_16_ричной_в_7_сегментов_6_out_2_2 [2]),
    .a(\перевод_из_16_ричной_в_7_сегментов_6_out_2_2 [1]),
    .b(\перевод_из_16_ричной_в_7_сегментов_6_out_2_2 [0]),
    .e(\перевод_из_16_ричной_в_7_сегментов_6_out_2 [3]), .d(\перевод_из_16_ричной_в_7_сегментов_6_out_2 [2]),
    .c(\перевод_из_16_ричной_в_7_сегментов_6_out_2 [1]), .dp(\перевод_из_16_ричной_в_7_сегментов_6_out_2 [0]));
  \Перевод_из_16_ричной_в_7_сегментов  \u_перевод_из_16_ричной_в_7_сегментов_6  (
    .in_1(\память_4_бит_6_out_4 ),
    .out_2({\перевод_из_16_ричной_в_7_сегментов_6_out_2 , \перевод_из_16_ричной_в_7_сегментов_6_out_2_2 }));
  // Probe on \память_4_бит_6_out_4 
  \Память_4_бит  \u_память_4_бит_6  (
    .in_1(\память_4_бит_7_out_4 ), .out_4(\память_4_бит_6_out_4 ), .in_2(not_1_out), .in_3(in_15));
  _7_Segment_Display u_7_segment_display_7 (
    .g(\перевод_из_16_ричной_в_7_сегментов_7_out_2_2 [3]),
    .f(\перевод_из_16_ричной_в_7_сегментов_7_out_2_2 [2]),
    .a(\перевод_из_16_ричной_в_7_сегментов_7_out_2_2 [1]),
    .b(\перевод_из_16_ричной_в_7_сегментов_7_out_2_2 [0]),
    .e(\перевод_из_16_ричной_в_7_сегментов_7_out_2 [3]), .d(\перевод_из_16_ричной_в_7_сегментов_7_out_2 [2]),
    .c(\перевод_из_16_ричной_в_7_сегментов_7_out_2 [1]), .dp(\перевод_из_16_ричной_в_7_сегментов_7_out_2 [0]));
  \Перевод_из_16_ричной_в_7_сегментов  \u_перевод_из_16_ричной_в_7_сегментов_7  (
    .in_1(\память_4_бит_7_out_4 ),
    .out_2({\перевод_из_16_ричной_в_7_сегментов_7_out_2 , \перевод_из_16_ричной_в_7_сегментов_7_out_2_2 }));
  // Probe on \память_4_бит_7_out_4 
  \Память_4_бит  \u_память_4_бит_7  (
    .in_1(\память_4_бит_8_out_4 ), .out_4(\память_4_бит_7_out_4 ), .in_2(not_1_out), .in_3(in_15));
  _7_Segment_Display u_7_segment_display_8 (
    .g(\перевод_из_16_ричной_в_7_сегментов_8_out_2_2 [3]),
    .f(\перевод_из_16_ричной_в_7_сегментов_8_out_2_2 [2]),
    .a(\перевод_из_16_ричной_в_7_сегментов_8_out_2_2 [1]),
    .b(\перевод_из_16_ричной_в_7_сегментов_8_out_2_2 [0]),
    .e(\перевод_из_16_ричной_в_7_сегментов_8_out_2 [3]), .d(\перевод_из_16_ричной_в_7_сегментов_8_out_2 [2]),
    .c(\перевод_из_16_ричной_в_7_сегментов_8_out_2 [1]), .dp(\перевод_из_16_ричной_в_7_сегментов_8_out_2 [0]));
  \Перевод_из_16_ричной_в_7_сегментов  \u_перевод_из_16_ричной_в_7_сегментов_8  (
    .in_1(\память_4_бит_8_out_4 ),
    .out_2({\перевод_из_16_ричной_в_7_сегментов_8_out_2 , \перевод_из_16_ричной_в_7_сегментов_8_out_2_2 }));
  // Probe on \память_4_бит_8_out_4 
  \Память_4_бит  \u_память_4_бит_8  (
    .in_1(\перевод_в_16_ричную_1_out_17 ), .out_4(\память_4_бит_8_out_4 ), .in_2(not_1_out), .in_3(in_15));
endmodule

module \Перевод_в_16_ричную  (
  input  _0,
  input  _1,
  input  _2,
  input  _3,
  input  _4,
  input  _5,
  input  _6,
  input  _7,
  input  _8,
  input  _9,
  input  A,
  input  B,
  input  C,
  input  D,
  input  E,
  input  F,
  output [3:0] out_17,
  output out_18
);

  \Бит_0  \u_бит_0_1  (.in_1({F, E, D, C, B, A, _9, _8, _7, _6, _5, _4, _3, _2, _1, _0}), .out_2(out_17[0]));
  \Бит_1  \u_бит_1_1  (.in_1({F, E, D, C, B, A, _9, _8, _7, _6, _5, _4, _3, _2, _1, _0}), .out_2(out_17[1]));
  \Бит_2  \u_бит_2_1  (.in_1({F, E, D, C, B, A, _9, _8, _7, _6, _5, _4, _3, _2, _1, _0}), .out_2(out_17[2]));
  \Бит_3  \u_бит_3_1  (.in_1({F, E, D, C, B, A, _9, _8, _7, _6, _5, _4, _3, _2, _1, _0}), .out_2(out_17[3]));
  or or_1 (out_18, _0, _1, _2, _3, _4, _5, _6, _7, _9, A, B, C, D, E, F, _8);
  // Probe on out_17
endmodule

module \Перевод_из_16_ричной_в_7_сегментов  (
  input  [3:0] in_1,
  output [7:0] out_2
);

  wire and_1_out, and_2_out, and_3_out, and_4_out, and_5_out, and_6_out, and_7_out, and_8_out, and_9_out,
       and_10_out, and_11_out, and_12_out, and_13_out, and_14_out, and_15_out, and_16_out, and_17_out,
       and_18_out, and_19_out, and_20_out, and_21_out, and_22_out, and_23_out, and_24_out, and_25_out,
       and_26_out, and_27_out, and_28_out, and_29_out, and_30_out, and_31_out, and_32_out, and_33_out,
       and_34_out, and_35_out, and_36_out, not_1_out, not_2_out, not_3_out, not_4_out, not_5_out, not_6_out,
       not_7_out, not_8_out, not_9_out, not_10_out, not_11_out, not_12_out, not_13_out, not_14_out,
       not_15_out, not_16_out, not_17_out, not_18_out, not_19_out, not_20_out, not_21_out, not_22_out,
       not_23_out, not_24_out, not_25_out, not_26_out, not_27_out, not_28_out, not_29_out, not_30_out,
       not_31_out, not_32_out, not_33_out, not_34_out, not_35_out, not_36_out, not_37_out, not_38_out,
       not_39_out, not_40_out, not_41_out, not_42_out, not_43_out, not_44_out, not_45_out;

  not not_1 (not_1_out, in_1[2]);
  not not_2 (not_2_out, in_1[0]);
  not not_3 (not_3_out, in_1[0]);
  not not_4 (not_4_out, in_1[3]);
  not not_5 (not_5_out, in_1[2]);
  not not_6 (not_6_out, in_1[0]);
  not not_7 (not_7_out, in_1[2]);
  not not_8 (not_8_out, in_1[1]);
  not not_9 (not_9_out, in_1[0]);
  not not_10 (not_10_out, in_1[1]);
  not not_11 (not_11_out, in_1[3]);
  not not_12 (not_12_out, in_1[1]);
  not not_13 (not_13_out, in_1[3]);
  not not_14 (not_14_out, in_1[1]);
  not not_15 (not_15_out, in_1[3]);
  not not_16 (not_16_out, in_1[2]);
  not not_17 (not_17_out, in_1[2]);
  not not_18 (not_18_out, in_1[0]);
  not not_19 (not_19_out, in_1[3]);
  not not_20 (not_20_out, in_1[1]);
  not not_21 (not_21_out, in_1[2]);
  not not_22 (not_22_out, in_1[1]);
  not not_23 (not_23_out, in_1[0]);
  not not_24 (not_24_out, in_1[3]);
  not not_25 (not_25_out, in_1[1]);
  not not_26 (not_26_out, in_1[0]);
  not not_27 (not_27_out, in_1[2]);
  not not_28 (not_28_out, in_1[2]);
  not not_29 (not_29_out, in_1[0]);
  not not_30 (not_30_out, in_1[3]);
  not not_31 (not_31_out, in_1[3]);
  not not_32 (not_32_out, in_1[2]);
  not not_33 (not_33_out, in_1[1]);
  not not_34 (not_34_out, in_1[0]);
  not not_35 (not_35_out, in_1[3]);
  not not_36 (not_36_out, in_1[2]);
  not not_37 (not_37_out, in_1[3]);
  not not_38 (not_38_out, in_1[1]);
  not not_39 (not_39_out, in_1[0]);
  not not_40 (not_40_out, in_1[2]);
  not not_41 (not_41_out, in_1[1]);
  not not_42 (not_42_out, in_1[2]);
  not not_43 (not_43_out, in_1[0]);
  not not_44 (not_44_out, in_1[3]);
  not not_45 (not_45_out, in_1[1]);
  and and_1 (and_1_out, not_1_out, not_2_out);
  and and_2 (and_2_out, in_1[1], not_3_out);
  and and_3 (and_3_out, in_1[3], in_1[1]);
  and and_4 (and_4_out, in_1[3], in_1[2]);
  and and_5 (and_5_out, not_4_out, not_5_out, not_6_out);
  and and_6 (and_6_out, not_7_out, in_1[1], in_1[0]);
  and and_7 (and_7_out, in_1[2], not_8_out, in_1[0]);
  and and_8 (and_8_out, in_1[2], in_1[1], not_9_out);
  and and_9 (and_9_out, in_1[3], not_10_out);
  and and_10 (and_10_out, not_11_out, not_12_out);
  and and_11 (and_11_out, not_13_out, in_1[0]);
  and and_12 (and_12_out, not_14_out, in_1[0]);
  and and_13 (and_13_out, not_15_out, in_1[2]);
  and and_14 (and_14_out, in_1[3], not_16_out);
  and and_15 (and_15_out, not_17_out, in_1[1]);
  and and_16 (and_16_out, in_1[1], not_18_out);
  and and_17 (and_17_out, not_19_out, in_1[2], not_20_out);
  and and_18 (and_18_out, in_1[3], not_21_out);
  and and_19 (and_19_out, in_1[3], in_1[0]);
  and and_20 (and_20_out, not_22_out, not_23_out);
  and and_21 (and_21_out, not_24_out, in_1[2], not_25_out);
  and and_22 (and_22_out, in_1[2], not_26_out);
  and and_23 (and_23_out, in_1[3], not_27_out);
  and and_24 (and_24_out, in_1[3], in_1[1]);
  and and_25 (and_25_out, not_28_out, not_29_out);
  and and_26 (and_26_out, not_30_out, in_1[1]);
  and and_27 (and_27_out, not_31_out, in_1[2], in_1[0]);
  and and_28 (and_28_out, in_1[2], in_1[1]);
  and and_29 (and_29_out, in_1[3], not_32_out, not_33_out);
  and and_30 (and_30_out, in_1[3], not_34_out);
  and and_31 (and_31_out, not_35_out, not_36_out);
  and and_32 (and_32_out, not_37_out, not_38_out, not_39_out);
  and and_33 (and_33_out, not_40_out, not_41_out);
  and and_34 (and_34_out, not_42_out, not_43_out);
  and and_35 (and_35_out, not_44_out, in_1[1], in_1[0]);
  and and_36 (and_36_out, in_1[3], not_45_out, in_1[0]);
  or or_1 (out_2[7], and_1_out, and_2_out, and_3_out, and_4_out);
  or or_2 (out_2[6], and_5_out, and_6_out, and_7_out, and_8_out, and_9_out);
  or or_3 (out_2[5], and_10_out, and_11_out, and_12_out, and_13_out, and_14_out);
  or or_4 (out_2[3], and_15_out, and_16_out, and_17_out, and_18_out, and_19_out);
  or or_5 (out_2[2], and_20_out, and_21_out, and_22_out, and_23_out, and_24_out);
  or or_6 (out_2[1], and_25_out, and_26_out, and_27_out, and_28_out, and_29_out, and_30_out);
  or or_7 (out_2[0], and_31_out, and_32_out, and_33_out, and_34_out, and_35_out, and_36_out);

  assign out_2[4] = 1'b0;
endmodule

module \Бит_3  (
  input  [15:0] in_1,
  output out_2
);

  wire and_1_out, and_2_out, and_3_out, and_4_out, and_5_out, and_6_out, and_7_out, and_8_out;

  and and_1 (and_1_out, ~in_1[0], ~in_1[1], ~in_1[2], ~in_1[3], ~in_1[4], ~in_1[5], ~in_1[6], ~in_1[7], ~in_1[8], ~in_1[9], ~in_1[10], ~in_1[11], ~in_1[12], ~in_1[13], ~in_1[14], in_1[15]);  // AND_Gate
  and and_2 (and_2_out, ~in_1[0], ~in_1[1], ~in_1[2], ~in_1[3], ~in_1[4], ~in_1[5], ~in_1[6], ~in_1[7], ~in_1[8], ~in_1[9], ~in_1[10], ~in_1[11], ~in_1[12], ~in_1[13], in_1[14], ~in_1[15]);  // AND_Gate
  and and_3 (and_3_out, ~in_1[0], ~in_1[1], ~in_1[2], ~in_1[3], ~in_1[4], ~in_1[5], ~in_1[6], ~in_1[7], ~in_1[8], ~in_1[9], ~in_1[10], ~in_1[11], ~in_1[12], in_1[13], ~in_1[14], ~in_1[15]);  // AND_Gate
  and and_4 (and_4_out, ~in_1[0], ~in_1[1], ~in_1[2], ~in_1[3], ~in_1[4], ~in_1[5], ~in_1[6], ~in_1[7], ~in_1[8], ~in_1[9], ~in_1[10], ~in_1[11], in_1[12], ~in_1[13], ~in_1[14], ~in_1[15]);  // AND_Gate
  and and_5 (and_5_out, ~in_1[0], ~in_1[1], ~in_1[2], ~in_1[3], ~in_1[4], ~in_1[5], ~in_1[6], ~in_1[7], ~in_1[8], ~in_1[9], ~in_1[10], in_1[11], ~in_1[12], ~in_1[13], ~in_1[14], ~in_1[15]);  // AND_Gate
  and and_6 (and_6_out, ~in_1[0], ~in_1[1], ~in_1[2], ~in_1[3], ~in_1[4], ~in_1[5], ~in_1[6], ~in_1[7], ~in_1[8], ~in_1[9], in_1[10], ~in_1[11], ~in_1[12], ~in_1[13], ~in_1[14], ~in_1[15]);  // AND_Gate
  and and_7 (and_7_out, ~in_1[0], ~in_1[1], ~in_1[2], ~in_1[3], ~in_1[4], ~in_1[5], ~in_1[6], ~in_1[7], ~in_1[8], in_1[9], ~in_1[10], ~in_1[11], ~in_1[12], ~in_1[13], ~in_1[14], ~in_1[15]);  // AND_Gate
  and and_8 (and_8_out, ~in_1[0], ~in_1[1], ~in_1[2], ~in_1[3], ~in_1[4], ~in_1[5], ~in_1[6], ~in_1[7], in_1[8], ~in_1[9], ~in_1[10], ~in_1[11], ~in_1[12], ~in_1[13], ~in_1[14], ~in_1[15]);  // AND_Gate
  or or_1 (out_2, and_1_out, and_2_out, and_3_out, and_4_out, and_5_out, and_6_out, and_7_out, and_8_out);
endmodule

module \Бит_2  (
  input  [15:0] in_1,
  output out_2
);

  wire and_1_out, and_2_out, and_3_out, and_4_out, and_5_out, and_6_out, and_7_out, and_8_out;

  and and_1 (and_1_out, ~in_1[0], ~in_1[1], ~in_1[2], ~in_1[3], ~in_1[4], ~in_1[5], ~in_1[6], ~in_1[7], ~in_1[8], ~in_1[9], ~in_1[10], ~in_1[11], ~in_1[12], ~in_1[13], ~in_1[14], in_1[15]);  // AND_Gate
  and and_2 (and_2_out, ~in_1[0], ~in_1[1], ~in_1[2], ~in_1[3], ~in_1[4], ~in_1[5], ~in_1[6], ~in_1[7], ~in_1[8], ~in_1[9], ~in_1[10], ~in_1[11], ~in_1[12], ~in_1[13], in_1[14], ~in_1[15]);  // AND_Gate
  and and_3 (and_3_out, ~in_1[0], ~in_1[1], ~in_1[2], ~in_1[3], ~in_1[4], ~in_1[5], ~in_1[6], ~in_1[7], ~in_1[8], ~in_1[9], ~in_1[10], ~in_1[11], ~in_1[12], in_1[13], ~in_1[14], ~in_1[15]);  // AND_Gate
  and and_4 (and_4_out, ~in_1[0], ~in_1[1], ~in_1[2], ~in_1[3], ~in_1[4], ~in_1[5], ~in_1[6], ~in_1[7], ~in_1[8], ~in_1[9], ~in_1[10], ~in_1[11], in_1[12], ~in_1[13], ~in_1[14], ~in_1[15]);  // AND_Gate
  and and_5 (and_5_out, ~in_1[0], ~in_1[1], ~in_1[2], ~in_1[3], ~in_1[4], ~in_1[5], ~in_1[6], in_1[7], ~in_1[8], ~in_1[9], ~in_1[10], ~in_1[11], ~in_1[12], ~in_1[13], ~in_1[14], ~in_1[15]);  // AND_Gate
  and and_6 (and_6_out, ~in_1[0], ~in_1[1], ~in_1[2], ~in_1[3], ~in_1[4], ~in_1[5], in_1[6], ~in_1[7], ~in_1[8], ~in_1[9], ~in_1[10], ~in_1[11], ~in_1[12], ~in_1[13], ~in_1[14], ~in_1[15]);  // AND_Gate
  and and_7 (and_7_out, ~in_1[0], ~in_1[1], ~in_1[2], ~in_1[3], ~in_1[4], in_1[5], ~in_1[6], ~in_1[7], ~in_1[8], ~in_1[9], ~in_1[10], ~in_1[11], ~in_1[12], ~in_1[13], ~in_1[14], ~in_1[15]);  // AND_Gate
  and and_8 (and_8_out, ~in_1[0], ~in_1[1], ~in_1[2], ~in_1[3], in_1[4], ~in_1[5], ~in_1[6], ~in_1[7], ~in_1[8], ~in_1[9], ~in_1[10], ~in_1[11], ~in_1[12], ~in_1[13], ~in_1[14], ~in_1[15]);  // AND_Gate
  or or_1 (out_2, and_1_out, and_2_out, and_3_out, and_4_out, and_5_out, and_6_out, and_7_out, and_8_out);
endmodule

module \Бит_1  (
  input  [15:0] in_1,
  output out_2
);

  wire and_1_out, and_2_out, and_3_out, and_4_out, and_5_out, and_6_out, and_7_out, and_8_out;

  and and_1 (and_1_out, ~in_1[0], ~in_1[1], ~in_1[2], ~in_1[3], ~in_1[4], ~in_1[5], ~in_1[6], ~in_1[7], ~in_1[8], ~in_1[9], ~in_1[10], ~in_1[11], ~in_1[12], ~in_1[13], ~in_1[14], in_1[15]);  // AND_Gate
  and and_2 (and_2_out, ~in_1[0], ~in_1[1], ~in_1[2], ~in_1[3], ~in_1[4], ~in_1[5], ~in_1[6], ~in_1[7], ~in_1[8], ~in_1[9], ~in_1[10], ~in_1[11], ~in_1[12], ~in_1[13], in_1[14], ~in_1[15]);  // AND_Gate
  and and_3 (and_3_out, ~in_1[0], ~in_1[1], ~in_1[2], ~in_1[3], ~in_1[4], ~in_1[5], ~in_1[6], ~in_1[7], ~in_1[8], ~in_1[9], ~in_1[10], in_1[11], ~in_1[12], ~in_1[13], ~in_1[14], ~in_1[15]);  // AND_Gate
  and and_4 (and_4_out, ~in_1[0], ~in_1[1], ~in_1[2], ~in_1[3], ~in_1[4], ~in_1[5], ~in_1[6], ~in_1[7], ~in_1[8], ~in_1[9], in_1[10], ~in_1[11], ~in_1[12], ~in_1[13], ~in_1[14], ~in_1[15]);  // AND_Gate
  and and_5 (and_5_out, ~in_1[0], ~in_1[1], ~in_1[2], ~in_1[3], ~in_1[4], ~in_1[5], ~in_1[6], in_1[7], ~in_1[8], ~in_1[9], ~in_1[10], ~in_1[11], ~in_1[12], ~in_1[13], ~in_1[14], ~in_1[15]);  // AND_Gate
  and and_6 (and_6_out, ~in_1[0], ~in_1[1], ~in_1[2], ~in_1[3], ~in_1[4], ~in_1[5], in_1[6], ~in_1[7], ~in_1[8], ~in_1[9], ~in_1[10], ~in_1[11], ~in_1[12], ~in_1[13], ~in_1[14], ~in_1[15]);  // AND_Gate
  and and_7 (and_7_out, ~in_1[0], ~in_1[1], ~in_1[2], in_1[3], ~in_1[4], ~in_1[5], ~in_1[6], ~in_1[7], ~in_1[8], ~in_1[9], ~in_1[10], ~in_1[11], ~in_1[12], ~in_1[13], ~in_1[14], ~in_1[15]);  // AND_Gate
  and and_8 (and_8_out, ~in_1[0], ~in_1[1], in_1[2], ~in_1[3], ~in_1[4], ~in_1[5], ~in_1[6], ~in_1[7], ~in_1[8], ~in_1[9], ~in_1[10], ~in_1[11], ~in_1[12], ~in_1[13], ~in_1[14], ~in_1[15]);  // AND_Gate
  or or_1 (out_2, and_1_out, and_2_out, and_3_out, and_4_out, and_5_out, and_6_out, and_7_out, and_8_out);
endmodule

module \Бит_0  (
  input  [15:0] in_1,
  output out_2
);

  wire and_1_out, and_2_out, and_3_out, and_4_out, and_5_out, and_6_out, and_7_out, and_8_out;

  and and_1 (and_1_out, ~in_1[0], ~in_1[1], ~in_1[2], ~in_1[3], ~in_1[4], ~in_1[5], ~in_1[6], ~in_1[7], ~in_1[8], ~in_1[9], ~in_1[10], ~in_1[11], ~in_1[12], ~in_1[13], ~in_1[14], in_1[15]);  // AND_Gate
  and and_2 (and_2_out, ~in_1[0], ~in_1[1], ~in_1[2], ~in_1[3], ~in_1[4], ~in_1[5], ~in_1[6], ~in_1[7], ~in_1[8], ~in_1[9], ~in_1[10], ~in_1[11], ~in_1[12], in_1[13], ~in_1[14], ~in_1[15]);  // AND_Gate
  and and_3 (and_3_out, ~in_1[0], ~in_1[1], ~in_1[2], ~in_1[3], ~in_1[4], ~in_1[5], ~in_1[6], ~in_1[7], ~in_1[8], ~in_1[9], ~in_1[10], in_1[11], ~in_1[12], ~in_1[13], ~in_1[14], ~in_1[15]);  // AND_Gate
  and and_4 (and_4_out, ~in_1[0], ~in_1[1], ~in_1[2], ~in_1[3], ~in_1[4], ~in_1[5], ~in_1[6], ~in_1[7], ~in_1[8], in_1[9], ~in_1[10], ~in_1[11], ~in_1[12], ~in_1[13], ~in_1[14], ~in_1[15]);  // AND_Gate
  and and_5 (and_5_out, ~in_1[0], ~in_1[1], ~in_1[2], ~in_1[3], ~in_1[4], ~in_1[5], ~in_1[6], in_1[7], ~in_1[8], ~in_1[9], ~in_1[10], ~in_1[11], ~in_1[12], ~in_1[13], ~in_1[14], ~in_1[15]);  // AND_Gate
  and and_6 (and_6_out, ~in_1[0], ~in_1[1], ~in_1[2], ~in_1[3], ~in_1[4], in_1[5], ~in_1[6], ~in_1[7], ~in_1[8], ~in_1[9], ~in_1[10], ~in_1[11], ~in_1[12], ~in_1[13], ~in_1[14], ~in_1[15]);  // AND_Gate
  and and_7 (and_7_out, ~in_1[0], ~in_1[1], ~in_1[2], in_1[3], ~in_1[4], ~in_1[5], ~in_1[6], ~in_1[7], ~in_1[8], ~in_1[9], ~in_1[10], ~in_1[11], ~in_1[12], ~in_1[13], ~in_1[14], ~in_1[15]);  // AND_Gate
  and and_8 (and_8_out, ~in_1[0], in_1[1], ~in_1[2], ~in_1[3], ~in_1[4], ~in_1[5], ~in_1[6], ~in_1[7], ~in_1[8], ~in_1[9], ~in_1[10], ~in_1[11], ~in_1[12], ~in_1[13], ~in_1[14], ~in_1[15]);  // AND_Gate
  or or_1 (out_2, and_1_out, and_2_out, and_3_out, and_4_out, and_5_out, and_6_out, and_7_out, and_8_out);
endmodule

module \Память_4_бит  (
  input  [3:0] in_1,
  input  in_2,
  input  in_3,
  output [3:0] out_4
);

  Register #(.width(4)) register_1 (.D(in_1), .Q(out_4), .clk(in_2), .clr(in_3));  // open: en
endmodule
