// Logisim project Lab_1_cybernetica_part_2.circ as structural Verilog: 7 circuits, main circuit Переходы
module \Свет_умный_дом  (
  input  in_1,
  input  in_2,
  input  in_3,
  input  in_4,
  output [1:0] out_5,
  output out_6
);

  wire [1:0] \переходы_1_состояние ;

  \Переходы  \u_переходы_1  (.D(in_1), .T(in_2), .\Состояние (\переходы_1_состояние ), .Clock(in_3), .Reset(in_4));
  // Probe on \переходы_1_состояние 
  \Условия  \u_условия_1  (.in_1(\переходы_1_состояние ), .L(out_5), .LED(out_6));

  // Notes on the sheet:
  //   Номер состояния:
  //   Условия:
  //   L = 00 (не горит)
  //   L = 01 (горит тускло)
  //   L = 10 (горит ярко)
  //   LED = 1 (вкл), LED = 0 (выкл)
endmodule

module dOn (
  input  a,
  input  b,
  output x,
  output y
);

  not not_1 (x, a);
  not not_2 (y, b);
endmodule

module dOff (
  input  a,
  input  b,
  output x,
  output y
);

  not not_1 (x, a);
  not not_2 (y, b);
endmodule

module nOn (
  input  a,
  input  b,
  output x,
  output y
);

  not not_1 (x, a);
  not not_2 (y, b);
endmodule

module nOff (
  input  a,
  input  b,
  output x,
  output y
);

  not not_1 (x, a);
  not not_2 (y, b);
endmodule

module \Переходы  (
  input  D,
  input  Clock,
  input  Reset,
  input  T,
  output [1:0] \Состояние 
);

  wire [1:0] doff_1_y, don_1_y, multiplexer_1_out, noff_1_y, non_1_y;

  dOn don_1 (.a(D), .b(T), .x(don_1_y[1]), .y(don_1_y[0]));
  dOff doff_1 (.a(D), .b(T), .x(doff_1_y[1]), .y(doff_1_y[0]));
  nOn non_1 (.a(D), .x(non_1_y[1]), .b(T), .y(non_1_y[0]));
  nOff noff_1 (.a(D), .b(T), .x(noff_1_y[1]), .y(noff_1_y[0]));
  Multiplexer #(.select(2), .width(2), .enable("false")) multiplexer_1 (
    .in0(don_1_y), .in1(doff_1_y), .in2(non_1_y), .in3(noff_1_y), .out(multiplexer_1_out), .sel(\Состояние ));
  Register #(.width(2)) register_1 (.D(multiplexer_1_out), .Q(\Состояние ), .clk(Clock), .clr(Reset));  // open: en
endmodule

module \Условия  (
  input  [1:0] in_1,
  output [1:0] L,
  output LED
);

  Multiplexer #(.select(2), .width(2), .enable("false")) multiplexer_1 (
    .in0(2'b01), .in1(2'b00), .in2(2'b10), .in3(2'b00), .out(L), .sel(in_1));
  Multiplexer #(.select(2), .enable("false")) multiplexer_2 (
    .in0(1'b0), .in1(1'b1), .in2(1'b0), .in3(1'b1), .out(LED), .sel(in_1));
endmodule
