// Logisim project Lab_1_part_1.circ as structural Verilog: 5 circuits, main circuit Светофор
module \Светофор  (
  input  in_1,
  input  in_2,
  input  in_3,
  input  in_4,
  input  in_5,
  input  in_6,
  output [1:0] out_7,
  output [1:0] out_8,
  output [1:0] out_9,
  output [1:0] out_10
);

  wire [1:0] \переходы_состояний_1_состояние ;

  \Переходы_состояний  \u_переходы_состояний_1  (
    .Ta(in_1), .Tb(in_2), .Bta(in_3), .Btb(in_4), .\Состояние (\переходы_состояний_1_состояние ),
    .Clock(in_5), .Reset(in_6));
  // Probe on \переходы_состояний_1_состояние 
  \Цвета_светофора  \u_цвета_светофора_1  (
    .in_1(\переходы_состояний_1_состояние ), .La(out_7), .Lb(out_8), .Pa(out_9), .Pb(out_10));
  // Probe on out_7
  // Probe on out_8
  // Probe on out_9
  // Probe on out_10

  // Notes on the sheet:
  //   Номер состояния:
  //   Цвета: 0 = зеленый, 1 = желтый, 2 = красный
endmodule

module S0 (
  input  a,
  input  b,
  output x,
  output y
);

  wire not_1_out;

  not not_1 (not_1_out, a);
  or or_1 (y, not_1_out, b);

  assign x = 1'b0;
endmodule

module S2 (
  input  a,
  input  b,
  output x,
  output y
);

  wire not_1_out;

  not not_1 (not_1_out, a);
  or or_1 (y, not_1_out, b);

  assign x = 1'b1;
endmodule

module \Переходы_состояний  (
  input  Ta,
  input  Tb,
  input  Clock,
  input  Reset,
  input  Bta,
  input  Btb,
  output [1:0] \Состояние 
);

  wire [1:0] multiplexer_1_out, s0_1_y, s2_1_y;

  S0 s0_1 (.a(Ta), .b(Bta), .x(s0_1_y[1]), .y(s0_1_y[0]));
  S2 s2_1 (.a(Tb), .b(Btb), .x(s2_1_y[1]), .y(s2_1_y[0]));
  Multiplexer #(.select(2), .width(2), .enable("false")) multiplexer_1 (
    .in0(s0_1_y), .in1(2'b10), .in2(s2_1_y), .in3(2'b00), .out(multiplexer_1_out), .sel(\Состояние ));
  Register #(.width(2)) register_1 (.D(multiplexer_1_out), .Q(\Состояние ), .clk(Clock), .clr(Reset));  // open: en
endmodule

module \Цвета_светофора  (
  input  [1:0] in_1,
  output [1:0] La,
  output [1:0] Lb,
  output [1:0] Pa,
  output [1:0] Pb
);

  Multiplexer #(.select(2), .width(2), .enable("false")) multiplexer_1 (
    .in0(2'b00), .in1(2'b01), .in2(2'b10), .in3(2'b10), .out(La), .sel(in_1));
  Multiplexer #(.select(2), .width(2), .enable("false")) multiplexer_2 (
    .in0(2'b10), .in1(2'b10), .in2(2'b00), .in3(2'b01), .out(Lb), .sel(in_1));
  Multiplexer #(.select(2), .width(2), .enable("false")) multiplexer_3 (
    .in0(2'b10), .in1(2'b10), .in2(2'b00), .in3(2'b00), .out(Pa), .sel(in_1));
  Multiplexer #(.select(2), .width(2), .enable("false")) multiplexer_4 (
    .in0(2'b00), .in1(2'b00), .in2(2'b10), .in3(2'b10), .out(Pb), .sel(in_1));
endmodule
