// Logisim project Lab_2.circ as structural Verilog: 2 circuits, main circuit ALU
module ALU_demo (
  input  [7:0] in_1,
  input  in_2,
  input  in_3,
  input  [3:0] in_4,
  output out_5,
  output out_6,
  output out_7
);

  wire not_1_out;
  wire [7:0] \alu_1_выход , multiplexer_1_out, multiplexer_2_out;

  // Probe on in_1
  not not_1 (not_1_out, in_3);
  Multiplexer #(.width(8), .enable("false")) multiplexer_1 (
    .in0(in_1), .in1(\alu_1_выход ), .out(multiplexer_1_out), .sel(in_3));
  Multiplexer #(.width(8), .enable("false")) multiplexer_2 (
    .in0(in_1), .in1(\alu_1_выход ), .out(multiplexer_2_out), .sel(not_1_out));
  // Probe on \alu_1_выход 
  // Probe on \alu_1_выход 
  ALU alu_1 (
    .A(multiplexer_1_out), .B(multiplexer_2_out), .\Выбор_команды (in_4), .\Запись (in_2), .Zero_Flag(out_5),
    .Negative_Flag(out_6), .\Выход (\alu_1_выход ), .Overflow_Flag(out_7));

  // Notes on the sheet:
  //   Список команд:
  //   0 = A
  //   5 = A x B
  //   6 = A / B
  //   7 = A - B
  //   8 = A + B
  //   1 = NOT(A)
  //   2 = A AND B
  //   3 = A OR B
  //   4 = A XOR B
  //   9 = MIN(A, B)
  //   10 = MAX(A, B)
  //   11 = (A = B)?
  //   12 = A << 1
endmodule

module ALU (
  input  [7:0] A,
  input  [7:0] B,
  input  [3:0] \Выбор_команды ,
  input  \Запись ,
  output Zero_Flag,
  output Negative_Flag,
  output [7:0] \Выход ,
  output Overflow_Flag
);

  wire comparator_1_lt, comparator_2_gt, comparator_3_eq, not_2_out, not_3_out;
  wire [6:0] multiplexer_4_out;
  wire [7:0] adder_1_out, and_1_out, divider_1_out, multiplexer_1_out, multiplexer_2_out, multiplexer_3_out,
       multiplier_1_out, not_1_out, or_1_out, shifter_1_out, subtractor_1_out, xor_1_out;

  // Probe on A
  // Probe on B
  // Probe on \Выбор_команды 
  assign not_1_out = ~A;  // NOT_Gate not_1, 8 bits wide
  assign and_1_out = A & B;  // AND_Gate and_1, 8 bits wide
  assign or_1_out = A | B;  // OR_Gate or_1, 8 bits wide
  assign xor_1_out = A ^ B;  // XOR_Gate xor_1, 8 bits wide
  Multiplier multiplier_1 (.a(A), .b(B), .out(multiplier_1_out));  // open: cin, cout
  Divider divider_1 (.a(A), .b(B), .out(divider_1_out));  // open: upper, rem
  Subtractor subtractor_1 (.a(A), .b(B), .out(subtractor_1_out));  // open: bin, bout
  Adder adder_1 (.a(A), .b(B), .out(adder_1_out), .cout(Overflow_Flag));  // open: cin
  Comparator comparator_1 (.a(A), .b(B), .lt(comparator_1_lt));  // open: gt, eq
  not not_2 (not_2_out, comparator_1_lt);
  not not_3 (not_3_out, comparator_2_gt);
  Comparator comparator_2 (.a(A), .b(B), .gt(comparator_2_gt));  // open: eq, lt
  Comparator comparator_3 (.a(A), .b(B), .eq(comparator_3_eq));  // open: gt, lt
  Shifter shifter_1 (.in(A), .\dist (3'b001), .out(shifter_1_out));
  Multiplexer #(.width(8), .enable("false")) multiplexer_1 (.in0(A), .in1(B), .out(multiplexer_1_out), .sel(not_2_out));
  Multiplexer #(.width(8), .enable("false")) multiplexer_2 (.in0(A), .in1(B), .out(multiplexer_2_out), .sel(not_3_out));
  Multiplexer #(.width(8), .enable("false")) multiplexer_3 (
    .in0({8{1'b0}}), .in1({8{1'b1}}), .out(multiplexer_3_out), .sel(comparator_3_eq));
  Register register_1 (.D({Negative_Flag, multiplexer_4_out}), .Q(\Выход ), .clk(\Запись ));  // open: en, clr
  Multiplexer #(.select(4), .width(8), .enable("false")) multiplexer_4 (
    .in0(A), .in1(not_1_out), .in2(and_1_out), .in3(or_1_out), .in4(xor_1_out), .in5(multiplier_1_out),
    .in6(divider_1_out), .in7(subtractor_1_out), .in8(adder_1_out), .in9(multiplexer_1_out),
    .in10(multiplexer_2_out), .in11(multiplexer_3_out), .in12(shifter_1_out), .in13({8{1'b0}}),
    .in14({8{1'b0}}), .in15({8{1'b0}}), .out({Negative_Flag, multiplexer_4_out}), .sel(\Выбор_команды ));
  nor nor_1 (Zero_Flag, multiplexer_4_out[3], multiplexer_4_out[0], multiplexer_4_out[1], multiplexer_4_out[2], multiplexer_4_out[4], multiplexer_4_out[5], multiplexer_4_out[6], Negative_Flag);
  // Probe on \Выход 

  // Notes on the sheet:
  //   Список команд:
  //   0 = A
  //   1 = NOT(A)
  //   2 = A AND B
  //   3 = A OR B
  //   4 = A XOR B
  //   5 = A x B
  //   6 = A / B
  //   7 = A - B
  //   8 = A + B
  //   9 = MIN(A, B)
  //   10 = MAX(A, B)
  //   11 = (A = B)?
  //   12 = A << 1
endmodule
