// Logisim project Lab_3.circ as structural Verilog: 3 circuits, main circuit Гарвардская архитектура
module \Гарвардская_архитектура  (
  input  \Сброс ,
  output out_2,
  output out_3,
  output out_4
);

  wire and_1_out, and_2_out, and_3_out, not_1_out, not_2_out, \Такты_out ;
  wire [2:0] OPC;
  wire [4:0] INSTR_q;
  wire [7:0] ADDRESS, counter_1_q;
  wire [15:0] ACC, \alu_16_бит_1_выход , multiplexer_1_out, multiplexer_2_out, ram_1_data, ram_2_data, TEMP_q;

  not not_1 (not_1_out, and_1_out);
  and and_1 (and_1_out, ~OPC[2], ~OPC[1], OPC[0]);  // AND_Gate
  Clock \u_Такты  (.out(\Такты_out ));
  Counter #(.trigger("falling")) counter_1 (
    .load(and_1_out), .D(ADDRESS), .count(not_1_out), .Q(counter_1_q), .clk(\Такты_out ), .clr(\Сброс ));  // open: carry
  RAM #(.dataWidth(16), .bus("separate")) ram_1 (
    .addr(counter_1_q), .data(ram_1_data));  // open: din, str, sel, clk, ld, clr
  Register u_ADDRESS (.D(ram_1_data[7:0]), .Q(ADDRESS), .clk(\Такты_out ), .clr(\Сброс ));  // open: en
  Register INSTR (.D(ram_1_data[15:8]), .Q({OPC, INSTR_q}), .clk(\Такты_out ), .clr(\Сброс ));  // open: en
  and and_2 (and_2_out, OPC[2], ~OPC[1], ~OPC[0]);  // AND_Gate
  RAM #(.dataWidth(16), .bus("separate")) ram_2 (
    .addr(ADDRESS), .din(ACC), .data(ram_2_data), .str(and_2_out), .clk(\Такты_out ));  // open: sel, ld, clr
  and and_3 (and_3_out, ~OPC[2], OPC[1], ~OPC[0]);  // AND_Gate
  Register #(.width(16), .trigger("falling")) TEMP (
    .D(ram_2_data), .en(and_3_out), .Q(TEMP_q), .clk(\Такты_out ), .clr(\Сброс ));
  Multiplexer #(.width(16), .enable("false")) multiplexer_1 (
    .in0(TEMP_q), .in1(ACC), .out(multiplexer_1_out), .sel(INSTR_q[4]));
  Multiplexer #(.width(16), .enable("false")) multiplexer_2 (
    .in0(TEMP_q), .in1(ACC), .out(multiplexer_2_out), .sel(not_2_out));
  not not_2 (not_2_out, INSTR_q[4]);
  \ALU_16_бит  \alu_16_бит_1  (
    .A(multiplexer_1_out), .B(multiplexer_2_out), .\Выбор_команды (INSTR_q[3:0]), .Zero_Flag(out_2),
    .Negative_Flag(out_3), .\Выход (\alu_16_бит_1_выход ), .Overflow_Flag(out_4));
  Register #(.width(16)) register_1 (.D(\alu_16_бит_1_выход ), .Q(ACC), .clk(\Такты_out ), .clr(\Сброс ));  // open: en

  // Other names for the same wires on the sheet: RESET = \Сброс 

  // Notes on the sheet:
  //   INSTR
  //   DATA
endmodule

module \Архитектура_фон_Неймана  (
  input  \Сброс ,
  output out_2,
  output out_3,
  output out_4
);

  wire and_1_out, and_2_out, and_3_out, not_1_out, not_2_out, not_3_out, not_4_out, \Такты_out ;
  wire [2:0] OPC;
  wire [4:0] INSTR_q;
  wire [7:0] ADDRESS, counter_1_q, multiplexer_1_out;
  wire [15:0] ACC, \alu_16_бит_1_выход , multiplexer_2_out, multiplexer_3_out, ram_1_data, TEMP_q;

  and and_1 (and_1_out, ~OPC[2], ~OPC[1], OPC[0]);  // AND_Gate
  Clock \u_Такты  (.out(\Такты_out ));
  Counter #(.trigger("falling")) counter_1 (
    .load(and_1_out), .D(ADDRESS), .count(not_1_out), .Q(counter_1_q), .clk(\Такты_out ), .clr(\Сброс ));  // open: carry
  not not_1 (not_1_out, and_1_out);
  Multiplexer #(.width(8), .enable("false")) multiplexer_1 (
    .in0(ADDRESS), .in1(counter_1_q), .out(multiplexer_1_out), .sel(not_2_out));
  not not_2 (not_2_out, \Такты_out );
  not not_3 (not_3_out, \Такты_out );
  and and_2 (and_2_out, OPC[2], ~OPC[1], ~OPC[0]);  // AND_Gate
  RAM #(.dataWidth(16), .bus("separate")) ram_1 (
    .addr(multiplexer_1_out), .din(ACC), .data(ram_1_data), .str(and_2_out), .clk(not_3_out));  // open: sel, ld, clr
  Register INSTR (.D(ram_1_data[15:8]), .Q({OPC, INSTR_q}), .clk(\Такты_out ), .clr(\Сброс ));  // open: en
  and and_3 (and_3_out, ~OPC[2], OPC[1], ~OPC[0]);  // AND_Gate
  Register u_ADDRESS (.D(ram_1_data[7:0]), .Q(ADDRESS), .clk(\Такты_out ), .clr(\Сброс ));  // open: en
  Register #(.width(16), .trigger("falling")) TEMP (
    .D(ram_1_data), .en(and_3_out), .Q(TEMP_q), .clk(\Такты_out ), .clr(\Сброс ));
  Multiplexer #(.width(16), .enable("false")) multiplexer_2 (
    .in0(TEMP_q), .in1(ACC), .out(multiplexer_2_out), .sel(INSTR_q[4]));
  Multiplexer #(.width(16), .enable("false")) multiplexer_3 (
    .in0(TEMP_q), .in1(ACC), .out(multiplexer_3_out), .sel(not_4_out));
  not not_4 (not_4_out, INSTR_q[4]);
  Register #(.width(16), .trigger("falling")) register_1 (
    .D(\alu_16_бит_1_выход ), .Q(ACC), .clk(\Такты_out ), .clr(\Сброс ));  // open: en
  \ALU_16_бит  \alu_16_бит_1  (
    .A(multiplexer_2_out), .B(multiplexer_3_out), .\Выбор_команды (INSTR_q[3:0]), .Zero_Flag(out_2),
    .Negative_Flag(out_3), .\Выход (\alu_16_бит_1_выход ), .Overflow_Flag(out_4));

  // Other names for the same wires on the sheet: RESET = \Сброс 
endmodule

module \ALU_16_бит  (
  input  [15:0] A,
  input  [15:0] B,
  input  [3:0] \Выбор_команды ,
  output Zero_Flag,
  output Negative_Flag,
  output [15:0] \Выход ,
  output Overflow_Flag
);

  wire comparator_1_lt, comparator_2_gt, comparator_3_eq, not_2_out, not_3_out;
  wire [15:0] adder_1_out, and_1_out, divider_1_out, multiplexer_1_out, multiplexer_2_out, multiplexer_3_out,
       multiplier_1_out, not_1_out, or_1_out, shifter_1_out, subtractor_1_out, xor_1_out;

  // Probe on A
  // Probe on B
  // Probe on \Выбор_команды 
  assign not_1_out = ~A;  // NOT_Gate not_1, 16 bits wide
  assign and_1_out = A & B;  // AND_Gate and_1, 16 bits wide
  assign or_1_out = A | B;  // OR_Gate or_1, 16 bits wide
  assign xor_1_out = A ^ B;  // XOR_Gate xor_1, 16 bits wide
  Multiplier #(.width(16)) multiplier_1 (.a(A), .b(B), .out(multiplier_1_out));  // open: cin, cout
  Divider #(.width(16)) divider_1 (.a(A), .b(B), .out(divider_1_out));  // open: upper, rem
  Subtractor #(.width(16)) subtractor_1 (.a(A), .b(B), .out(subtractor_1_out));  // open: bin, bout
  Adder #(.width(16)) adder_1 (.a(A), .b(B), .out(adder_1_out), .cout(Overflow_Flag));  // open: cin
  Comparator #(.width(16)) comparator_1 (.a(A), .b(B), .lt(comparator_1_lt));  // open: gt, eq
  not not_2 (not_2_out, comparator_1_lt);
  not not_3 (not_3_out, comparator_2_gt);
  Comparator #(.width(16)) comparator_2 (.a(A), .b(B), .gt(comparator_2_gt));  // open: eq, lt
  Comparator #(.width(16)) comparator_3 (.a(A), .b(B), .eq(comparator_3_eq));  // open: gt, lt
  Shifter #(.width(16)) shifter_1 (.in(A), .\dist (4'b0001), .out(shifter_1_out));
  Multiplexer #(.width(16), .enable("false")) multiplexer_1 (
    .in0(A), .in1(B), .out(multiplexer_1_out), .sel(not_2_out));
  Multiplexer #(.width(16), .enable("false")) multiplexer_2 (
    .in0(A), .in1(B), .out(multiplexer_2_out), .sel(not_3_out));
  Multiplexer #(.width(16), .enable("false")) multiplexer_3 (
    .in0({16{1'b0}}), .in1({16{1'b1}}), .out(multiplexer_3_out), .sel(comparator_3_eq));
  Multiplexer #(.select(4), .width(16), .enable("false")) multiplexer_4 (
    .in0(A), .in1(not_1_out), .in2(and_1_out), .in3(or_1_out), .in4(xor_1_out), .in5(multiplier_1_out),
    .in6(divider_1_out), .in7(subtractor_1_out), .in8(adder_1_out), .in9(multiplexer_1_out),
    .in10(multiplexer_2_out), .in11(multiplexer_3_out), .in12(shifter_1_out), .in13({16{1'b0}}),
    .in14({16{1'b0}}), .in15({16{1'b0}}), .out({Negative_Flag, \Выход [14:0]}), .sel(\Выбор_команды ));
  // Probe on {Negative_Flag, \Выход [14:0]}
  nor nor_1 (Zero_Flag, \Выход [7], \Выход [0], \Выход [1], \Выход [2], \Выход [3], \Выход [4], \Выход [5], \Выход [6], \Выход [8], \Выход [9], \Выход [10], \Выход [11], \Выход [12], \Выход [13], \Выход [14], Negative_Flag);

  assign \Выход [15] = Negative_Flag;

  // Notes on the sheet:
  //   Список команд:
  //   0 = A
  //   1 = NOT(A)
  //   2 = A AND B
  //   3 = A OR B
  //   4 = A XOR B
  //   5 = A x B
  //   6 = A / B
  //   7 = A - B
  //   8 = A + B
  //   9 = MIN(A, B)
  //   10 = MAX(A, B)
  //   11 = (A = B)?
  //   12 = A << 1
endmodule
