// Logisim project Lab_4.circ as structural Verilog: 9 circuits, main circuit Процессор
module \Процессор  (
);

  wire and_1_out, demultiplexer_2_out0, demultiplexer_2_out1, NF, not_1_out, not_2_out, not_3_out, not_4_out,
       OF, RESET, xor_1_out, ZF, \декодер_1_halt , \декодер_1_выбордругрег , \декодер_1_загрinstr ,
       \декодер_1_загрtemp , \декодер_1_заградринстр , \декодер_1_запram , \декодер_1_истtemp ,
       \декодер_1_режимсчет , \декодер_1_сохррегa_b , \Такты_out ;
  wire [4:0] register_1_q, \автомат_для_процессора_1_следующее_состояние ;
  wire [5:0] INSTR_q_2;
  wire [9:0] INSTR_q;
  wire [15:0] ADDRESS, counter_1_q, multiplexer_1_out, multiplexer_2_out;
  wire [31:0] A_q, ACC, \alu_32_бит_1_выход , B_q, demultiplexer_1_out0, demultiplexer_1_out1,
       multiplexer_3_out, multiplexer_4_out, multiplexer_5_out, ram_1_data, TEMP_q;

  Clock \u_Такты  (.out(\Такты_out ));
  Multiplexer #(.width(16), .enable("false")) multiplexer_1 (
    .in0(counter_1_q), .in1(ADDRESS), .out(multiplexer_1_out), .sel(\декодер_1_заградринстр ));
  and and_1 (and_1_out, \Такты_out , \декодер_1_halt );
  Counter #(.width(16), .max('hffff), .trigger("falling")) counter_1 (
    .load(\декодер_1_режимсчет ), .D(multiplexer_1_out), .count(not_1_out), .Q(counter_1_q), .clk(and_1_out),
    .clr(RESET));  // open: carry
  not not_1 (not_1_out, \декодер_1_режимсчет );
  not not_2 (not_2_out, and_1_out);
  Multiplexer #(.width(16), .enable("false")) multiplexer_2 (
    .in0(ADDRESS), .in1(counter_1_q), .out(multiplexer_2_out), .sel(not_2_out));
  not not_3 (not_3_out, and_1_out);
  RAM #(.addrWidth(16), .dataWidth(32), .bus("separate")) ram_1 (
    .addr(multiplexer_2_out), .din(ACC), .data(ram_1_data), .str(\декодер_1_запram ), .clk(not_3_out));  // open: sel, ld, clr
  Register #(.width(16)) INSTR (
    .D(ram_1_data[31:16]), .en(\декодер_1_загрinstr ), .Q({INSTR_q, INSTR_q_2}), .clk(and_1_out), .clr(RESET));
  Register #(.width(16)) u_ADDRESS (
    .D(ram_1_data[15:0]), .en(\декодер_1_загрinstr ), .Q(ADDRESS), .clk(and_1_out), .clr(RESET));
  \Автомат_для_процессора  \u_автомат_для_процессора_1  (
    .\Следующее_состояние (\автомат_для_процессора_1_следующее_состояние ), .\Биты_опкода (INSTR_q),
    .\Текущее_состояние (register_1_q), .ZF(ZF), .NF(NF), .OF(OF));
  Register #(.width(5)) register_1 (
    .D(\автомат_для_процессора_1_следующее_состояние ), .Q(register_1_q), .clk(and_1_out), .clr(RESET));  // open: en
  \Декодер  \u_декодер_1  (
    .in_1(register_1_q), .HALT(\декодер_1_halt ), .\ЗагрАдрИнстр (\декодер_1_заградринстр ),
    .\РежимСчет (\декодер_1_режимсчет ), .\Сброс (RESET), .\ЗапRAM (\декодер_1_запram ),
    .\ЗагрINSTR (\декодер_1_загрinstr ), .\ИстTEMP (\декодер_1_истtemp ), .\ЗагрTEMP (\декодер_1_загрtemp ),
    .\ВыборДругРег (\декодер_1_выбордругрег ), .\СохрРегA_B (\декодер_1_сохррегa_b ));
  Multiplexer #(.width(32), .enable("false")) multiplexer_3 (
    .in0(ram_1_data), .in1(ACC), .out(multiplexer_3_out), .sel(\декодер_1_истtemp ));
  Register #(.width(32), .trigger("falling")) TEMP (
    .D(multiplexer_3_out), .en(\декодер_1_загрtemp ), .Q(TEMP_q), .clk(and_1_out), .clr(RESET));
  Multiplexer #(.width(32), .enable("false")) multiplexer_4 (
    .in0(TEMP_q), .in1(ACC), .out(multiplexer_4_out), .sel(INSTR_q_2[4]));
  Multiplexer #(.width(32), .enable("false")) multiplexer_5 (
    .in0(TEMP_q), .in1(ACC), .out(multiplexer_5_out), .sel(not_4_out));
  not not_4 (not_4_out, INSTR_q_2[4]);
  xor xor_1 (xor_1_out, INSTR_q_2[5], \декодер_1_выбордругрег );
  Demultiplexer #(.width(32), .enable("false")) demultiplexer_1 (
    .out0(demultiplexer_1_out0), .out1(demultiplexer_1_out1), .in(\alu_32_бит_1_выход ), .sel(xor_1_out));
  \ALU_32_бит  \alu_32_бит_1  (
    .A(multiplexer_4_out), .B(multiplexer_5_out), .\Выбор_команды (INSTR_q_2[3:0]), .Zero_Flag(ZF),
    .Negative_Flag(NF), .\Выход (\alu_32_бит_1_выход ), .Overflow_Flag(OF));
  Demultiplexer #(.enable("false")) demultiplexer_2 (
    .out0(demultiplexer_2_out0), .out1(demultiplexer_2_out1), .in(\декодер_1_сохррегa_b ), .sel(xor_1_out));
  Register #(.width(32)) A (.D(demultiplexer_1_out0), .en(demultiplexer_2_out0), .Q(A_q), .clk(and_1_out), .clr(RESET));
  Register #(.width(32)) B (.D(demultiplexer_1_out1), .en(demultiplexer_2_out1), .Q(B_q), .clk(and_1_out), .clr(RESET));
  Multiplexer #(.width(32), .enable("false")) multiplexer_6 (.in0(A_q), .in1(B_q), .out(ACC), .sel(xor_1_out));
endmodule

module \ALU_32_бит  (
  input  [31:0] A,
  input  [31:0] B,
  input  [3:0] \Выбор_команды ,
  output Zero_Flag,
  output Negative_Flag,
  output [31:0] \Выход ,
  output Overflow_Flag
);

  wire comparator_1_lt, comparator_2_gt, comparator_3_eq, not_2_out, not_3_out;
  wire [31:0] adder_1_out, and_1_out, divider_1_out, multiplexer_1_out, multiplexer_2_out, multiplexer_3_out,
       multiplier_1_out, not_1_out, or_1_out, shifter_1_out, subtractor_1_out, xor_1_out;

  // Probe on A
  // Probe on B
  // Probe on \Выбор_команды 
  assign not_1_out = ~A;  // NOT_Gate not_1, 32 bits wide
  assign and_1_out = A & B;  // AND_Gate and_1, 32 bits wide
  assign or_1_out = A | B;  // OR_Gate or_1, 32 bits wide
  assign xor_1_out = A ^ B;  // XOR_Gate xor_1, 32 bits wide
  Multiplier #(.width(32)) multiplier_1 (.a(A), .b(B), .out(multiplier_1_out));  // open: cin, cout
  Divider #(.width(32)) divider_1 (.a(A), .b(B), .out(divider_1_out));  // open: upper, rem
  Subtractor #(.width(32)) subtractor_1 (.a(A), .b(B), .out(subtractor_1_out));  // open: bin, bout
  Adder #(.width(32)) adder_1 (.a(A), .b(B), .out(adder_1_out), .cout(Overflow_Flag));  // open: cin
  Comparator #(.width(32)) comparator_1 (.a(A), .b(B), .lt(comparator_1_lt));  // open: gt, eq
  Comparator #(.width(32)) comparator_2 (.a(A), .b(B), .gt(comparator_2_gt));  // open: eq, lt
  Comparator #(.width(32)) comparator_3 (.a(A), .b(B), .eq(comparator_3_eq));  // open: gt, lt
  Shifter #(.width(32)) shifter_1 (.in(A), .\dist (5'b00001), .out(shifter_1_out));
  Multiplexer #(.width(32), .enable("false")) multiplexer_1 (
    .in0(A), .in1(B), .out(multiplexer_1_out), .sel(not_2_out));
  not not_2 (not_2_out, comparator_1_lt);
  Multiplexer #(.width(32), .enable("false")) multiplexer_2 (
    .in0(A), .in1(B), .out(multiplexer_2_out), .sel(not_3_out));
  not not_3 (not_3_out, comparator_2_gt);
  Multiplexer #(.width(32), .enable("false")) multiplexer_3 (
    .in0({32{1'b0}}), .in1({32{1'b1}}), .out(multiplexer_3_out), .sel(comparator_3_eq));
  Multiplexer #(.select(4), .width(32), .enable("false")) multiplexer_4 (
    .in0(A), .in1(not_1_out), .in2(and_1_out), .in3(or_1_out), .in4(xor_1_out), .in5(multiplier_1_out),
    .in6(divider_1_out), .in7(subtractor_1_out), .in8(adder_1_out), .in9(multiplexer_1_out),
    .in10(multiplexer_2_out), .in11(multiplexer_3_out), .in12(shifter_1_out), .in13({32{1'b0}}),
    .in14({32{1'b0}}), .in15({32{1'b0}}), .out({Negative_Flag, \Выход [30:0]}), .sel(\Выбор_команды ));
  // Probe on {Negative_Flag, \Выход [30:0]}
  nor nor_1 (Zero_Flag, \Выход [15], \Выход [0], \Выход [1], \Выход [2], \Выход [3], \Выход [4], \Выход [5], \Выход [6], \Выход [7], \Выход [8], \Выход [9], \Выход [10], \Выход [11], \Выход [12], \Выход [13], \Выход [14], \Выход [16], \Выход [17], \Выход [18], \Выход [19], \Выход [20], \Выход [21], \Выход [22], \Выход [23], \Выход [24], \Выход [25], \Выход [26], \Выход [27], \Выход [28], \Выход [29], \Выход [30], Negative_Flag);

  assign \Выход [31] = Negative_Flag;

  // Notes on the sheet:
  //   Список команд:
  //   0 = A
  //   1 = NOT(A)
  //   2 = A AND B
  //   3 = A OR B
  //   4 = A XOR B
  //   5 = A x B
  //   6 = A / B
  //   7 = A - B
  //   8 = A + B
  //   9 = MIN(A, B)
  //   10 = MAX(A, B)
  //   11 = (A = B)?
  //   12 = A << 1
endmodule

module \Автомат_для_процессора  (
  input  [4:0] \Текущее_состояние ,
  input  [9:0] \Биты_опкода ,
  input  ZF,
  input  NF,
  input  OF,
  output [4:0] \Следующее_состояние 
);

  F0 f0_1 (.in_1({OF, NF, ZF, \Биты_опкода , \Текущее_состояние }), .out_2(\Следующее_состояние [0]));
  F1 f1_1 (.in_1({OF, NF, ZF, \Биты_опкода , \Текущее_состояние }), .out_2(\Следующее_состояние [1]));
  F2 f2_1 (.in_1({OF, NF, ZF, \Биты_опкода , \Текущее_состояние }), .out_2(\Следующее_состояние [2]));
  F3 f3_1 (.in_1({OF, NF, ZF, \Биты_опкода , \Текущее_состояние }), .out_2(\Следующее_состояние [3]));
  F4 f4_1 (.in_1({OF, NF, ZF, \Биты_опкода , \Текущее_состояние }), .out_2(\Следующее_состояние [4]));
endmodule

module F0 (
  input  [17:0] in_1,
  output out_2
);

  wire and_1_out, and_2_out, and_3_out, and_4_out, and_5_out, and_6_out, and_7_out, and_8_out, and_9_out;

  and and_1 (and_1_out, ~in_1[17], ~in_1[16], ~in_1[15], ~in_1[14], ~in_1[13], ~in_1[12], ~in_1[11], ~in_1[10], ~in_1[9], ~in_1[7], ~in_1[6], ~in_1[5], ~in_1[4], ~in_1[3], ~in_1[2], ~in_1[1], ~in_1[0], ~in_1[8]);  // AND_Gate
  and and_2 (and_2_out, ~in_1[17], ~in_1[16], ~in_1[15], ~in_1[14], in_1[13], ~in_1[12], ~in_1[11], ~in_1[10], ~in_1[9], ~in_1[7], ~in_1[6], ~in_1[5], ~in_1[4], in_1[3], ~in_1[2], ~in_1[1], ~in_1[0], ~in_1[8]);  // AND_Gate
  and and_3 (and_3_out, ~in_1[17], ~in_1[16], ~in_1[15], ~in_1[14], in_1[13], ~in_1[12], ~in_1[11], ~in_1[10], ~in_1[9], ~in_1[7], ~in_1[6], in_1[5], ~in_1[4], ~in_1[3], ~in_1[2], ~in_1[1], ~in_1[0], ~in_1[8]);  // AND_Gate
  and and_4 (and_4_out, ~in_1[17], ~in_1[16], ~in_1[15], ~in_1[14], in_1[13], ~in_1[12], ~in_1[11], ~in_1[10], ~in_1[9], ~in_1[7], ~in_1[6], in_1[5], ~in_1[4], in_1[3], ~in_1[2], ~in_1[1], ~in_1[0], ~in_1[8]);  // AND_Gate
  and and_5 (and_5_out, ~in_1[17], ~in_1[16], ~in_1[15], ~in_1[14], in_1[13], ~in_1[12], ~in_1[11], ~in_1[10], ~in_1[9], ~in_1[7], in_1[6], ~in_1[5], ~in_1[4], in_1[3], ~in_1[2], ~in_1[1], ~in_1[0], ~in_1[8]);  // AND_Gate
  and and_6 (and_6_out, ~in_1[17], ~in_1[16], ~in_1[15], ~in_1[14], in_1[13], in_1[12], in_1[11], in_1[10], in_1[9], in_1[7], in_1[6], in_1[5], in_1[4], in_1[3], ~in_1[2], ~in_1[1], ~in_1[0], in_1[8]);  // AND_Gate
  and and_7 (and_7_out, ~in_1[17], ~in_1[16], in_1[15], ~in_1[14], ~in_1[13], ~in_1[12], ~in_1[11], ~in_1[10], ~in_1[9], ~in_1[7], ~in_1[6], ~in_1[5], ~in_1[4], ~in_1[3], ~in_1[2], ~in_1[1], ~in_1[0], ~in_1[8]);  // AND_Gate
  and and_8 (and_8_out, ~in_1[17], in_1[16], ~in_1[15], ~in_1[14], ~in_1[13], ~in_1[12], ~in_1[11], ~in_1[10], ~in_1[9], ~in_1[7], ~in_1[6], ~in_1[5], ~in_1[4], ~in_1[3], ~in_1[2], ~in_1[1], ~in_1[0], ~in_1[8]);  // AND_Gate
  and and_9 (and_9_out, ~in_1[17], in_1[16], in_1[15], ~in_1[14], ~in_1[13], ~in_1[12], ~in_1[11], ~in_1[10], ~in_1[9], ~in_1[7], ~in_1[6], ~in_1[5], ~in_1[4], ~in_1[3], ~in_1[2], ~in_1[1], ~in_1[0], ~in_1[8]);  // AND_Gate
  or or_1 (out_2, and_1_out, and_2_out, and_3_out, and_4_out, and_5_out, and_6_out, and_7_out, and_8_out, and_9_out);
endmodule

module F1 (
  input  [17:0] in_1,
  output out_2
);

  wire and_1_out, and_2_out, and_3_out, and_4_out, and_5_out, and_6_out, and_7_out, and_8_out, and_9_out;

  and and_1 (and_1_out, ~in_1[17], ~in_1[16], ~in_1[15], ~in_1[14], in_1[13], ~in_1[12], ~in_1[11], ~in_1[10], ~in_1[9], ~in_1[7], ~in_1[6], ~in_1[5], ~in_1[4], ~in_1[3], ~in_1[2], ~in_1[1], ~in_1[0], ~in_1[8]);  // AND_Gate
  and and_2 (and_2_out, ~in_1[17], ~in_1[16], ~in_1[15], ~in_1[14], in_1[13], ~in_1[12], ~in_1[11], ~in_1[10], ~in_1[9], ~in_1[7], ~in_1[6], ~in_1[5], ~in_1[4], in_1[3], ~in_1[2], ~in_1[1], ~in_1[0], ~in_1[8]);  // AND_Gate
  and and_3 (and_3_out, ~in_1[17], ~in_1[16], ~in_1[15], ~in_1[14], in_1[13], ~in_1[12], ~in_1[11], ~in_1[10], ~in_1[9], ~in_1[7], ~in_1[6], ~in_1[5], in_1[4], in_1[3], ~in_1[2], ~in_1[1], ~in_1[0], ~in_1[8]);  // AND_Gate
  and and_4 (and_4_out, ~in_1[17], ~in_1[16], ~in_1[15], ~in_1[14], in_1[13], ~in_1[12], ~in_1[11], ~in_1[10], ~in_1[9], ~in_1[7], ~in_1[6], in_1[5], ~in_1[4], ~in_1[3], ~in_1[2], ~in_1[1], ~in_1[0], ~in_1[8]);  // AND_Gate
  and and_5 (and_5_out, ~in_1[17], ~in_1[16], ~in_1[15], ~in_1[14], in_1[13], ~in_1[12], ~in_1[11], ~in_1[10], ~in_1[9], ~in_1[7], ~in_1[6], in_1[5], ~in_1[4], in_1[3], ~in_1[2], ~in_1[1], ~in_1[0], ~in_1[8]);  // AND_Gate
  and and_6 (and_6_out, ~in_1[17], ~in_1[16], ~in_1[15], ~in_1[14], in_1[13], in_1[12], in_1[11], in_1[10], in_1[9], in_1[7], in_1[6], in_1[5], in_1[4], in_1[3], ~in_1[2], ~in_1[1], ~in_1[0], in_1[8]);  // AND_Gate
  and and_7 (and_7_out, ~in_1[17], in_1[16], ~in_1[15], ~in_1[14], ~in_1[13], ~in_1[12], ~in_1[11], ~in_1[10], ~in_1[9], ~in_1[7], ~in_1[6], ~in_1[5], ~in_1[4], ~in_1[3], ~in_1[2], in_1[1], ~in_1[0], ~in_1[8]);  // AND_Gate
  and and_8 (and_8_out, ~in_1[17], in_1[16], in_1[15], ~in_1[14], ~in_1[13], ~in_1[12], ~in_1[11], ~in_1[10], ~in_1[9], ~in_1[7], ~in_1[6], ~in_1[5], ~in_1[4], ~in_1[3], in_1[2], ~in_1[1], ~in_1[0], ~in_1[8]);  // AND_Gate
  and and_9 (and_9_out, in_1[17], ~in_1[16], ~in_1[15], ~in_1[14], in_1[13], ~in_1[12], ~in_1[11], ~in_1[10], ~in_1[9], ~in_1[7], ~in_1[6], ~in_1[5], ~in_1[4], ~in_1[3], ~in_1[2], ~in_1[1], ~in_1[0], ~in_1[8]);  // AND_Gate
  or or_1 (out_2, and_1_out, and_2_out, and_3_out, and_4_out, and_5_out, and_6_out, and_7_out, and_8_out, and_9_out);
endmodule

module F2 (
  input  [17:0] in_1,
  output out_2
);

  wire and_1_out, and_2_out, and_3_out, and_4_out, and_5_out, and_6_out, and_7_out, and_8_out;

  and and_1 (and_1_out, ~in_1[17], ~in_1[16], ~in_1[15], ~in_1[14], in_1[13], ~in_1[12], ~in_1[11], ~in_1[10], ~in_1[9], ~in_1[7], ~in_1[6], ~in_1[5], in_1[4], ~in_1[3], ~in_1[2], ~in_1[1], ~in_1[0], ~in_1[8]);  // AND_Gate
  and and_2 (and_2_out, ~in_1[17], ~in_1[16], ~in_1[15], ~in_1[14], in_1[13], ~in_1[12], ~in_1[11], ~in_1[10], ~in_1[9], ~in_1[7], ~in_1[6], ~in_1[5], in_1[4], in_1[3], ~in_1[2], ~in_1[1], ~in_1[0], ~in_1[8]);  // AND_Gate
  and and_3 (and_3_out, ~in_1[17], ~in_1[16], ~in_1[15], ~in_1[14], in_1[13], ~in_1[12], ~in_1[11], ~in_1[10], ~in_1[9], ~in_1[7], ~in_1[6], in_1[5], ~in_1[4], ~in_1[3], ~in_1[2], ~in_1[1], ~in_1[0], ~in_1[8]);  // AND_Gate
  and and_4 (and_4_out, ~in_1[17], ~in_1[16], ~in_1[15], ~in_1[14], in_1[13], in_1[12], in_1[11], in_1[10], in_1[9], in_1[7], in_1[6], in_1[5], in_1[4], in_1[3], ~in_1[2], ~in_1[1], ~in_1[0], in_1[8]);  // AND_Gate
  and and_5 (and_5_out, ~in_1[17], ~in_1[16], in_1[15], ~in_1[14], ~in_1[13], ~in_1[12], ~in_1[11], ~in_1[10], ~in_1[9], ~in_1[7], ~in_1[6], ~in_1[5], ~in_1[4], ~in_1[3], ~in_1[2], ~in_1[1], ~in_1[0], ~in_1[8]);  // AND_Gate
  and and_6 (and_6_out, ~in_1[17], in_1[16], ~in_1[15], in_1[14], in_1[13], ~in_1[12], ~in_1[11], ~in_1[10], ~in_1[9], ~in_1[7], ~in_1[6], ~in_1[5], ~in_1[4], ~in_1[3], ~in_1[2], ~in_1[1], ~in_1[0], ~in_1[8]);  // AND_Gate
  and and_7 (and_7_out, ~in_1[17], in_1[16], in_1[15], ~in_1[14], ~in_1[13], ~in_1[12], ~in_1[11], ~in_1[10], ~in_1[9], ~in_1[7], ~in_1[6], ~in_1[5], ~in_1[4], ~in_1[3], ~in_1[2], ~in_1[1], ~in_1[0], ~in_1[8]);  // AND_Gate
  and and_8 (and_8_out, ~in_1[17], in_1[16], in_1[15], ~in_1[14], ~in_1[13], ~in_1[12], ~in_1[11], ~in_1[10], ~in_1[9], ~in_1[7], ~in_1[6], ~in_1[5], ~in_1[4], ~in_1[3], in_1[2], ~in_1[1], ~in_1[0], ~in_1[8]);  // AND_Gate
  or or_1 (out_2, and_1_out, and_2_out, and_3_out, and_4_out, and_6_out, and_7_out, and_8_out, and_5_out);
endmodule

module F3 (
  input  [17:0] in_1,
  output out_2
);

  wire and_1_out, and_2_out, and_3_out, and_4_out, and_5_out, and_6_out, and_7_out, and_8_out;

  and and_1 (and_1_out, ~in_1[17], ~in_1[16], ~in_1[15], ~in_1[14], in_1[13], ~in_1[12], ~in_1[11], ~in_1[10], ~in_1[9], ~in_1[7], ~in_1[6], in_1[5], ~in_1[4], in_1[3], ~in_1[2], ~in_1[1], ~in_1[0], ~in_1[8]);  // AND_Gate
  and and_2 (and_2_out, ~in_1[17], ~in_1[16], ~in_1[15], ~in_1[14], in_1[13], in_1[12], in_1[11], in_1[10], in_1[9], in_1[7], in_1[6], in_1[5], in_1[4], in_1[3], ~in_1[2], ~in_1[1], ~in_1[0], in_1[8]);  // AND_Gate
  and and_3 (and_3_out, ~in_1[17], ~in_1[16], in_1[15], in_1[14], in_1[13], ~in_1[12], ~in_1[11], ~in_1[10], ~in_1[9], ~in_1[7], ~in_1[6], ~in_1[5], ~in_1[4], ~in_1[3], ~in_1[2], ~in_1[1], ~in_1[0], ~in_1[8]);  // AND_Gate
  and and_4 (and_4_out, ~in_1[17], in_1[16], ~in_1[15], ~in_1[14], ~in_1[13], ~in_1[12], ~in_1[11], ~in_1[10], ~in_1[9], ~in_1[7], ~in_1[6], ~in_1[5], ~in_1[4], ~in_1[3], ~in_1[2], ~in_1[1], ~in_1[0], ~in_1[8]);  // AND_Gate
  and and_5 (and_5_out, ~in_1[17], in_1[16], ~in_1[15], ~in_1[14], ~in_1[13], ~in_1[12], ~in_1[11], ~in_1[10], ~in_1[9], ~in_1[7], ~in_1[6], ~in_1[5], ~in_1[4], ~in_1[3], ~in_1[2], in_1[1], ~in_1[0], ~in_1[8]);  // AND_Gate
  and and_6 (and_6_out, ~in_1[17], in_1[16], ~in_1[15], in_1[14], in_1[13], ~in_1[12], ~in_1[11], ~in_1[10], ~in_1[9], ~in_1[7], ~in_1[6], ~in_1[5], ~in_1[4], ~in_1[3], ~in_1[2], ~in_1[1], ~in_1[0], ~in_1[8]);  // AND_Gate
  and and_7 (and_7_out, ~in_1[17], in_1[16], in_1[15], ~in_1[14], ~in_1[13], ~in_1[12], ~in_1[11], ~in_1[10], ~in_1[9], ~in_1[7], ~in_1[6], ~in_1[5], ~in_1[4], ~in_1[3], ~in_1[2], ~in_1[1], ~in_1[0], ~in_1[8]);  // AND_Gate
  and and_8 (and_8_out, ~in_1[17], in_1[16], in_1[15], ~in_1[14], ~in_1[13], ~in_1[12], ~in_1[11], ~in_1[10], ~in_1[9], ~in_1[7], ~in_1[6], ~in_1[5], ~in_1[4], ~in_1[3], in_1[2], ~in_1[1], ~in_1[0], ~in_1[8]);  // AND_Gate
  or or_1 (out_2, and_1_out, and_2_out, and_3_out, and_4_out, and_6_out, and_7_out, and_8_out, and_5_out);
endmodule

module F4 (
  input  [17:0] in_1,
  output out_2
);

  wire and_1_out, and_2_out, and_3_out, and_4_out;

  and and_1 (and_1_out, ~in_1[17], ~in_1[16], ~in_1[15], ~in_1[14], in_1[13], ~in_1[12], ~in_1[11], ~in_1[10], ~in_1[9], ~in_1[7], in_1[6], ~in_1[5], ~in_1[4], ~in_1[3], ~in_1[2], ~in_1[1], ~in_1[0], ~in_1[8]);  // AND_Gate
  and and_2 (and_2_out, ~in_1[17], ~in_1[16], ~in_1[15], ~in_1[14], in_1[13], ~in_1[12], ~in_1[11], ~in_1[10], ~in_1[9], ~in_1[7], in_1[6], ~in_1[5], ~in_1[4], in_1[3], ~in_1[2], ~in_1[1], ~in_1[0], ~in_1[8]);  // AND_Gate
  and and_3 (and_3_out, ~in_1[17], ~in_1[16], ~in_1[15], ~in_1[14], in_1[13], in_1[12], in_1[11], in_1[10], in_1[9], in_1[7], in_1[6], in_1[5], in_1[4], in_1[3], ~in_1[2], ~in_1[1], ~in_1[0], in_1[8]);  // AND_Gate
  and and_4 (and_4_out, in_1[17], ~in_1[16], ~in_1[15], ~in_1[14], in_1[13], ~in_1[12], ~in_1[11], ~in_1[10], ~in_1[9], ~in_1[7], ~in_1[6], ~in_1[5], ~in_1[4], ~in_1[3], ~in_1[2], ~in_1[1], ~in_1[0], ~in_1[8]);  // AND_Gate
  or or_1 (out_2, and_1_out, and_2_out, and_4_out, and_3_out);
endmodule

module \Декодер  (
  input  [4:0] in_1,
  output HALT,
  output \ЗагрАдрИнстр ,
  output \РежимСчет ,
  output \Сброс ,
  output \ЗапRAM ,
  output \ЗагрINSTR ,
  output \ИстTEMP ,
  output \ЗагрTEMP ,
  output \ВыборДругРег ,
  output \СохрРегA_B 
);

  Multiplexer #(.select(5), .width(10), .enable("false")) multiplexer_1 (
    .in0(10'h20), .in1({10{1'b0}}), .in2({10{1'b0}}), .in3(10'h6), .in4(10'h80), .in5(10'h200), .in6(10'h10),
    .in7(10'hc0), .in8(10'h100), .in9({10{1'b0}}), .in10(10'h6), .in11(10'hc0), .in12(10'h100),
    .in13({10{1'b0}}), .in14(10'h6), .in15({10{1'b0}}), .in16(10'h200), .in17(10'hc0), .in18(10'h300),
    .in19({10{1'b0}}), .in20({10{1'b0}}), .in21({10{1'b0}}), .in22({10{1'b0}}), .in23({10{1'b0}}),
    .in24({10{1'b0}}), .in25({10{1'b0}}), .in26({10{1'b0}}), .in27({10{1'b0}}), .in28({10{1'b0}}),
    .in29({10{1'b0}}), .in30({10{1'b0}}), .in31(10'h1),
    .out({\СохрРегA_B , \ВыборДругРег , \ЗагрTEMP , \ИстTEMP , \ЗагрINSTR , \ЗапRAM , \Сброс , \РежимСчет , \ЗагрАдрИнстр , HALT}),
    .sel(in_1));

  // Notes on the sheet:
  //   JUMP_NEG_3_0
  //   JUMP_NEG_2
  //   JUMP_NEG_3_1
  //   JUMP_NEG_1
  //   JUMP_ZERO_1
  //   SAVE
  //   JUMP_ZERO_2
  //   LOAD_2
  //   JUMP_ZERO_3_0
  //   LOAD_1
  //   JUMP_ZERO_3_1
  //   JUMP
  //   ALU_Type_A
  //   ALU_Type_B_1
  //   IDLE
  //   Декодирование
  //   ALU_Type_B_2
  //   Считывание
  //   HALT
endmodule
