// Logisim project Lab_6.circ as structural Verilog: 2 circuits, main circuit main
module main (
  input  \Сброс ,
  output HALT,
  output MOV,
  output ADD,
  output SWAP_ALU
);

  wire and_1_out, and_2_out, and_3_out, and_4_out, and_5_out, and_6_out, and_7_out, and_8_out, and_9_out,
       and_10_out, and_11_out, and_12_out, and_13_out, and_14_out, clock_1_out, comparator_1_eq,
       comparator_2_eq, comparator_3_eq, comparator_4_eq, comparator_5_eq, comparator_6_eq, comparator_7_eq,
       comparator_8_eq, comparator_9_eq, comparator_10_eq, comparator_11_eq, comparator_12_eq,
       comparator_13_eq, comparator_14_eq, comparator_15_eq, comparator_16_eq, comparator_17_eq,
       comparator_18_eq, d_ff_1_q, d_ff_2_q, d_ff_3_q, d_ff_4_q, d_ff_5_q, d_ff_6_q, d_ff_7_q, d_ff_8_q,
       d_ff_9_q, d_ff_12_q, d_ff_14_q, d_ff_15_q, d_ff_16_q, d_ff_17_q;
  wire [6:0] keyboard_1_data;

  Clock clock_1 (.out(clock_1_out));
  Keyboard keyboard_1 (.clk(clock_1_out), .clr(\Сброс ), .data(keyboard_1_data));  // open: re, avail
  // Probe on keyboard_1_data
  // Probe on keyboard_1_data
  TTY tty_1 (.data(keyboard_1_data), .clk(clock_1_out), .clr(\Сброс ));  // open: we
  Comparator #(.width(7)) comparator_1 (.a(keyboard_1_data), .b(7'b1001000), .eq(comparator_1_eq));  // open: gt, lt
  Comparator #(.width(7)) comparator_2 (.a(keyboard_1_data), .b(7'b1000001), .eq(comparator_2_eq));  // open: gt, lt
  Comparator #(.width(7)) comparator_3 (.a(keyboard_1_data), .b(7'b1001100), .eq(comparator_3_eq));  // open: gt, lt
  Comparator #(.width(7)) comparator_4 (.a(keyboard_1_data), .b(7'b1010100), .eq(comparator_4_eq));  // open: gt, lt
  Comparator #(.width(7)) comparator_5 (.a(keyboard_1_data), .b(7'b1001101), .eq(comparator_5_eq));  // open: gt, lt
  Comparator #(.width(7)) comparator_6 (.a(keyboard_1_data), .b(7'b1001111), .eq(comparator_6_eq));  // open: gt, lt
  Comparator #(.width(7)) comparator_7 (.a(keyboard_1_data), .b(7'b1010110), .eq(comparator_7_eq));  // open: gt, lt
  Comparator #(.width(7)) comparator_8 (.a(keyboard_1_data), .b(7'b1000001), .eq(comparator_8_eq));  // open: gt, lt
  Comparator #(.width(7)) comparator_9 (.a(keyboard_1_data), .b(7'b1000100), .eq(comparator_9_eq));  // open: gt, lt
  Comparator #(.width(7)) comparator_10 (.a(keyboard_1_data), .b(7'b1000100), .eq(comparator_10_eq));  // open: gt, lt
  Comparator #(.width(7)) comparator_11 (.a(keyboard_1_data), .b(7'b1010011), .eq(comparator_11_eq));  // open: gt, lt
  Comparator #(.width(7)) comparator_12 (.a(keyboard_1_data), .b(7'b1010111), .eq(comparator_12_eq));  // open: gt, lt
  Comparator #(.width(7)) comparator_13 (.a(keyboard_1_data), .b(7'b1000001), .eq(comparator_13_eq));  // open: gt, lt
  Comparator #(.width(7)) comparator_14 (.a(keyboard_1_data), .b(7'b1010000), .eq(comparator_14_eq));  // open: gt, lt
  Comparator #(.width(7)) comparator_15 (.a(keyboard_1_data), .b(7'b1011111), .eq(comparator_15_eq));  // open: gt, lt
  Comparator #(.width(7)) comparator_16 (.a(keyboard_1_data), .b(7'b1000001), .eq(comparator_16_eq));  // open: gt, lt
  Comparator #(.width(7)) comparator_17 (.a(keyboard_1_data), .b(7'b1001100), .eq(comparator_17_eq));  // open: gt, lt
  Comparator #(.width(7)) comparator_18 (.a(keyboard_1_data), .b(7'b1010101), .eq(comparator_18_eq));  // open: gt, lt
  D_Flip_Flop d_ff_1 (.clk(clock_1_out), .D(comparator_1_eq), .Q(d_ff_1_q));  // open: Qn, preset, en, reset
  and and_1 (and_1_out, d_ff_1_q, comparator_2_eq);
  D_Flip_Flop d_ff_2 (.clk(clock_1_out), .D(comparator_5_eq), .Q(d_ff_2_q));  // open: Qn, preset, en, reset
  and and_2 (and_2_out, d_ff_2_q, comparator_6_eq);
  D_Flip_Flop d_ff_3 (.clk(clock_1_out), .D(comparator_8_eq), .Q(d_ff_3_q));  // open: Qn, preset, en, reset
  and and_3 (and_3_out, d_ff_3_q, comparator_9_eq);
  D_Flip_Flop d_ff_4 (.clk(clock_1_out), .D(comparator_11_eq), .Q(d_ff_4_q));  // open: Qn, preset, en, reset
  and and_4 (and_4_out, d_ff_4_q, comparator_12_eq);
  D_Flip_Flop d_ff_5 (.clk(clock_1_out), .D(and_1_out), .Q(d_ff_5_q));  // open: Qn, preset, en, reset
  and and_5 (and_5_out, d_ff_5_q, comparator_3_eq);
  D_Flip_Flop d_ff_6 (.clk(clock_1_out), .D(and_2_out), .Q(d_ff_6_q));  // open: Qn, preset, en, reset
  and and_6 (and_6_out, d_ff_6_q, comparator_7_eq);
  D_Flip_Flop d_ff_7 (.clk(clock_1_out), .D(and_3_out), .Q(d_ff_7_q));  // open: Qn, preset, en, reset
  and and_7 (and_7_out, d_ff_7_q, comparator_10_eq);
  D_Flip_Flop d_ff_8 (.clk(clock_1_out), .D(and_4_out), .Q(d_ff_8_q));  // open: Qn, preset, en, reset
  and and_8 (and_8_out, d_ff_8_q, comparator_13_eq);
  D_Flip_Flop d_ff_9 (.clk(clock_1_out), .D(and_5_out), .Q(d_ff_9_q));  // open: Qn, preset, en, reset
  D_Flip_Flop d_ff_10 (.clk(clock_1_out), .D(and_6_out), .Q(MOV));  // open: Qn, preset, en, reset
  D_Flip_Flop d_ff_11 (.clk(clock_1_out), .D(and_7_out), .Q(ADD));  // open: Qn, preset, en, reset
  D_Flip_Flop d_ff_12 (.clk(clock_1_out), .D(and_8_out), .Q(d_ff_12_q));  // open: Qn, preset, en, reset
  D_Flip_Flop d_ff_13 (.clk(clock_1_out), .D(and_9_out), .Q(HALT));  // open: Qn, preset, en, reset
  and and_9 (and_9_out, d_ff_9_q, comparator_4_eq);
  D_Flip_Flop d_ff_14 (.clk(clock_1_out), .D(and_10_out), .Q(d_ff_14_q));  // open: Qn, preset, en, reset
  and and_10 (and_10_out, d_ff_12_q, comparator_14_eq);
  and and_11 (and_11_out, d_ff_14_q, comparator_15_eq);
  D_Flip_Flop d_ff_15 (.clk(clock_1_out), .D(and_11_out), .Q(d_ff_15_q));  // open: Qn, preset, en, reset
  and and_12 (and_12_out, d_ff_15_q, comparator_16_eq);
  D_Flip_Flop d_ff_16 (.clk(clock_1_out), .D(and_12_out), .Q(d_ff_16_q));  // open: Qn, preset, en, reset
  D_Flip_Flop d_ff_17 (.clk(clock_1_out), .D(and_13_out), .Q(d_ff_17_q));  // open: Qn, preset, en, reset
  and and_13 (and_13_out, d_ff_16_q, comparator_17_eq);
  D_Flip_Flop d_ff_18 (.clk(clock_1_out), .D(and_14_out), .Q(SWAP_ALU));  // open: Qn, preset, en, reset
  and and_14 (and_14_out, d_ff_17_q, comparator_18_eq);
endmodule

module \Пример_из_лекции  (
  input  \Сброс ,
  output HLT
);

  wire and_1_out, and_2_out, clock_1_out, comparator_1_eq, comparator_2_eq, comparator_3_eq, d_ff_1_q,
       d_ff_2_q;
  wire [6:0] keyboard_1_data;

  Clock clock_1 (.out(clock_1_out));
  Keyboard keyboard_1 (.clk(clock_1_out), .clr(\Сброс ), .data(keyboard_1_data));  // open: re, avail
  // Probe on keyboard_1_data
  // Probe on keyboard_1_data
  TTY tty_1 (.data(keyboard_1_data), .clk(clock_1_out), .clr(\Сброс ));  // open: we
  Comparator #(.width(7)) comparator_1 (.a(keyboard_1_data), .b(7'b1001000), .eq(comparator_1_eq));  // open: gt, lt
  Comparator #(.width(7)) comparator_2 (.a(keyboard_1_data), .b(7'b1001100), .eq(comparator_2_eq));  // open: gt, lt
  Comparator #(.width(7)) comparator_3 (.a(keyboard_1_data), .b(7'b1010100), .eq(comparator_3_eq));  // open: gt, lt
  D_Flip_Flop d_ff_1 (.clk(clock_1_out), .D(comparator_1_eq), .Q(d_ff_1_q));  // open: Qn, preset, en, reset
  and and_1 (and_1_out, d_ff_1_q, comparator_2_eq);
  D_Flip_Flop d_ff_2 (.clk(clock_1_out), .D(and_1_out), .Q(d_ff_2_q));  // open: Qn, preset, en, reset
  and and_2 (and_2_out, d_ff_2_q, comparator_3_eq);
  D_Flip_Flop d_ff_3 (.clk(clock_1_out), .D(and_2_out), .Q(HLT));  // open: Qn, preset, en, reset
endmodule
