// Logisim project Lab_5_cybernetica.circ as structural Verilog: 9 circuits, main circuit Lab_5
module Lab_5 (
  input  _0,
  input  _1,
  input  _2,
  input  _3,
  input  _4,
  input  _5,
  input  _6,
  input  _7,
  input  _8,
  input  _9,
  input  A,
  input  B,
  input  [2:0] \Вход_0 ,
  input  C,
  input  [2:0] \Вход_1 ,
  input  D,
  input  [2:0] \Вход_2 ,
  input  E,
  input  [2:0] \Вход_3 ,
  input  F,
  input  [2:0] in_21,
  input  [2:0] \Вход_4 ,
  input  [2:0] \Вход_5 ,
  input  [2:0] \Вход_6 ,
  input  [2:0] \Вход_7 ,
  input  [2:0] in_26,
  input  [2:0] in_27,
  output [2:0] \Выход_0 ,
  output [2:0] \Выход_1 ,
  output [2:0] \Выход_2 ,
  output [2:0] \Выход_3 ,
  output [2:0] out_32,
  output [2:0] \Выход_4 ,
  output [2:0] \Выход_5 ,
  output [2:0] \Выход_6 ,
  output [2:0] \Выход_7 
);

  wire [3:0] \перевод_в_16_ричную_1_out_17 ;
  wire [7:0] \перевод_из_16_ричной_в_7_сегментов_1_out_2 ;

  \Перевод_в_16_ричную  \u_перевод_в_16_ричную_1  (
    ._0(_0), ._1(_1), ._2(_2), ._3(_3), ._4(_4), ._5(_5), ._6(_6), ._7(_7), ._8(_8), ._9(_9), .A(A), .B(B),
    .C(C), .D(D), .E(E), .F(F), .out_17(\перевод_в_16_ричную_1_out_17 ));
  // Probe on \перевод_в_16_ричную_1_out_17 
  // Probe on \перевод_в_16_ричную_1_out_17 
  \Перевод_из_16_ричной_в_7_сегментов  \u_перевод_из_16_ричной_в_7_сегментов_1  (
    .in_1(\перевод_в_16_ричную_1_out_17 ), .out_2(\перевод_из_16_ричной_в_7_сегментов_1_out_2 ));
  _7_Segment_Display u_7_segment_display_1 (
    .g(\перевод_из_16_ричной_в_7_сегментов_1_out_2 [3]), .f(\перевод_из_16_ричной_в_7_сегментов_1_out_2 [2]),
    .a(\перевод_из_16_ричной_в_7_сегментов_1_out_2 [1]), .b(\перевод_из_16_ричной_в_7_сегментов_1_out_2 [0]),
    .e(\перевод_из_16_ричной_в_7_сегментов_1_out_2 [7]), .d(\перевод_из_16_ричной_в_7_сегментов_1_out_2 [6]),
    .c(\перевод_из_16_ричной_в_7_сегментов_1_out_2 [5]), .dp(\перевод_из_16_ричной_в_7_сегментов_1_out_2 [4]));
  \Мультиплексер_3_бит  \u_мультиплексер_3_бит_1  (
    .in_1(\Вход_0 ), .in_2(\Вход_1 ), .in_3(\Вход_2 ), .in_4(\Вход_3 ), .in_5(\Вход_4 ), .in_6(\Вход_5 ),
    .in_7(\Вход_6 ), .in_8(\Вход_7 ), .out_12(out_32), .\Бит_2 (in_26[2]), .\Бит_1 (in_26[1]),
    .\Бит_0 (in_26[0]));
  \Демультиплексер_3_бит  \u_демультиплексер_3_бит_1  (
    .a(in_21), .\Бит_2 (in_27[2]), .\Бит_1 (in_27[1]), .\Бит_0 (in_27[0]), .x(\Выход_0 ), .y(\Выход_1 ),
    .z(\Выход_2 ), .u(\Выход_3 ), .v(\Выход_4 ), .w(\Выход_5 ), .s(\Выход_6 ), .t(\Выход_7 ));
endmodule

module \Перевод_в_16_ричную  (
  input  _0,
  input  _1,
  input  _2,
  input  _3,
  input  _4,
  input  _5,
  input  _6,
  input  _7,
  input  _8,
  input  _9,
  input  A,
  input  B,
  input  C,
  input  D,
  input  E,
  input  F,
  output [3:0] out_17
);

  \Бит_0  \u_бит_0_1  (.in_1({F, E, D, C, B, A, _9, _8, _7, _6, _5, _4, _3, _2, _1, _0}), .out_2(out_17[0]));
  \Бит_1  \u_бит_1_1  (.in_1({F, E, D, C, B, A, _9, _8, _7, _6, _5, _4, _3, _2, _1, _0}), .out_2(out_17[1]));
  \Бит_2  \u_бит_2_1  (.in_1({F, E, D, C, B, A, _9, _8, _7, _6, _5, _4, _3, _2, _1, _0}), .out_2(out_17[2]));
  \Бит_3  \u_бит_3_1  (.in_1({F, E, D, C, B, A, _9, _8, _7, _6, _5, _4, _3, _2, _1, _0}), .out_2(out_17[3]));
  // Probe on out_17
endmodule

module \Перевод_из_16_ричной_в_7_сегментов  (
  input  [3:0] in_1,
  output [7:0] out_2
);

  wire and_1_out, and_2_out, and_3_out, and_4_out, and_5_out, and_6_out, and_7_out, and_8_out, and_9_out,
       and_10_out, and_11_out, and_12_out, and_13_out, and_14_out, and_15_out, and_16_out, and_17_out,
       and_18_out, and_19_out, and_20_out, and_21_out, and_22_out, and_23_out, and_24_out, and_25_out,
       and_26_out, and_27_out, and_28_out, and_29_out, and_30_out, and_31_out, and_32_out, and_33_out,
       and_34_out, and_35_out, and_36_out, not_1_out, not_2_out, not_3_out, not_4_out, not_5_out, not_6_out,
       not_7_out, not_8_out, not_9_out, not_10_out, not_11_out, not_12_out, not_13_out, not_14_out,
       not_15_out, not_16_out, not_17_out, not_18_out, not_19_out, not_20_out, not_21_out, not_22_out,
       not_23_out, not_24_out, not_25_out, not_26_out, not_27_out, not_28_out, not_29_out, not_30_out,
       not_31_out, not_32_out, not_33_out, not_34_out, not_35_out, not_36_out, not_37_out, not_38_out,
       not_39_out, not_40_out, not_41_out, not_42_out, not_43_out, not_44_out, not_45_out;

  not not_1 (not_1_out, in_1[2]);
  not not_2 (not_2_out, in_1[0]);
  not not_3 (not_3_out, in_1[0]);
  not not_4 (not_4_out, in_1[3]);
  not not_5 (not_5_out, in_1[2]);
  not not_6 (not_6_out, in_1[0]);
  not not_7 (not_7_out, in_1[2]);
  not not_8 (not_8_out, in_1[1]);
  not not_9 (not_9_out, in_1[0]);
  not not_10 (not_10_out, in_1[1]);
  not not_11 (not_11_out, in_1[3]);
  not not_12 (not_12_out, in_1[1]);
  not not_13 (not_13_out, in_1[3]);
  not not_14 (not_14_out, in_1[1]);
  not not_15 (not_15_out, in_1[3]);
  not not_16 (not_16_out, in_1[2]);
  not not_17 (not_17_out, in_1[2]);
  not not_18 (not_18_out, in_1[0]);
  not not_19 (not_19_out, in_1[3]);
  not not_20 (not_20_out, in_1[1]);
  not not_21 (not_21_out, in_1[2]);
  not not_22 (not_22_out, in_1[1]);
  not not_23 (not_23_out, in_1[0]);
  not not_24 (not_24_out, in_1[3]);
  not not_25 (not_25_out, in_1[1]);
  not not_26 (not_26_out, in_1[0]);
  not not_27 (not_27_out, in_1[2]);
  not not_28 (not_28_out, in_1[2]);
  not not_29 (not_29_out, in_1[0]);
  not not_30 (not_30_out, in_1[3]);
  not not_31 (not_31_out, in_1[3]);
  not not_32 (not_32_out, in_1[2]);
  not not_33 (not_33_out, in_1[1]);
  not not_34 (not_34_out, in_1[0]);
  not not_35 (not_35_out, in_1[3]);
  not not_36 (not_36_out, in_1[2]);
  not not_37 (not_37_out, in_1[3]);
  not not_38 (not_38_out, in_1[1]);
  not not_39 (not_39_out, in_1[0]);
  not not_40 (not_40_out, in_1[2]);
  not not_41 (not_41_out, in_1[1]);
  not not_42 (not_42_out, in_1[2]);
  not not_43 (not_43_out, in_1[0]);
  not not_44 (not_44_out, in_1[3]);
  not not_45 (not_45_out, in_1[1]);
  and and_1 (and_1_out, not_1_out, not_2_out);
  and and_2 (and_2_out, in_1[1], not_3_out);
  and and_3 (and_3_out, in_1[3], in_1[1]);
  and and_4 (and_4_out, in_1[3], in_1[2]);
  and and_5 (and_5_out, not_4_out, not_5_out, not_6_out);
  and and_6 (and_6_out, not_7_out, in_1[1], in_1[0]);
  and and_7 (and_7_out, in_1[2], not_8_out, in_1[0]);
  and and_8 (and_8_out, in_1[2], in_1[1], not_9_out);
  and and_9 (and_9_out, in_1[3], not_10_out);
  and and_10 (and_10_out, not_11_out, not_12_out);
  and and_11 (and_11_out, not_13_out, in_1[0]);
  and and_12 (and_12_out, not_14_out, in_1[0]);
  and and_13 (and_13_out, not_15_out, in_1[2]);
  and and_14 (and_14_out, in_1[3], not_16_out);
  and and_15 (and_15_out, not_17_out, in_1[1]);
  and and_16 (and_16_out, in_1[1], not_18_out);
  and and_17 (and_17_out, not_19_out, in_1[2], not_20_out);
  and and_18 (and_18_out, in_1[3], not_21_out);
  and and_19 (and_19_out, in_1[3], in_1[0]);
  and and_20 (and_20_out, not_22_out, not_23_out);
  and and_21 (and_21_out, not_24_out, in_1[2], not_25_out);
  and and_22 (and_22_out, in_1[2], not_26_out);
  and and_23 (and_23_out, in_1[3], not_27_out);
  and and_24 (and_24_out, in_1[3], in_1[1]);
  and and_25 (and_25_out, not_28_out, not_29_out);
  and and_26 (and_26_out, not_30_out, in_1[1]);
  and and_27 (and_27_out, not_31_out, in_1[2], in_1[0]);
  and and_28 (and_28_out, in_1[2], in_1[1]);
  and and_29 (and_29_out, in_1[3], not_32_out, not_33_out);
  and and_30 (and_30_out, in_1[3], not_34_out);
  and and_31 (and_31_out, not_35_out, not_36_out);
  and and_32 (and_32_out, not_37_out, not_38_out, not_39_out);
  and and_33 (and_33_out, not_40_out, not_41_out);
  and and_34 (and_34_out, not_42_out, not_43_out);
  and and_35 (and_35_out, not_44_out, in_1[1], in_1[0]);
  and and_36 (and_36_out, in_1[3], not_45_out, in_1[0]);
  or or_1 (out_2[7], and_1_out, and_2_out, and_3_out, and_4_out);
  or or_2 (out_2[6], and_5_out, and_6_out, and_7_out, and_8_out, and_9_out);
  or or_3 (out_2[5], and_10_out, and_11_out, and_12_out, and_13_out, and_14_out);
  or or_4 (out_2[3], and_15_out, and_16_out, and_17_out, and_18_out, and_19_out);
  or or_5 (out_2[2], and_20_out, and_21_out, and_22_out, and_23_out, and_24_out);
  or or_6 (out_2[1], and_25_out, and_26_out, and_27_out, and_28_out, and_29_out, and_30_out);
  or or_7 (out_2[0], and_31_out, and_32_out, and_33_out, and_34_out, and_35_out, and_36_out);

  assign out_2[4] = 1'b0;
endmodule

module \Бит_3  (
  input  [15:0] in_1,
  output out_2
);

  wire and_1_out, and_2_out, and_3_out, and_4_out, and_5_out, and_6_out, and_7_out, and_8_out;

  and and_1 (and_1_out, ~in_1[0], ~in_1[1], ~in_1[2], ~in_1[3], ~in_1[4], ~in_1[5], ~in_1[6], ~in_1[7], ~in_1[8], ~in_1[9], ~in_1[10], ~in_1[11], ~in_1[12], ~in_1[13], ~in_1[14], in_1[15]);  // AND_Gate
  and and_2 (and_2_out, ~in_1[0], ~in_1[1], ~in_1[2], ~in_1[3], ~in_1[4], ~in_1[5], ~in_1[6], ~in_1[7], ~in_1[8], ~in_1[9], ~in_1[10], ~in_1[11], ~in_1[12], ~in_1[13], in_1[14], ~in_1[15]);  // AND_Gate
  and and_3 (and_3_out, ~in_1[0], ~in_1[1], ~in_1[2], ~in_1[3], ~in_1[4], ~in_1[5], ~in_1[6], ~in_1[7], ~in_1[8], ~in_1[9], ~in_1[10], ~in_1[11], ~in_1[12], in_1[13], ~in_1[14], ~in_1[15]);  // AND_Gate
  and and_4 (and_4_out, ~in_1[0], ~in_1[1], ~in_1[2], ~in_1[3], ~in_1[4], ~in_1[5], ~in_1[6], ~in_1[7], ~in_1[8], ~in_1[9], ~in_1[10], ~in_1[11], in_1[12], ~in_1[13], ~in_1[14], ~in_1[15]);  // AND_Gate
  and and_5 (and_5_out, ~in_1[0], ~in_1[1], ~in_1[2], ~in_1[3], ~in_1[4], ~in_1[5], ~in_1[6], ~in_1[7], ~in_1[8], ~in_1[9], ~in_1[10], in_1[11], ~in_1[12], ~in_1[13], ~in_1[14], ~in_1[15]);  // AND_Gate
  and and_6 (and_6_out, ~in_1[0], ~in_1[1], ~in_1[2], ~in_1[3], ~in_1[4], ~in_1[5], ~in_1[6], ~in_1[7], ~in_1[8], ~in_1[9], in_1[10], ~in_1[11], ~in_1[12], ~in_1[13], ~in_1[14], ~in_1[15]);  // AND_Gate
  and and_7 (and_7_out, ~in_1[0], ~in_1[1], ~in_1[2], ~in_1[3], ~in_1[4], ~in_1[5], ~in_1[6], ~in_1[7], ~in_1[8], in_1[9], ~in_1[10], ~in_1[11], ~in_1[12], ~in_1[13], ~in_1[14], ~in_1[15]);  // AND_Gate
  and and_8 (and_8_out, ~in_1[0], ~in_1[1], ~in_1[2], ~in_1[3], ~in_1[4], ~in_1[5], ~in_1[6], ~in_1[7], in_1[8], ~in_1[9], ~in_1[10], ~in_1[11], ~in_1[12], ~in_1[13], ~in_1[14], ~in_1[15]);  // AND_Gate
  or or_1 (out_2, and_1_out, and_2_out, and_3_out, and_4_out, and_5_out, and_6_out, and_7_out, and_8_out);
endmodule

module \Бит_2  (
  input  [15:0] in_1,
  output out_2
);

  wire and_1_out, and_2_out, and_3_out, and_4_out, and_5_out, and_6_out, and_7_out, and_8_out;

  and and_1 (and_1_out, ~in_1[0], ~in_1[1], ~in_1[2], ~in_1[3], ~in_1[4], ~in_1[5], ~in_1[6], ~in_1[7], ~in_1[8], ~in_1[9], ~in_1[10], ~in_1[11], ~in_1[12], ~in_1[13], ~in_1[14], in_1[15]);  // AND_Gate
  and and_2 (and_2_out, ~in_1[0], ~in_1[1], ~in_1[2], ~in_1[3], ~in_1[4], ~in_1[5], ~in_1[6], ~in_1[7], ~in_1[8], ~in_1[9], ~in_1[10], ~in_1[11], ~in_1[12], ~in_1[13], in_1[14], ~in_1[15]);  // AND_Gate
  and and_3 (and_3_out, ~in_1[0], ~in_1[1], ~in_1[2], ~in_1[3], ~in_1[4], ~in_1[5], ~in_1[6], ~in_1[7], ~in_1[8], ~in_1[9], ~in_1[10], ~in_1[11], ~in_1[12], in_1[13], ~in_1[14], ~in_1[15]);  // AND_Gate
  and and_4 (and_4_out, ~in_1[0], ~in_1[1], ~in_1[2], ~in_1[3], ~in_1[4], ~in_1[5], ~in_1[6], ~in_1[7], ~in_1[8], ~in_1[9], ~in_1[10], ~in_1[11], in_1[12], ~in_1[13], ~in_1[14], ~in_1[15]);  // AND_Gate
  and and_5 (and_5_out, ~in_1[0], ~in_1[1], ~in_1[2], ~in_1[3], ~in_1[4], ~in_1[5], ~in_1[6], in_1[7], ~in_1[8], ~in_1[9], ~in_1[10], ~in_1[11], ~in_1[12], ~in_1[13], ~in_1[14], ~in_1[15]);  // AND_Gate
  and and_6 (and_6_out, ~in_1[0], ~in_1[1], ~in_1[2], ~in_1[3], ~in_1[4], ~in_1[5], in_1[6], ~in_1[7], ~in_1[8], ~in_1[9], ~in_1[10], ~in_1[11], ~in_1[12], ~in_1[13], ~in_1[14], ~in_1[15]);  // AND_Gate
  and and_7 (and_7_out, ~in_1[0], ~in_1[1], ~in_1[2], ~in_1[3], ~in_1[4], in_1[5], ~in_1[6], ~in_1[7], ~in_1[8], ~in_1[9], ~in_1[10], ~in_1[11], ~in_1[12], ~in_1[13], ~in_1[14], ~in_1[15]);  // AND_Gate
  and and_8 (and_8_out, ~in_1[0], ~in_1[1], ~in_1[2], ~in_1[3], in_1[4], ~in_1[5], ~in_1[6], ~in_1[7], ~in_1[8], ~in_1[9], ~in_1[10], ~in_1[11], ~in_1[12], ~in_1[13], ~in_1[14], ~in_1[15]);  // AND_Gate
  or or_1 (out_2, and_1_out, and_2_out, and_3_out, and_4_out, and_5_out, and_6_out, and_7_out, and_8_out);
endmodule

module \Бит_1  (
  input  [15:0] in_1,
  output out_2
);

  wire and_1_out, and_2_out, and_3_out, and_4_out, and_5_out, and_6_out, and_7_out, and_8_out;

  and and_1 (and_1_out, ~in_1[0], ~in_1[1], ~in_1[2], ~in_1[3], ~in_1[4], ~in_1[5], ~in_1[6], ~in_1[7], ~in_1[8], ~in_1[9], ~in_1[10], ~in_1[11], ~in_1[12], ~in_1[13], ~in_1[14], in_1[15]);  // AND_Gate
  and and_2 (and_2_out, ~in_1[0], ~in_1[1], ~in_1[2], ~in_1[3], ~in_1[4], ~in_1[5], ~in_1[6], ~in_1[7], ~in_1[8], ~in_1[9], ~in_1[10], ~in_1[11], ~in_1[12], ~in_1[13], in_1[14], ~in_1[15]);  // AND_Gate
  and and_3 (and_3_out, ~in_1[0], ~in_1[1], ~in_1[2], ~in_1[3], ~in_1[4], ~in_1[5], ~in_1[6], ~in_1[7], ~in_1[8], ~in_1[9], ~in_1[10], in_1[11], ~in_1[12], ~in_1[13], ~in_1[14], ~in_1[15]);  // AND_Gate
  and and_4 (and_4_out, ~in_1[0], ~in_1[1], ~in_1[2], ~in_1[3], ~in_1[4], ~in_1[5], ~in_1[6], ~in_1[7], ~in_1[8], ~in_1[9], in_1[10], ~in_1[11], ~in_1[12], ~in_1[13], ~in_1[14], ~in_1[15]);  // AND_Gate
  and and_5 (and_5_out, ~in_1[0], ~in_1[1], ~in_1[2], ~in_1[3], ~in_1[4], ~in_1[5], ~in_1[6], in_1[7], ~in_1[8], ~in_1[9], ~in_1[10], ~in_1[11], ~in_1[12], ~in_1[13], ~in_1[14], ~in_1[15]);  // AND_Gate
  and and_6 (and_6_out, ~in_1[0], ~in_1[1], ~in_1[2], ~in_1[3], ~in_1[4], ~in_1[5], in_1[6], ~in_1[7], ~in_1[8], ~in_1[9], ~in_1[10], ~in_1[11], ~in_1[12], ~in_1[13], ~in_1[14], ~in_1[15]);  // AND_Gate
  and and_7 (and_7_out, ~in_1[0], ~in_1[1], ~in_1[2], in_1[3], ~in_1[4], ~in_1[5], ~in_1[6], ~in_1[7], ~in_1[8], ~in_1[9], ~in_1[10], ~in_1[11], ~in_1[12], ~in_1[13], ~in_1[14], ~in_1[15]);  // AND_Gate
  and and_8 (and_8_out, ~in_1[0], ~in_1[1], in_1[2], ~in_1[3], ~in_1[4], ~in_1[5], ~in_1[6], ~in_1[7], ~in_1[8], ~in_1[9], ~in_1[10], ~in_1[11], ~in_1[12], ~in_1[13], ~in_1[14], ~in_1[15]);  // AND_Gate
  or or_1 (out_2, and_1_out, and_2_out, and_3_out, and_4_out, and_5_out, and_6_out, and_7_out, and_8_out);
endmodule

module \Бит_0  (
  input  [15:0] in_1,
  output out_2
);

  wire and_1_out, and_2_out, and_3_out, and_4_out, and_5_out, and_6_out, and_7_out, and_8_out;

  and and_1 (and_1_out, ~in_1[0], ~in_1[1], ~in_1[2], ~in_1[3], ~in_1[4], ~in_1[5], ~in_1[6], ~in_1[7], ~in_1[8], ~in_1[9], ~in_1[10], ~in_1[11], ~in_1[12], ~in_1[13], ~in_1[14], in_1[15]);  // AND_Gate
  and and_2 (and_2_out, ~in_1[0], ~in_1[1], ~in_1[2], ~in_1[3], ~in_1[4], ~in_1[5], ~in_1[6], ~in_1[7], ~in_1[8], ~in_1[9], ~in_1[10], ~in_1[11], ~in_1[12], in_1[13], ~in_1[14], ~in_1[15]);  // AND_Gate
  and and_3 (and_3_out, ~in_1[0], ~in_1[1], ~in_1[2], ~in_1[3], ~in_1[4], ~in_1[5], ~in_1[6], ~in_1[7], ~in_1[8], ~in_1[9], ~in_1[10], in_1[11], ~in_1[12], ~in_1[13], ~in_1[14], ~in_1[15]);  // AND_Gate
  and and_4 (and_4_out, ~in_1[0], ~in_1[1], ~in_1[2], ~in_1[3], ~in_1[4], ~in_1[5], ~in_1[6], ~in_1[7], ~in_1[8], in_1[9], ~in_1[10], ~in_1[11], ~in_1[12], ~in_1[13], ~in_1[14], ~in_1[15]);  // AND_Gate
  and and_5 (and_5_out, ~in_1[0], ~in_1[1], ~in_1[2], ~in_1[3], ~in_1[4], ~in_1[5], ~in_1[6], in_1[7], ~in_1[8], ~in_1[9], ~in_1[10], ~in_1[11], ~in_1[12], ~in_1[13], ~in_1[14], ~in_1[15]);  // AND_Gate
  and and_6 (and_6_out, ~in_1[0], ~in_1[1], ~in_1[2], ~in_1[3], ~in_1[4], in_1[5], ~in_1[6], ~in_1[7], ~in_1[8], ~in_1[9], ~in_1[10], ~in_1[11], ~in_1[12], ~in_1[13], ~in_1[14], ~in_1[15]);  // AND_Gate
  and and_7 (and_7_out, ~in_1[0], ~in_1[1], ~in_1[2], in_1[3], ~in_1[4], ~in_1[5], ~in_1[6], ~in_1[7], ~in_1[8], ~in_1[9], ~in_1[10], ~in_1[11], ~in_1[12], ~in_1[13], ~in_1[14], ~in_1[15]);  // AND_Gate
  and and_8 (and_8_out, ~in_1[0], in_1[1], ~in_1[2], ~in_1[3], ~in_1[4], ~in_1[5], ~in_1[6], ~in_1[7], ~in_1[8], ~in_1[9], ~in_1[10], ~in_1[11], ~in_1[12], ~in_1[13], ~in_1[14], ~in_1[15]);  // AND_Gate
  or or_1 (out_2, and_1_out, and_2_out, and_3_out, and_4_out, and_5_out, and_6_out, and_7_out, and_8_out);
endmodule

module \Мультиплексер_3_бит  (
  input  [2:0] in_1,
  input  [2:0] in_2,
  input  [2:0] in_3,
  input  [2:0] in_4,
  input  [2:0] in_5,
  input  [2:0] in_6,
  input  [2:0] in_7,
  input  [2:0] in_8,
  input  \Бит_2 ,
  input  \Бит_1 ,
  input  \Бит_0 ,
  output [2:0] out_12
);

  wire [2:0] transistor_1_out, transistor_2_out, transistor_3_out, transistor_4_out, transistor_5_out,
       transistor_6_out, transistor_7_out, transistor_8_out, transistor_9_out, transistor_11_out,
       transistor_13_out, transistor_16_out, transistor_17_out, transistor_19_out, transistor_21_out,
       transistor_23_out;

  Transistor #(.width(3)) transistor_1 (.in(in_1), .out(transistor_1_out), .gate(\Бит_2 ));
  Transistor #(.width(3)) transistor_2 (.in(in_2), .out(transistor_2_out), .gate(\Бит_2 ));
  Transistor #(.width(3)) transistor_3 (.in(in_3), .out(transistor_3_out), .gate(\Бит_2 ));
  Transistor #(.width(3)) transistor_4 (.in(in_4), .out(transistor_4_out), .gate(\Бит_2 ));
  Transistor #(.\type ("n"), .width(3)) transistor_5 (.in(in_5), .out(transistor_5_out), .gate(\Бит_2 ));
  Transistor #(.\type ("n"), .width(3)) transistor_6 (.in(in_6), .out(transistor_6_out), .gate(\Бит_2 ));
  Transistor #(.\type ("n"), .width(3)) transistor_7 (.in(in_7), .out(transistor_7_out), .gate(\Бит_2 ));
  Transistor #(.\type ("n"), .width(3)) transistor_8 (.in(in_8), .out(transistor_8_out), .gate(\Бит_2 ));
  Transistor #(.width(3)) transistor_9 (.in(transistor_1_out), .out(transistor_9_out), .gate(\Бит_1 ));
  Transistor #(.width(3)) transistor_10 (.in(transistor_9_out), .out(out_12), .gate(\Бит_0 ));
  Transistor #(.width(3)) transistor_11 (.in(transistor_2_out), .out(transistor_11_out), .gate(\Бит_1 ));
  Transistor #(.\type ("n"), .width(3)) transistor_12 (.in(transistor_11_out), .out(out_12), .gate(\Бит_0 ));
  Transistor #(.\type ("n"), .width(3)) transistor_13 (.in(transistor_3_out), .out(transistor_13_out), .gate(\Бит_1 ));
  Transistor #(.width(3)) transistor_14 (.in(transistor_13_out), .out(out_12), .gate(\Бит_0 ));
  Transistor #(.\type ("n"), .width(3)) transistor_15 (.in(transistor_16_out), .out(out_12), .gate(\Бит_0 ));
  Transistor #(.\type ("n"), .width(3)) transistor_16 (.in(transistor_4_out), .out(transistor_16_out), .gate(\Бит_1 ));
  Transistor #(.width(3)) transistor_17 (.in(transistor_5_out), .out(transistor_17_out), .gate(\Бит_1 ));
  Transistor #(.width(3)) transistor_18 (.in(transistor_17_out), .out(out_12), .gate(\Бит_0 ));
  Transistor #(.width(3)) transistor_19 (.in(transistor_6_out), .out(transistor_19_out), .gate(\Бит_1 ));
  Transistor #(.\type ("n"), .width(3)) transistor_20 (.in(transistor_19_out), .out(out_12), .gate(\Бит_0 ));
  Transistor #(.\type ("n"), .width(3)) transistor_21 (.in(transistor_7_out), .out(transistor_21_out), .gate(\Бит_1 ));
  Transistor #(.width(3)) transistor_22 (.in(transistor_21_out), .out(out_12), .gate(\Бит_0 ));
  Transistor #(.\type ("n"), .width(3)) transistor_23 (.in(transistor_8_out), .out(transistor_23_out), .gate(\Бит_1 ));
  Transistor #(.\type ("n"), .width(3)) transistor_24 (.in(transistor_23_out), .out(out_12), .gate(\Бит_0 ));
endmodule

module \Демультиплексер_3_бит  (
  input  [2:0] a,
  input  \Бит_2 ,
  input  \Бит_1 ,
  input  \Бит_0 ,
  output [2:0] x,
  output [2:0] y,
  output [2:0] z,
  output [2:0] u,
  output [2:0] v,
  output [2:0] w,
  output [2:0] s,
  output [2:0] t
);

  wire [2:0] not_1_out, not_2_out, not_3_out, not_4_out, not_5_out, not_6_out, not_7_out, not_8_out,
       not_9_out, not_10_out, not_11_out, not_12_out;

  assign not_1_out = ~{3{\Бит_2 }};  // NOT_Gate not_1, 3 bits wide
  assign not_2_out = ~{3{\Бит_1 }};  // NOT_Gate not_2, 3 bits wide
  assign not_3_out = ~{3{\Бит_0 }};  // NOT_Gate not_3, 3 bits wide
  assign not_4_out = ~{3{\Бит_2 }};  // NOT_Gate not_4, 3 bits wide
  assign not_5_out = ~{3{\Бит_1 }};  // NOT_Gate not_5, 3 bits wide
  assign not_6_out = ~{3{\Бит_2 }};  // NOT_Gate not_6, 3 bits wide
  assign not_7_out = ~{3{\Бит_0 }};  // NOT_Gate not_7, 3 bits wide
  assign not_8_out = ~{3{\Бит_2 }};  // NOT_Gate not_8, 3 bits wide
  assign not_9_out = ~{3{\Бит_1 }};  // NOT_Gate not_9, 3 bits wide
  assign not_10_out = ~{3{\Бит_0 }};  // NOT_Gate not_10, 3 bits wide
  assign not_11_out = ~{3{\Бит_1 }};  // NOT_Gate not_11, 3 bits wide
  assign not_12_out = ~{3{\Бит_0 }};  // NOT_Gate not_12, 3 bits wide
  assign t = a & {3{\Бит_2 }} & {3{\Бит_1 }} & {3{\Бит_0 }};  // AND_Gate and_1, 3 bits wide
  assign x = a & not_1_out & not_2_out & not_3_out;  // AND_Gate and_2, 3 bits wide
  assign y = a & not_4_out & not_5_out & {3{\Бит_0 }};  // AND_Gate and_3, 3 bits wide
  assign z = a & not_6_out & {3{\Бит_1 }} & not_7_out;  // AND_Gate and_4, 3 bits wide
  assign u = a & not_8_out & {3{\Бит_1 }} & {3{\Бит_0 }};  // AND_Gate and_5, 3 bits wide
  assign v = a & {3{\Бит_2 }} & not_9_out & not_10_out;  // AND_Gate and_6, 3 bits wide
  assign w = a & {3{\Бит_2 }} & not_11_out & {3{\Бит_0 }};  // AND_Gate and_7, 3 bits wide
  assign s = a & {3{\Бит_2 }} & {3{\Бит_1 }} & not_12_out;  // AND_Gate and_8, 3 bits wide
endmodule
