// Logisim project Lab_6_cybernetica.circ as structural Verilog: 15 circuits, main circuit SR триггер
module Lab_6 (
  input  in_1,
  input  in_2,
  input  in_3,
  input  in_4,
  input  in_5,
  input  in_6,
  input  in_7,
  input  in_8,
  input  in_9,
  input  in_10,
  input  [7:0] in_11,
  input  in_12,
  input  in_13,
  input  \SR_триггер ,
  input  in_15,
  input  in_16,
  input  in_17,
  input  [7:0] in_18,
  input  in_19,
  input  in_20,
  input  in_21,
  input  \Регистр_8_бит ,
  input  in_23,
  input  in_24,
  input  in_25,
  input  in_26,
  input  in_27,
  input  in_28,
  input  in_29,
  input  in_30,
  input  in_31,
  input  in_32,
  input  in_33,
  input  \T_триггер ,
  input  \JK_триггер ,
  input  in_36,
  input  in_37,
  input  [2:0] in_38,
  input  [2:0] in_39,
  input  in_40,
  input  in_41,
  input  in_42,
  input  in_43,
  input  in_44,
  input  in_45,
  input  in_46,
  input  in_47,
  input  [7:0] in_48,
  input  in_49,
  input  in_50,
  input  in_51,
  input  in_52,
  input  [7:0] in_53,
  input  [9:0] in_54,
  input  [9:0] in_55,
  input  in_56,
  input  in_57,
  input  in_58,
  output [7:0] out_59,
  output out_60,
  output out_61,
  output out_62,
  output out_63,
  output out_64,
  output out_65,
  output [7:0] out_66,
  output out_67,
  output out_68,
  output out_69,
  output out_70,
  output out_71,
  output out_72,
  output out_73,
  output [3:0] out_74,
  output out_75,
  output out_76,
  output [7:0] out_77,
  output [7:0] out_78,
  output out_79
);

  wire not_1_out, not_2_out, \детектор_переднего_фронта_1_out_2 , \детектор_переднего_фронта_2_out_2 ;

  \SR_триггер  \sr_триггер_1  (.in_1(\SR_триггер ), .in_2(in_16), .in_3(in_17), .out_4(out_64), .out_5(out_65));
  \T_триггер  \t_триггер_1  (.T(in_40), .in_3(in_43), .out_5(out_72), .out_6(out_75), .in_1(\T_триггер ), .in_4(in_46));
  // Probe on in_53
  \Детектор_переднего_фронта  \u_детектор_переднего_фронта_1  (
    .in_1(in_26), .out_2(\детектор_переднего_фронта_1_out_2 ));
  \D_триггер  \d_триггер_1  (.in_2(in_5), .in_3(in_8), .out_5(out_60), .out_6(out_62), .in_1(in_2), .in_4(in_12));
  \D_триггер  \d_триггер_2  (
    .in_2(in_24), .in_3(\детектор_переднего_фронта_1_out_2 ), .out_5(out_67), .out_6(out_69), .in_1(in_19),
    .in_4(in_28));
  \JK_триггер  \jk_триггер_1  (
    .in_2(in_37), .in_3(in_42), .in_4(in_44), .out_6(out_73), .out_7(out_76), .in_1(\JK_триггер ),
    .in_5(in_47));
  // Probe on out_78
  \Сумматор_с_памятью  \u_сумматор_с_памятью_1  (
    .in_1(in_52), .in_5(in_53), .out_6(out_78), .out_7(out_79), .in_2(in_56), .in_3(in_57), .in_4(in_58));
  not not_1 (not_1_out, in_27);
  not not_2 (not_2_out, in_9);
  \Детектор_переднего_фронта  \u_детектор_переднего_фронта_2  (
    .in_1(not_1_out), .out_2(\детектор_переднего_фронта_2_out_2 ));
  \D_триггер  \d_триггер_3  (.in_2(in_6), .in_3(not_2_out), .out_5(out_61), .out_6(out_63), .in_1(in_3), .in_4(in_13));
  \D_триггер  \d_триггер_4  (
    .in_2(in_25), .in_3(\детектор_переднего_фронта_2_out_2 ), .out_5(out_68), .out_6(out_70), .in_1(in_20),
    .in_4(in_29));
  \Счётчик_4_бит  \u_счётчик_4_бит_1  (.Enable(in_36), .Clock(in_41), .in_3(in_45), .out_4(out_74));
  // Probe on in_38
  // Probe on in_48
  // Probe on in_54
  \Регистр_8_бит  \u_регистр_8_бит_1  (
    .Clock(in_21), .\Сброс (\Регистр_8_бит ), .Enable(in_23), .in_4(in_18), .out_5(out_66));
  // Probe on in_39
  \Улучшенный_счётчик_8_бит  \u_улучшенный_счётчик_8_бит_1  (
    .Clock(in_1), .\Счёт_вверх_вниз (in_4), .Enable(in_7), .\Сброс (in_10), .\Запись (in_15), .out_7(out_59),
    .in_6(in_11));
  _8_x_1_RAM u_8_x_1_ram_1 (
    .\Запись (in_30), .Input_Data(in_31), .out_7(out_71), .in_3(in_38), .Clock(in_32), .\Сброс (in_33),
    .in_4(in_39));
  // Probe on out_77
  _1024_x_8_RAM u_1024_x_8_ram_1 (
    .in_1(in_48), .in_2(in_49), .out_7(out_77), .in_3(in_54), .in_5(in_50), .in_6(in_51), .in_4(in_55));
  // Probe on in_55

  // Notes on the sheet:
  //   D триггер (верхний уровень)
  //   D триггер (передний фронт)
  //   Сумматор с памятью
  //   D триггер (нижний уровень)
  //   D триггер (задний фронт)
  //   Счетчик 4 бит
  //   Улучшенный счётчик 8 бит
  //   8 x 1 RAM
  //   1024 x 8 RAM
endmodule

module \SR_триггер  (
  input  in_1,
  input  in_2,
  input  in_3,
  output out_4,
  output out_5
);

  wire nand_1_out, nand_2_out;

  nand nand_1 (nand_1_out, in_1, in_2);
  nand nand_2 (nand_2_out, in_2, in_3);
  nand nand_3 (out_4, nand_1_out, out_5);
  nand nand_4 (out_5, out_4, nand_2_out);
endmodule

module \D_триггер  (
  input  in_1,
  input  in_2,
  input  in_3,
  input  in_4,
  output out_5,
  output out_6
);

  wire nand_1_out, nand_2_out;

  nand nand_1 (nand_1_out, in_2, in_3);
  nand nand_2 (nand_2_out, in_3, ~in_2);  // NAND_Gate
  nand nand_3 (out_5, ~in_1, nand_1_out, out_6);  // NAND_Gate
  nand nand_4 (out_6, out_5, nand_2_out, ~in_4);  // NAND_Gate
endmodule

module \Детектор_переднего_фронта  (
  input  in_1,
  output out_2
);

  wire not_1_out, not_2_out, not_3_out;

  not not_1 (not_1_out, in_1);
  not not_2 (not_2_out, not_1_out);
  not not_3 (not_3_out, not_2_out);
  and and_1 (out_2, not_3_out, in_1);
endmodule

module \T_триггер  (
  input  in_1,
  input  T,
  input  in_3,
  input  in_4,
  output out_5,
  output out_6
);

  wire xor_1_out, \детектор_переднего_фронта_1_out_2 ;

  xor xor_1 (xor_1_out, out_5, T);
  \Детектор_переднего_фронта  \u_детектор_переднего_фронта_1  (
    .in_1(in_3), .out_2(\детектор_переднего_фронта_1_out_2 ));
  \D_триггер  \d_триггер_1  (
    .in_2(xor_1_out), .in_3(\детектор_переднего_фронта_1_out_2 ), .out_5(out_5), .out_6(out_6), .in_1(in_1),
    .in_4(in_4));
endmodule

module \JK_триггер  (
  input  in_1,
  input  in_2,
  input  in_3,
  input  in_4,
  input  in_5,
  output out_6,
  output out_7
);

  wire and_1_out, and_2_out, not_1_out, or_1_out, \детектор_переднего_фронта_1_out_2 ;

  not not_1 (not_1_out, in_3);
  and and_1 (and_1_out, out_7, in_2);
  or or_1 (or_1_out, and_1_out, and_2_out);
  and and_2 (and_2_out, not_1_out, out_6);
  \Детектор_переднего_фронта  \u_детектор_переднего_фронта_1  (
    .in_1(in_4), .out_2(\детектор_переднего_фронта_1_out_2 ));
  \D_триггер  \d_триггер_1  (
    .in_2(or_1_out), .in_3(\детектор_переднего_фронта_1_out_2 ), .out_5(out_6), .out_6(out_7), .in_1(in_1),
    .in_4(in_5));
endmodule

module \Счётчик_4_бит  (
  input  Enable,
  input  Clock,
  input  in_3,
  output [3:0] out_4
);

  wire and_1_out, and_2_out, and_3_out;

  and and_1 (and_1_out, Enable, Clock);
  \T_триггер  \t_триггер_1  (.T(1'b1), .in_3(and_1_out), .out_5(out_4[0]), .in_1(1'b0), .in_4(in_3));  // open: out_6
  \T_триггер  \t_триггер_2  (
    .T(out_4[0]), .in_3(and_1_out), .out_5(out_4[1]), .in_1(1'b0), .in_4(in_3));  // open: out_6
  and and_2 (and_2_out, out_4[0], out_4[1]);
  \T_триггер  \t_триггер_3  (
    .T(and_2_out), .in_3(and_1_out), .out_5(out_4[2]), .in_1(1'b0), .in_4(in_3));  // open: out_6
  and and_3 (and_3_out, and_2_out, out_4[2]);
  \T_триггер  \t_триггер_4  (
    .T(and_3_out), .in_3(and_1_out), .out_5(out_4[3]), .in_1(1'b0), .in_4(in_3));  // open: out_6
endmodule

module \Улучшенный_счётчик_8_бит  (
  input  Clock,
  input  \Счёт_вверх_вниз ,
  input  Enable,
  input  \Сброс ,
  input  \Запись ,
  input  [7:0] in_6,
  output [7:0] out_7
);

  wire and_1_out, and_2_out, and_3_out, and_4_out, and_5_out, and_6_out, and_7_out, and_8_out, and_9_out,
       and_10_out, and_11_out, and_12_out, and_13_out, and_14_out, demultiplexer_1_out0,
       demultiplexer_1_out1, demultiplexer_2_out0, demultiplexer_2_out1, demultiplexer_3_out0,
       demultiplexer_3_out1, demultiplexer_4_out0, demultiplexer_4_out1, demultiplexer_5_out0,
       demultiplexer_5_out1, demultiplexer_6_out0, demultiplexer_6_out1, demultiplexer_7_out0,
       demultiplexer_7_out1, demultiplexer_8_out0, demultiplexer_8_out1, or_1_out, or_2_out, or_3_out,
       or_4_out, or_5_out, or_6_out, or_7_out, or_8_out, or_9_out, or_10_out, or_11_out, or_12_out,
       or_13_out, or_14_out, or_15_out, t_ff_1_qn, t_ff_2_qn, t_ff_3_qn, t_ff_4_qn, t_ff_5_qn, t_ff_6_qn,
       t_ff_7_qn;

  T_Flip_Flop t_ff_1 (
    .clk(Clock), .T(1'b1), .Q(out_7[0]), .Qn(t_ff_1_qn), .preset(demultiplexer_1_out1), .reset(or_1_out),
    .en(Enable));
  or or_1 (or_1_out, demultiplexer_1_out0, \Сброс );
  Demultiplexer #(.disabled(0)) demultiplexer_1 (
    .out0(demultiplexer_1_out0), .out1(demultiplexer_1_out1), .in(\Запись ), .sel(in_6[0]));  // open: en
  and and_1 (and_1_out, \Счёт_вверх_вниз , out_7[0]);
  and and_2 (and_2_out, t_ff_1_qn, ~\Счёт_вверх_вниз );  // AND_Gate
  T_Flip_Flop t_ff_2 (
    .clk(Clock), .T(or_2_out), .Q(out_7[1]), .Qn(t_ff_2_qn), .preset(demultiplexer_2_out1), .reset(or_3_out),
    .en(Enable));
  or or_2 (or_2_out, and_1_out, and_2_out);
  or or_3 (or_3_out, demultiplexer_2_out0, \Сброс );
  Demultiplexer #(.disabled(0)) demultiplexer_2 (
    .out0(demultiplexer_2_out0), .out1(demultiplexer_2_out1), .in(\Запись ), .sel(in_6[1]));  // open: en
  and and_3 (and_3_out, and_1_out, out_7[1]);
  and and_4 (and_4_out, t_ff_2_qn, and_2_out);
  T_Flip_Flop t_ff_3 (
    .clk(Clock), .T(or_4_out), .Q(out_7[2]), .Qn(t_ff_3_qn), .preset(demultiplexer_3_out1), .reset(or_5_out),
    .en(Enable));
  or or_4 (or_4_out, and_3_out, and_4_out);
  or or_5 (or_5_out, demultiplexer_3_out0, \Сброс );
  Demultiplexer #(.disabled(0)) demultiplexer_3 (
    .out0(demultiplexer_3_out0), .out1(demultiplexer_3_out1), .in(\Запись ), .sel(in_6[2]));  // open: en
  and and_5 (and_5_out, and_3_out, out_7[2]);
  and and_6 (and_6_out, t_ff_3_qn, and_4_out);
  T_Flip_Flop t_ff_4 (
    .clk(Clock), .T(or_6_out), .Q(out_7[3]), .Qn(t_ff_4_qn), .preset(demultiplexer_4_out1), .reset(or_7_out),
    .en(Enable));
  or or_6 (or_6_out, and_5_out, and_6_out);
  or or_7 (or_7_out, demultiplexer_4_out0, \Сброс );
  Demultiplexer #(.disabled(0)) demultiplexer_4 (
    .out0(demultiplexer_4_out0), .out1(demultiplexer_4_out1), .in(\Запись ), .sel(in_6[3]));  // open: en
  and and_7 (and_7_out, and_5_out, out_7[3]);
  and and_8 (and_8_out, t_ff_4_qn, and_6_out);
  T_Flip_Flop t_ff_5 (
    .clk(Clock), .T(or_8_out), .Q(out_7[4]), .Qn(t_ff_5_qn), .preset(demultiplexer_5_out1), .reset(or_9_out),
    .en(Enable));
  or or_8 (or_8_out, and_7_out, and_8_out);
  or or_9 (or_9_out, demultiplexer_5_out0, \Сброс );
  Demultiplexer #(.disabled(0)) demultiplexer_5 (
    .out0(demultiplexer_5_out0), .out1(demultiplexer_5_out1), .in(\Запись ), .sel(in_6[4]));  // open: en
  and and_9 (and_9_out, and_7_out, out_7[4]);
  and and_10 (and_10_out, t_ff_5_qn, and_8_out);
  T_Flip_Flop t_ff_6 (
    .clk(Clock), .T(or_10_out), .Q(out_7[5]), .Qn(t_ff_6_qn), .preset(demultiplexer_6_out1),
    .reset(or_11_out), .en(Enable));
  or or_10 (or_10_out, and_9_out, and_10_out);
  or or_11 (or_11_out, demultiplexer_6_out0, \Сброс );
  Demultiplexer #(.disabled(0)) demultiplexer_6 (
    .out0(demultiplexer_6_out0), .out1(demultiplexer_6_out1), .in(\Запись ), .sel(in_6[5]));  // open: en
  and and_11 (and_11_out, and_9_out, out_7[5]);
  and and_12 (and_12_out, t_ff_6_qn, and_10_out);
  T_Flip_Flop t_ff_7 (
    .clk(Clock), .T(or_12_out), .Q(out_7[6]), .Qn(t_ff_7_qn), .preset(demultiplexer_7_out1),
    .reset(or_13_out), .en(Enable));
  or or_12 (or_12_out, and_11_out, and_12_out);
  or or_13 (or_13_out, demultiplexer_7_out0, \Сброс );
  Demultiplexer #(.disabled(0)) demultiplexer_7 (
    .out0(demultiplexer_7_out0), .out1(demultiplexer_7_out1), .in(\Запись ), .sel(in_6[6]));  // open: en
  and and_13 (and_13_out, and_11_out, out_7[6]);
  and and_14 (and_14_out, t_ff_7_qn, and_12_out);
  T_Flip_Flop t_ff_8 (
    .clk(Clock), .T(or_14_out), .Q(out_7[7]), .preset(demultiplexer_8_out1), .reset(or_15_out), .en(Enable));  // open: Qn
  or or_14 (or_14_out, and_13_out, and_14_out);
  or or_15 (or_15_out, demultiplexer_8_out0, \Сброс );
  Demultiplexer #(.disabled(0)) demultiplexer_8 (
    .out0(demultiplexer_8_out0), .out1(demultiplexer_8_out1), .in(\Запись ), .sel(in_6[7]));  // open: en
endmodule

module \Регистр_8_бит  (
  input  Clock,
  input  \Сброс ,
  input  Enable,
  input  [7:0] in_4,
  output [7:0] out_5
);

  D_Flip_Flop d_ff_1 (.clk(Clock), .D(in_4[0]), .Q(out_5[0]), .en(Enable), .reset(\Сброс ));  // open: Qn, preset
  D_Flip_Flop d_ff_2 (.clk(Clock), .D(in_4[1]), .Q(out_5[1]), .en(Enable), .reset(\Сброс ));  // open: Qn, preset
  D_Flip_Flop d_ff_3 (.clk(Clock), .D(in_4[2]), .Q(out_5[2]), .en(Enable), .reset(\Сброс ));  // open: Qn, preset
  D_Flip_Flop d_ff_4 (.clk(Clock), .D(in_4[3]), .Q(out_5[3]), .en(Enable), .reset(\Сброс ));  // open: Qn, preset
  D_Flip_Flop d_ff_5 (.clk(Clock), .D(in_4[4]), .Q(out_5[4]), .en(Enable), .reset(\Сброс ));  // open: Qn, preset
  D_Flip_Flop d_ff_6 (.clk(Clock), .D(in_4[5]), .Q(out_5[5]), .en(Enable), .reset(\Сброс ));  // open: Qn, preset
  D_Flip_Flop d_ff_7 (.clk(Clock), .D(in_4[6]), .Q(out_5[6]), .en(Enable), .reset(\Сброс ));  // open: Qn, preset
  D_Flip_Flop d_ff_8 (.clk(Clock), .D(in_4[7]), .Q(out_5[7]), .en(Enable), .reset(\Сброс ));  // open: Qn, preset
endmodule

module \Сумматор_с_памятью  (
  input  in_1,
  input  in_2,
  input  in_3,
  input  in_4,
  input  [7:0] in_5,
  output [7:0] out_6,
  output out_7
);

  wire adder_1_cout;
  wire [7:0] adder_1_out, xor_1_out;

  // Probe on in_5
  assign xor_1_out = {8{in_1}} ^ in_5;  // XOR_Gate xor_1, 8 bits wide
  xor xor_2 (out_7, in_1, adder_1_cout);
  Adder adder_1 (.a(out_6), .b(xor_1_out), .out(adder_1_out), .cin(in_1), .cout(adder_1_cout));
  \Регистр_8_бит  \u_регистр_8_бит_1  (.Clock(in_2), .\Сброс (in_3), .Enable(in_4), .in_4(adder_1_out), .out_5(out_6));
  // Probe on out_6
endmodule

module _8_x_1_RAM (
  input  \Запись ,
  input  Input_Data,
  input  [2:0] in_3,
  input  [2:0] in_4,
  input  Clock,
  input  \Сброс ,
  output out_7
);

  wire d_ff_1_q, d_ff_2_q, d_ff_3_q, d_ff_4_q, d_ff_5_q, d_ff_6_q, d_ff_7_q, d_ff_8_q;
  wire [1:0] demultiplexer_1_out0, demultiplexer_1_out1, demultiplexer_1_out2, demultiplexer_1_out3,
       demultiplexer_1_out4, demultiplexer_1_out5, demultiplexer_1_out6, demultiplexer_1_out7;

  Demultiplexer #(.select(3), .width(2)) demultiplexer_1 (
    .out0(demultiplexer_1_out0), .out1(demultiplexer_1_out1), .out2(demultiplexer_1_out2),
    .out3(demultiplexer_1_out3), .out4(demultiplexer_1_out4), .out5(demultiplexer_1_out5),
    .out6(demultiplexer_1_out6), .out7(demultiplexer_1_out7), .in({Input_Data, \Запись }), .sel(in_3));  // open: en
  D_Flip_Flop d_ff_1 (
    .clk(Clock), .D(demultiplexer_1_out0[0]), .Q(d_ff_1_q), .en(demultiplexer_1_out0[1]), .reset(\Сброс ));  // open: Qn, preset
  D_Flip_Flop d_ff_2 (
    .clk(Clock), .D(demultiplexer_1_out1[0]), .Q(d_ff_2_q), .en(demultiplexer_1_out1[1]), .reset(\Сброс ));  // open: Qn, preset
  D_Flip_Flop d_ff_3 (
    .clk(Clock), .D(demultiplexer_1_out2[0]), .Q(d_ff_3_q), .en(demultiplexer_1_out2[1]), .reset(\Сброс ));  // open: Qn, preset
  D_Flip_Flop d_ff_4 (
    .clk(Clock), .D(demultiplexer_1_out3[0]), .Q(d_ff_4_q), .en(demultiplexer_1_out3[1]), .reset(\Сброс ));  // open: Qn, preset
  D_Flip_Flop d_ff_5 (
    .clk(Clock), .D(demultiplexer_1_out4[0]), .Q(d_ff_5_q), .en(demultiplexer_1_out4[1]), .reset(\Сброс ));  // open: Qn, preset
  D_Flip_Flop d_ff_6 (
    .clk(Clock), .D(demultiplexer_1_out5[0]), .Q(d_ff_6_q), .en(demultiplexer_1_out5[1]), .reset(\Сброс ));  // open: Qn, preset
  D_Flip_Flop d_ff_7 (
    .clk(Clock), .D(demultiplexer_1_out6[0]), .Q(d_ff_7_q), .en(demultiplexer_1_out6[1]), .reset(\Сброс ));  // open: Qn, preset
  D_Flip_Flop d_ff_8 (
    .clk(Clock), .D(demultiplexer_1_out7[0]), .Q(d_ff_8_q), .en(demultiplexer_1_out7[1]), .reset(\Сброс ));  // open: Qn, preset
  Multiplexer #(.select(3)) multiplexer_1 (
    .in0(d_ff_1_q), .in1(d_ff_2_q), .in2(d_ff_3_q), .in3(d_ff_4_q), .in4(d_ff_5_q), .in5(d_ff_6_q),
    .in6(d_ff_7_q), .in7(d_ff_8_q), .out(out_7), .sel(in_4));  // open: en
endmodule

module _8_x_8_RAM (
  input  [7:0] in_1,
  input  in_2,
  input  [2:0] in_3,
  input  [2:0] in_4,
  input  in_5,
  input  in_6,
  output [7:0] out_7
);

  wire [7:0] register_1_q, register_2_q, register_3_q, register_4_q, register_5_q, register_6_q,
       register_7_q, register_8_q;
  wire [8:0] demultiplexer_1_out0, demultiplexer_1_out1, demultiplexer_1_out2, demultiplexer_1_out3,
       demultiplexer_1_out4, demultiplexer_1_out5, demultiplexer_1_out6, demultiplexer_1_out7;

  Demultiplexer #(.select(3), .width(9)) demultiplexer_1 (
    .out0(demultiplexer_1_out0), .out1(demultiplexer_1_out1), .out2(demultiplexer_1_out2),
    .out3(demultiplexer_1_out3), .out4(demultiplexer_1_out4), .out5(demultiplexer_1_out5),
    .out6(demultiplexer_1_out6), .out7(demultiplexer_1_out7), .in({in_2, in_1}), .sel(in_4));  // open: en
  Register register_1 (
    .D(demultiplexer_1_out0[7:0]), .en(demultiplexer_1_out0[8]), .Q(register_1_q), .clk(in_5), .clr(in_6));
  Register register_2 (
    .D(demultiplexer_1_out1[7:0]), .en(demultiplexer_1_out1[8]), .Q(register_2_q), .clk(in_5), .clr(in_6));
  Register register_3 (
    .D(demultiplexer_1_out2[7:0]), .en(demultiplexer_1_out2[8]), .Q(register_3_q), .clk(in_5), .clr(in_6));
  Register register_4 (
    .D(demultiplexer_1_out3[7:0]), .en(demultiplexer_1_out3[8]), .Q(register_4_q), .clk(in_5), .clr(in_6));
  Register register_5 (
    .D(demultiplexer_1_out4[7:0]), .en(demultiplexer_1_out4[8]), .Q(register_5_q), .clk(in_5), .clr(in_6));
  Register register_6 (
    .D(demultiplexer_1_out5[7:0]), .en(demultiplexer_1_out5[8]), .Q(register_6_q), .clk(in_5), .clr(in_6));
  Register register_7 (
    .D(demultiplexer_1_out6[7:0]), .en(demultiplexer_1_out6[8]), .Q(register_7_q), .clk(in_5), .clr(in_6));
  Register register_8 (
    .D(demultiplexer_1_out7[7:0]), .en(demultiplexer_1_out7[8]), .Q(register_8_q), .clk(in_5), .clr(in_6));
  Multiplexer #(.select(3), .width(8)) multiplexer_1 (
    .in0(register_1_q), .in1(register_2_q), .in2(register_3_q), .in3(register_4_q), .in4(register_5_q),
    .in5(register_6_q), .in6(register_7_q), .in7(register_8_q), .out(out_7), .sel(in_3));  // open: en
endmodule

module _64_x_8_RAM (
  input  [7:0] in_1,
  input  in_2,
  input  [5:0] in_3,
  input  [5:0] in_4,
  input  in_5,
  input  in_6,
  output [7:0] out_7
);

  wire [7:0] n8_x_8_ram_1_out_7, n8_x_8_ram_2_out_7, n8_x_8_ram_3_out_7, n8_x_8_ram_4_out_7,
       n8_x_8_ram_5_out_7, n8_x_8_ram_6_out_7, n8_x_8_ram_7_out_7, n8_x_8_ram_8_out_7;
  wire [8:0] demultiplexer_1_out0, demultiplexer_1_out1, demultiplexer_1_out2, demultiplexer_1_out3,
       demultiplexer_1_out4, demultiplexer_1_out5, demultiplexer_1_out6, demultiplexer_1_out7;

  Demultiplexer #(.select(3), .width(9)) demultiplexer_1 (
    .out0(demultiplexer_1_out0), .out1(demultiplexer_1_out1), .out2(demultiplexer_1_out2),
    .out3(demultiplexer_1_out3), .out4(demultiplexer_1_out4), .out5(demultiplexer_1_out5),
    .out6(demultiplexer_1_out6), .out7(demultiplexer_1_out7), .in({in_2, in_1}), .sel(in_4[5:3]));  // open: en
  _8_x_8_RAM u_8_x_8_ram_1 (
    .in_1(demultiplexer_1_out0[7:0]), .in_2(demultiplexer_1_out0[8]), .out_7(n8_x_8_ram_1_out_7),
    .in_4(in_4[2:0]), .in_5(in_5), .in_6(in_6), .in_3(in_3[2:0]));
  _8_x_8_RAM u_8_x_8_ram_2 (
    .in_1(demultiplexer_1_out1[7:0]), .in_2(demultiplexer_1_out1[8]), .out_7(n8_x_8_ram_2_out_7),
    .in_4(in_4[2:0]), .in_5(in_5), .in_6(in_6), .in_3(in_3[2:0]));
  _8_x_8_RAM u_8_x_8_ram_3 (
    .in_1(demultiplexer_1_out2[7:0]), .in_2(demultiplexer_1_out2[8]), .out_7(n8_x_8_ram_3_out_7),
    .in_4(in_4[2:0]), .in_5(in_5), .in_6(in_6), .in_3(in_3[2:0]));
  _8_x_8_RAM u_8_x_8_ram_4 (
    .in_1(demultiplexer_1_out3[7:0]), .in_2(demultiplexer_1_out3[8]), .out_7(n8_x_8_ram_4_out_7),
    .in_4(in_4[2:0]), .in_5(in_5), .in_6(in_6), .in_3(in_3[2:0]));
  _8_x_8_RAM u_8_x_8_ram_5 (
    .in_1(demultiplexer_1_out4[7:0]), .in_2(demultiplexer_1_out4[8]), .out_7(n8_x_8_ram_5_out_7),
    .in_4(in_4[2:0]), .in_5(in_5), .in_6(in_6), .in_3(in_3[2:0]));
  _8_x_8_RAM u_8_x_8_ram_6 (
    .in_1(demultiplexer_1_out5[7:0]), .in_2(demultiplexer_1_out5[8]), .out_7(n8_x_8_ram_6_out_7),
    .in_4(in_4[2:0]), .in_5(in_5), .in_6(in_6), .in_3(in_3[2:0]));
  _8_x_8_RAM u_8_x_8_ram_7 (
    .in_1(demultiplexer_1_out6[7:0]), .in_2(demultiplexer_1_out6[8]), .out_7(n8_x_8_ram_7_out_7),
    .in_4(in_4[2:0]), .in_5(in_5), .in_6(in_6), .in_3(in_3[2:0]));
  _8_x_8_RAM u_8_x_8_ram_8 (
    .in_1(demultiplexer_1_out7[7:0]), .in_2(demultiplexer_1_out7[8]), .out_7(n8_x_8_ram_8_out_7),
    .in_4(in_4[2:0]), .in_5(in_5), .in_6(in_6), .in_3(in_3[2:0]));
  Multiplexer #(.select(3), .width(8)) multiplexer_1 (
    .in0(n8_x_8_ram_1_out_7), .in1(n8_x_8_ram_2_out_7), .in2(n8_x_8_ram_3_out_7), .in3(n8_x_8_ram_4_out_7),
    .in4(n8_x_8_ram_5_out_7), .in5(n8_x_8_ram_6_out_7), .in6(n8_x_8_ram_7_out_7), .in7(n8_x_8_ram_8_out_7),
    .out(out_7), .sel(in_3[5:3]));  // open: en
endmodule

module _512_x_8_RAM (
  input  [7:0] in_1,
  input  in_2,
  input  [8:0] in_3,
  input  [8:0] in_4,
  input  in_5,
  input  in_6,
  output [7:0] out_7
);

  wire [7:0] n64_x_8_ram_1_out_7, n64_x_8_ram_2_out_7, n64_x_8_ram_3_out_7, n64_x_8_ram_4_out_7,
       n64_x_8_ram_5_out_7, n64_x_8_ram_6_out_7, n64_x_8_ram_7_out_7, n64_x_8_ram_8_out_7;
  wire [8:0] demultiplexer_1_out0, demultiplexer_1_out1, demultiplexer_1_out2, demultiplexer_1_out3,
       demultiplexer_1_out4, demultiplexer_1_out5, demultiplexer_1_out6, demultiplexer_1_out7;

  Demultiplexer #(.select(3), .width(9)) demultiplexer_1 (
    .out0(demultiplexer_1_out0), .out1(demultiplexer_1_out1), .out2(demultiplexer_1_out2),
    .out3(demultiplexer_1_out3), .out4(demultiplexer_1_out4), .out5(demultiplexer_1_out5),
    .out6(demultiplexer_1_out6), .out7(demultiplexer_1_out7), .in({in_2, in_1}), .sel(in_4[8:6]));  // open: en
  _64_x_8_RAM u_64_x_8_ram_1 (
    .in_1(demultiplexer_1_out0[7:0]), .in_2(demultiplexer_1_out0[8]), .out_7(n64_x_8_ram_1_out_7),
    .in_4(in_4[5:0]), .in_5(in_5), .in_6(in_6), .in_3(in_3[5:0]));
  _64_x_8_RAM u_64_x_8_ram_2 (
    .in_1(demultiplexer_1_out1[7:0]), .in_2(demultiplexer_1_out1[8]), .out_7(n64_x_8_ram_2_out_7),
    .in_4(in_4[5:0]), .in_5(in_5), .in_6(in_6), .in_3(in_3[5:0]));
  _64_x_8_RAM u_64_x_8_ram_3 (
    .in_1(demultiplexer_1_out2[7:0]), .in_2(demultiplexer_1_out2[8]), .out_7(n64_x_8_ram_3_out_7),
    .in_4(in_4[5:0]), .in_5(in_5), .in_6(in_6), .in_3(in_3[5:0]));
  _64_x_8_RAM u_64_x_8_ram_4 (
    .in_1(demultiplexer_1_out3[7:0]), .in_2(demultiplexer_1_out3[8]), .out_7(n64_x_8_ram_4_out_7),
    .in_4(in_4[5:0]), .in_5(in_5), .in_6(in_6), .in_3(in_3[5:0]));
  _64_x_8_RAM u_64_x_8_ram_5 (
    .in_1(demultiplexer_1_out4[7:0]), .in_2(demultiplexer_1_out4[8]), .out_7(n64_x_8_ram_5_out_7),
    .in_4(in_4[5:0]), .in_5(in_5), .in_6(in_6), .in_3(in_3[5:0]));
  _64_x_8_RAM u_64_x_8_ram_6 (
    .in_1(demultiplexer_1_out5[7:0]), .in_2(demultiplexer_1_out5[8]), .out_7(n64_x_8_ram_6_out_7),
    .in_4(in_4[5:0]), .in_5(in_5), .in_6(in_6), .in_3(in_3[5:0]));
  _64_x_8_RAM u_64_x_8_ram_7 (
    .in_1(demultiplexer_1_out6[7:0]), .in_2(demultiplexer_1_out6[8]), .out_7(n64_x_8_ram_7_out_7),
    .in_4(in_4[5:0]), .in_5(in_5), .in_6(in_6), .in_3(in_3[5:0]));
  _64_x_8_RAM u_64_x_8_ram_8 (
    .in_1(demultiplexer_1_out7[7:0]), .in_2(demultiplexer_1_out7[8]), .out_7(n64_x_8_ram_8_out_7),
    .in_4(in_4[5:0]), .in_5(in_5), .in_6(in_6), .in_3(in_3[5:0]));
  Multiplexer #(.select(3), .width(8)) multiplexer_1 (
    .in0(n64_x_8_ram_1_out_7), .in1(n64_x_8_ram_2_out_7), .in2(n64_x_8_ram_3_out_7),
    .in3(n64_x_8_ram_4_out_7), .in4(n64_x_8_ram_5_out_7), .in5(n64_x_8_ram_6_out_7),
    .in6(n64_x_8_ram_7_out_7), .in7(n64_x_8_ram_8_out_7), .out(out_7), .sel(in_3[8:6]));  // open: en
endmodule

module _1024_x_8_RAM (
  input  [7:0] in_1,
  input  in_2,
  input  [9:0] in_3,
  input  [9:0] in_4,
  input  in_5,
  input  in_6,
  output [7:0] out_7
);

  wire [7:0] n512_x_8_ram_1_out_7, n512_x_8_ram_2_out_7;
  wire [8:0] demultiplexer_1_out0, demultiplexer_1_out1;

  Demultiplexer #(.width(9)) demultiplexer_1 (
    .out0(demultiplexer_1_out0), .out1(demultiplexer_1_out1), .in({in_2, in_1}), .sel(in_3[9]));  // open: en
  _512_x_8_RAM u_512_x_8_ram_1 (
    .in_1(demultiplexer_1_out0[7:0]), .in_2(demultiplexer_1_out0[8]), .out_7(n512_x_8_ram_1_out_7),
    .in_4(in_3[8:0]), .in_5(in_5), .in_6(in_6), .in_3(in_4[8:0]));
  _512_x_8_RAM u_512_x_8_ram_2 (
    .in_1(demultiplexer_1_out1[7:0]), .in_2(demultiplexer_1_out1[8]), .out_7(n512_x_8_ram_2_out_7),
    .in_4(in_3[8:0]), .in_5(in_5), .in_6(in_6), .in_3(in_4[8:0]));
  Multiplexer #(.width(8)) multiplexer_1 (
    .in0(n512_x_8_ram_1_out_7), .in1(n512_x_8_ram_2_out_7), .out(out_7), .sel(in_4[9]));  // open: en
endmodule
