// Logisim project Timer.circ as structural Verilog: 24 circuits, main circuit Timer
module Timer (
  input  in_1,
  input  in_2,
  output out_3,
  output out_4,
  output out_5,
  output out_6,
  output out_7,
  output out_8
);

  wire _0_out, _1_out, _2_out, _3_out, _4_out, _5_out, _6_out, _7_out, _8_out, _9_out, button_2_out,
       button_out, clock_1_out, \перевод_в_10_ричную_1_out_12 ;
  wire [2:0] \выбор_1_out_3 ;
  wire [3:0] \перевод_в_10_ричную_1_out_11 , \часовой_механизм_1_out_7 , \часовой_механизм_1_out_8 ,
       \часовой_механизм_1_out_9 , \часовой_механизм_1_out_10 , \часовой_механизм_1_out_11 ,
       \часовой_механизм_1_out_12 ;
  wire [7:0] n10_7_1_out_2, n10_7_2_out_2, n10_7_3_out_2, n10_7_4_out_2, \n10_7_сег_1_out_2 ,
       \n10_7_сег_2_out_2 ;

  _7_Segment_Display u_7_segment_display_1 (
    .g(n10_7_1_out_2[3]), .f(n10_7_1_out_2[2]), .a(n10_7_1_out_2[1]), .b(n10_7_1_out_2[0]),
    .e(n10_7_1_out_2[7]), .d(n10_7_1_out_2[6]), .c(n10_7_1_out_2[5]), .dp(n10_7_1_out_2[4]));
  _10____7 u_10_7_1 (.in_1(\часовой_механизм_1_out_7 ), .out_2(n10_7_1_out_2));
  \_10____7_сег_2  \u_10_7_сег_1  (.in_1(\часовой_механизм_1_out_8 ), .out_2(\n10_7_сег_1_out_2 ));
  _7_Segment_Display u_7_segment_display_2 (
    .g(\n10_7_сег_1_out_2 [3]), .f(\n10_7_сег_1_out_2 [2]), .a(\n10_7_сег_1_out_2 [1]),
    .b(\n10_7_сег_1_out_2 [0]), .e(\n10_7_сег_1_out_2 [7]), .d(\n10_7_сег_1_out_2 [6]),
    .c(\n10_7_сег_1_out_2 [5]), .dp(\n10_7_сег_1_out_2 [4]));
  _10____7 u_10_7_2 (.in_1(\часовой_механизм_1_out_9 ), .out_2(n10_7_2_out_2));
  \Выбор  \u_выбор_1  (.in_1(button_out), .out_3(\выбор_1_out_3 ), .in_2(button_2_out));
  Button button (.out(button_out));
  Button button_2 (.out(button_2_out));
  Demultiplexer #(.select(3), .enable("false")) demultiplexer_1 (
    .out0(out_3), .out1(out_4), .out2(out_5), .out3(out_6), .out4(out_7), .out5(out_8), .in(1'b1),
    .sel(\выбор_1_out_3 ));  // open: out6, out7
  _7_Segment_Display u_7_segment_display_3 (
    .g(n10_7_2_out_2[3]), .f(n10_7_2_out_2[2]), .a(n10_7_2_out_2[1]), .b(n10_7_2_out_2[0]),
    .e(n10_7_2_out_2[7]), .d(n10_7_2_out_2[6]), .c(n10_7_2_out_2[5]), .dp(n10_7_2_out_2[4]));
  \_10____7_сег_2  \u_10_7_сег_2  (.in_1(\часовой_механизм_1_out_10 ), .out_2(\n10_7_сег_2_out_2 ));
  \Часовой_механизм  \u_часовой_механизм_1  (
    .in_1(in_1), .in_2(in_2), .out_7(\часовой_механизм_1_out_7 ), .out_8(\часовой_механизм_1_out_8 ),
    .out_9(\часовой_механизм_1_out_9 ), .out_10(\часовой_механизм_1_out_10 ),
    .out_11(\часовой_механизм_1_out_11 ), .out_12(\часовой_механизм_1_out_12 ),
    .in_5(\перевод_в_10_ричную_1_out_11 ), .in_4(\выбор_1_out_3 ), .in_3(clock_1_out),
    .in_6(\перевод_в_10_ричную_1_out_12 ));
  Clock clock_1 (.out(clock_1_out));
  _7_Segment_Display u_7_segment_display_4 (
    .g(\n10_7_сег_2_out_2 [3]), .f(\n10_7_сег_2_out_2 [2]), .a(\n10_7_сег_2_out_2 [1]),
    .b(\n10_7_сег_2_out_2 [0]), .e(\n10_7_сег_2_out_2 [7]), .d(\n10_7_сег_2_out_2 [6]),
    .c(\n10_7_сег_2_out_2 [5]), .dp(\n10_7_сег_2_out_2 [4]));
  _10____7 u_10_7_3 (.in_1(\часовой_механизм_1_out_11 ), .out_2(n10_7_3_out_2));
  _7_Segment_Display u_7_segment_display_5 (
    .g(n10_7_3_out_2[3]), .f(n10_7_3_out_2[2]), .a(n10_7_3_out_2[1]), .b(n10_7_3_out_2[0]),
    .e(n10_7_3_out_2[7]), .d(n10_7_3_out_2[6]), .c(n10_7_3_out_2[5]), .dp(n10_7_3_out_2[4]));
  _10____7 u_10_7_4 (.in_1(\часовой_механизм_1_out_12 ), .out_2(n10_7_4_out_2));
  _7_Segment_Display u_7_segment_display_6 (
    .g(n10_7_4_out_2[3]), .f(n10_7_4_out_2[2]), .a(n10_7_4_out_2[1]), .b(n10_7_4_out_2[0]),
    .e(n10_7_4_out_2[7]), .d(n10_7_4_out_2[6]), .c(n10_7_4_out_2[5]), .dp(n10_7_4_out_2[4]));
  Button _1 (.out(_1_out));
  Button _2 (.out(_2_out));
  Button _4 (.out(_4_out));
  Button _5 (.out(_5_out));
  Button _8 (.out(_8_out));
  Button _7 (.out(_7_out));
  Button _0 (.out(_0_out));
  Button _3 (.out(_3_out));
  Button _6 (.out(_6_out));
  Button _9 (.out(_9_out));
  \Перевод_в_10_ричную  \u_перевод_в_10_ричную_1  (
    ._0(_0_out), ._1(_1_out), ._2(_2_out), ._3(_3_out), ._4(_4_out), ._5(_5_out), ._6(_6_out), ._7(_7_out),
    ._8(_8_out), ._9(_9_out), .out_11(\перевод_в_10_ричную_1_out_11 ), .out_12(\перевод_в_10_ричную_1_out_12 ));
endmodule

module \Улучшенный_счетчик_3_бит  (
  input  \Счет_вверх_вниз ,
  input  Clock,
  input  Enable,
  input  \Сброс ,
  input  \Запись ,
  input  [2:0] in_6,
  output [2:0] out_7
);

  wire and_1_out, and_2_out, and_3_out, and_4_out, demultiplexer_1_out0, demultiplexer_1_out1,
       demultiplexer_2_out0, demultiplexer_2_out1, demultiplexer_3_out0, demultiplexer_3_out1, or_1_out,
       or_2_out, or_3_out, or_4_out, or_5_out, t_ff_1_qn, t_ff_2_qn;

  Demultiplexer #(.enable("false")) demultiplexer_1 (
    .out0(demultiplexer_1_out0), .out1(demultiplexer_1_out1), .in(\Запись ), .sel(in_6[0]));
  and and_1 (and_1_out, \Счет_вверх_вниз , out_7[0]);
  T_Flip_Flop t_ff_1 (
    .clk(Clock), .T(1'b1), .Q(out_7[0]), .Qn(t_ff_1_qn), .preset(demultiplexer_1_out1), .reset(or_1_out),
    .en(Enable));
  and and_2 (and_2_out, t_ff_1_qn, ~\Счет_вверх_вниз );  // AND_Gate
  or or_1 (or_1_out, demultiplexer_1_out0, \Сброс );
  or or_2 (or_2_out, and_1_out, and_2_out);
  Demultiplexer #(.enable("false")) demultiplexer_2 (
    .out0(demultiplexer_2_out0), .out1(demultiplexer_2_out1), .in(\Запись ), .sel(in_6[1]));
  and and_3 (and_3_out, and_1_out, out_7[1]);
  T_Flip_Flop t_ff_2 (
    .clk(Clock), .T(or_2_out), .Q(out_7[1]), .Qn(t_ff_2_qn), .preset(demultiplexer_2_out1), .reset(or_3_out),
    .en(Enable));
  and and_4 (and_4_out, t_ff_2_qn, and_2_out);
  or or_3 (or_3_out, demultiplexer_2_out0, \Сброс );
  or or_4 (or_4_out, and_3_out, and_4_out);
  Demultiplexer #(.enable("false")) demultiplexer_3 (
    .out0(demultiplexer_3_out0), .out1(demultiplexer_3_out1), .in(\Запись ), .sel(in_6[2]));
  T_Flip_Flop t_ff_3 (
    .clk(Clock), .T(or_4_out), .Q(out_7[2]), .preset(demultiplexer_3_out1), .reset(or_5_out), .en(Enable));  // open: Qn
  or or_5 (or_5_out, demultiplexer_3_out0, \Сброс );
endmodule

module \Улучшенный_счетчик_4_бит  (
  input  \Счет_вверх_вниз ,
  input  Clock,
  input  Enable,
  input  \Сброс ,
  input  \Запись ,
  input  [3:0] in_6,
  output [3:0] out_7
);

  wire and_1_out, and_2_out, and_3_out, and_4_out, and_5_out, and_6_out, demultiplexer_1_out0,
       demultiplexer_1_out1, demultiplexer_2_out0, demultiplexer_2_out1, demultiplexer_3_out0,
       demultiplexer_3_out1, demultiplexer_4_out0, demultiplexer_4_out1, or_1_out, or_2_out, or_3_out,
       or_4_out, or_5_out, or_6_out, or_7_out, t_ff_1_qn, t_ff_2_qn, t_ff_3_qn;

  Demultiplexer #(.enable("false")) demultiplexer_1 (
    .out0(demultiplexer_1_out0), .out1(demultiplexer_1_out1), .in(\Запись ), .sel(in_6[0]));
  and and_1 (and_1_out, \Счет_вверх_вниз , out_7[0]);
  T_Flip_Flop t_ff_1 (
    .clk(Clock), .T(1'b1), .Q(out_7[0]), .Qn(t_ff_1_qn), .preset(demultiplexer_1_out1), .reset(or_1_out),
    .en(Enable));
  and and_2 (and_2_out, t_ff_1_qn, ~\Счет_вверх_вниз );  // AND_Gate
  or or_1 (or_1_out, demultiplexer_1_out0, \Сброс );
  or or_2 (or_2_out, and_1_out, and_2_out);
  Demultiplexer #(.enable("false")) demultiplexer_2 (
    .out0(demultiplexer_2_out0), .out1(demultiplexer_2_out1), .in(\Запись ), .sel(in_6[1]));
  and and_3 (and_3_out, and_1_out, out_7[1]);
  T_Flip_Flop t_ff_2 (
    .clk(Clock), .T(or_2_out), .Q(out_7[1]), .Qn(t_ff_2_qn), .preset(demultiplexer_2_out1), .reset(or_3_out),
    .en(Enable));
  and and_4 (and_4_out, t_ff_2_qn, and_2_out);
  or or_3 (or_3_out, demultiplexer_2_out0, \Сброс );
  or or_4 (or_4_out, and_3_out, and_4_out);
  Demultiplexer #(.enable("false")) demultiplexer_3 (
    .out0(demultiplexer_3_out0), .out1(demultiplexer_3_out1), .in(\Запись ), .sel(in_6[2]));
  T_Flip_Flop t_ff_3 (
    .clk(Clock), .T(or_4_out), .Q(out_7[2]), .Qn(t_ff_3_qn), .preset(demultiplexer_3_out1), .reset(or_5_out),
    .en(Enable));
  or or_5 (or_5_out, demultiplexer_3_out0, \Сброс );
  and and_5 (and_5_out, and_3_out, out_7[2]);
  or or_6 (or_6_out, and_5_out, and_6_out);
  and and_6 (and_6_out, t_ff_3_qn, and_4_out);
  T_Flip_Flop t_ff_4 (
    .clk(Clock), .T(or_6_out), .Q(out_7[3]), .preset(demultiplexer_4_out1), .reset(or_7_out), .en(Enable));  // open: Qn
  or or_7 (or_7_out, demultiplexer_4_out0, \Сброс );
  Demultiplexer #(.enable("false")) demultiplexer_4 (
    .out0(demultiplexer_4_out0), .out1(demultiplexer_4_out1), .in(\Запись ), .sel(in_6[3]));
endmodule

module \Сравнение_границы_3_бит  (
  input  [2:0] in_1,
  input  [2:0] in_2,
  output out_3
);

  wire not_1_out, not_2_out, not_3_out, xor_1_out, xor_2_out, xor_3_out;

  xor xor_1 (xor_1_out, in_1[0], in_2[0]);
  not not_1 (not_1_out, xor_1_out);
  not not_2 (not_2_out, xor_2_out);
  xor xor_2 (xor_2_out, in_1[1], in_2[1]);
  not not_3 (not_3_out, xor_3_out);
  xor xor_3 (xor_3_out, in_1[2], in_2[2]);
  and and_1 (out_3, not_1_out, not_2_out, not_3_out);
endmodule

module \Сравнение_границы_4_бит  (
  input  [3:0] in_1,
  input  [3:0] in_2,
  output out_3
);

  wire not_1_out, not_2_out, not_3_out, not_4_out, xor_1_out, xor_2_out, xor_3_out, xor_4_out;

  xor xor_1 (xor_1_out, in_1[0], in_2[0]);
  not not_1 (not_1_out, xor_1_out);
  xor xor_2 (xor_2_out, in_1[1], in_2[1]);
  not not_2 (not_2_out, xor_2_out);
  xor xor_3 (xor_3_out, in_1[2], in_2[2]);
  not not_3 (not_3_out, xor_3_out);
  xor xor_4 (xor_4_out, in_1[3], in_2[3]);
  not not_4 (not_4_out, xor_4_out);
  and and_1 (out_3, not_1_out, not_2_out, not_3_out, not_4_out);
endmodule

module \Сравнение_1_бит  (
  input  in_1,
  input  in_2,
  output out_3
);

  and and_1 (out_3, ~in_1, in_2);  // AND_Gate
endmodule

module \Сравнение_с_приоритетом  (
  input  in_1,
  input  in_2,
  input  in_3,
  output out_4,
  output out_5
);

  wire not_1_out, xnor_1_out, \сравнение_1_бит_1_out_3 ;

  \Сравнение_1_бит  \u_сравнение_1_бит_1  (.in_1(in_1), .in_2(in_2), .out_3(\сравнение_1_бит_1_out_3 ));
  xnor xnor_1 (xnor_1_out, in_1, in_2);
  not not_1 (not_1_out, xnor_1_out);
  or or_1 (out_4, not_1_out, in_3);
  or or_2 (out_5, \сравнение_1_бит_1_out_3 , xnor_1_out, in_3);
endmodule

module \Сравнение_с_приоритетом_2_0  (
  input  [3:0] A,
  input  [3:0] B,
  output out_3
);

  wire \сравнение_с_приоритетом_1_out_4 , \сравнение_с_приоритетом_1_out_5 ,
       \сравнение_с_приоритетом_2_out_4 , \сравнение_с_приоритетом_2_out_5 ,
       \сравнение_с_приоритетом_3_out_4 , \сравнение_с_приоритетом_3_out_5 ,
       \сравнение_с_приоритетом_4_out_5 ;

  \Сравнение_с_приоритетом  \u_сравнение_с_приоритетом_1  (
    .in_1(A[3]), .in_2(B[3]), .in_3(1'b0), .out_5(\сравнение_с_приоритетом_1_out_5 ),
    .out_4(\сравнение_с_приоритетом_1_out_4 ));
  \Сравнение_с_приоритетом  \u_сравнение_с_приоритетом_2  (
    .in_1(A[2]), .in_2(B[2]), .in_3(\сравнение_с_приоритетом_1_out_4 ),
    .out_5(\сравнение_с_приоритетом_2_out_5 ), .out_4(\сравнение_с_приоритетом_2_out_4 ));
  \Сравнение_с_приоритетом  \u_сравнение_с_приоритетом_3  (
    .in_1(A[1]), .in_2(B[1]), .in_3(\сравнение_с_приоритетом_2_out_4 ),
    .out_5(\сравнение_с_приоритетом_3_out_5 ), .out_4(\сравнение_с_приоритетом_3_out_4 ));
  \Сравнение_с_приоритетом  \u_сравнение_с_приоритетом_4  (
    .in_1(A[0]), .in_2(B[0]), .in_3(\сравнение_с_приоритетом_3_out_4 ),
    .out_5(\сравнение_с_приоритетом_4_out_5 ));  // open: out_4
  and and_1 (out_3, \сравнение_с_приоритетом_1_out_5 , \сравнение_с_приоритетом_2_out_5 , \сравнение_с_приоритетом_3_out_5 , \сравнение_с_приоритетом_4_out_5 );
endmodule

module \Ограничитель_0_9  (
  input  in_1,
  input  in_2,
  input  in_3,
  input  in_4,
  input  [3:0] in_5,
  output [3:0] out_6
);

  wire and_1_out, or_1_out, \сравнение_границы_4_бит_1_out_3 ;
  wire [3:0] multiplexer_1_out;

  and and_1 (and_1_out, in_1, \сравнение_границы_4_бит_1_out_3 );
  or or_1 (or_1_out, and_1_out, in_4);
  \Улучшенный_счетчик_4_бит  \u_улучшенный_счетчик_4_бит_1  (
    .\Счет_вверх_вниз (1'b0), .Clock(in_1), .Enable(in_2), .\Сброс (in_3), .\Запись (or_1_out),
    .out_7(out_6), .in_6(multiplexer_1_out));
  Multiplexer #(.width(4), .enable("false")) multiplexer_1 (
    .in0(4'b1001), .in1(in_5), .out(multiplexer_1_out), .sel(in_4));
  \Сравнение_границы_4_бит  \u_сравнение_границы_4_бит_1  (
    .in_1(out_6), .in_2(4'b1111), .out_3(\сравнение_границы_4_бит_1_out_3 ));
endmodule

module \Ограничитель_0_5  (
  input  in_1,
  input  in_2,
  input  in_3,
  input  in_4,
  input  [3:0] in_5,
  output [3:0] out_6
);

  wire and_1_out, or_1_out, \сравнение_границы_4_бит_1_out_3 ;
  wire [3:0] multiplexer_1_out;

  and and_1 (and_1_out, in_1, \сравнение_границы_4_бит_1_out_3 );
  or or_1 (or_1_out, and_1_out, in_4);
  \Улучшенный_счетчик_4_бит  \u_улучшенный_счетчик_4_бит_1  (
    .\Счет_вверх_вниз (1'b0), .Clock(in_1), .Enable(in_2), .\Сброс (in_3), .\Запись (or_1_out),
    .out_7(out_6), .in_6(multiplexer_1_out));
  Multiplexer #(.width(4), .enable("false")) multiplexer_1 (
    .in0(4'b0101), .in1(in_5), .out(multiplexer_1_out), .sel(in_4));
  \Сравнение_границы_4_бит  \u_сравнение_границы_4_бит_1  (
    .in_1(out_6), .in_2(4'b1111), .out_3(\сравнение_границы_4_бит_1_out_3 ));
endmodule

module \Ограничитель_0_5_2_0  (
  input  in_1,
  input  in_2,
  input  in_3,
  input  in_4,
  input  [3:0] in_5,
  output [3:0] out_6
);

  wire and_1_out, not_1_out, or_1_out, \сравнение_границы_4_бит_1_out_3 ,
       \сравнение_с_приоритетом_2_0_1_out_3 ;
  wire [3:0] multiplexer_1_out, multiplexer_2_out;

  and and_1 (and_1_out, in_1, \сравнение_границы_4_бит_1_out_3 );
  or or_1 (or_1_out, and_1_out, in_4);
  \Сравнение_с_приоритетом_2_0  \u_сравнение_с_приоритетом_2_0_1  (
    .A(in_5), .B(4'b0101), .out_3(\сравнение_с_приоритетом_2_0_1_out_3 ));
  \Улучшенный_счетчик_4_бит  \u_улучшенный_счетчик_4_бит_1  (
    .\Счет_вверх_вниз (1'b0), .Clock(in_1), .Enable(in_2), .\Сброс (in_3), .\Запись (or_1_out),
    .out_7(out_6), .in_6(multiplexer_1_out));
  Multiplexer #(.width(4), .enable("false")) multiplexer_1 (
    .in0(4'b0101), .in1(multiplexer_2_out), .out(multiplexer_1_out), .sel(in_4));
  Multiplexer #(.width(4), .disabled(0), .enable("false")) multiplexer_2 (
    .in0(in_5), .in1(4'b0101), .out(multiplexer_2_out), .sel(not_1_out));
  not not_1 (not_1_out, \сравнение_с_приоритетом_2_0_1_out_3 );
  \Сравнение_границы_4_бит  \u_сравнение_границы_4_бит_1  (
    .in_1(out_6), .in_2(4'b1111), .out_3(\сравнение_границы_4_бит_1_out_3 ));
endmodule

module \Часовой_механизм  (
  input  in_1,
  input  in_2,
  input  in_3,
  input  [2:0] in_4,
  input  [3:0] in_5,
  input  in_6,
  output [3:0] out_7,
  output [3:0] out_8,
  output [3:0] out_9,
  output [3:0] out_10,
  output [3:0] out_11,
  output [3:0] out_12
);

  wire demultiplexer_2_out0, demultiplexer_2_out1, demultiplexer_2_out2, demultiplexer_2_out3,
       demultiplexer_2_out4, demultiplexer_2_out5, \сравнение_границы_4_бит_1_out_3 ,
       \сравнение_границы_4_бит_2_out_3 , \сравнение_границы_4_бит_3_out_3 ,
       \сравнение_границы_4_бит_4_out_3 , \сравнение_границы_4_бит_5_out_3 ;
  wire [3:0] demultiplexer_1_out0, demultiplexer_1_out1, demultiplexer_1_out2, demultiplexer_1_out3,
       demultiplexer_1_out4, demultiplexer_1_out5;

  // Probe on out_7
  \Ограничитель_0_9  \u_ограничитель_0_9_1  (
    .in_1(\сравнение_границы_4_бит_1_out_3 ), .in_2(in_1), .in_3(in_2), .out_6(out_7),
    .in_5(demultiplexer_1_out0), .in_4(demultiplexer_2_out0));
  \Сравнение_границы_4_бит  \u_сравнение_границы_4_бит_1  (
    .in_1(out_8), .in_2(4'b1001), .out_3(\сравнение_границы_4_бит_1_out_3 ));
  // Probe on out_8
  \Ограничитель_0_9  \u_ограничитель_0_9_2  (
    .in_1(\сравнение_границы_4_бит_2_out_3 ), .in_2(in_1), .in_3(in_2), .out_6(out_8),
    .in_5(demultiplexer_1_out1), .in_4(demultiplexer_2_out1));
  \Сравнение_границы_4_бит  \u_сравнение_границы_4_бит_2  (
    .in_1(out_9), .in_2(4'b0101), .out_3(\сравнение_границы_4_бит_2_out_3 ));
  // Probe on out_9
  \Ограничитель_0_5_2_0  \u_ограничитель_0_5_2_0_1  (
    .in_1(\сравнение_границы_4_бит_3_out_3 ), .in_2(in_1), .in_3(in_2), .out_6(out_9),
    .in_4(demultiplexer_2_out2), .in_5(demultiplexer_1_out2));
  \Сравнение_границы_4_бит  \u_сравнение_границы_4_бит_3  (
    .in_1(out_10), .in_2(4'b1001), .out_3(\сравнение_границы_4_бит_3_out_3 ));
  Demultiplexer #(.select(3), .width(4), .enable("false")) demultiplexer_1 (
    .out0(demultiplexer_1_out0), .out1(demultiplexer_1_out1), .out2(demultiplexer_1_out2),
    .out3(demultiplexer_1_out3), .out4(demultiplexer_1_out4), .out5(demultiplexer_1_out5), .in(in_5),
    .sel(in_4));  // open: out6, out7
  // Probe on out_10
  \Ограничитель_0_9  \u_ограничитель_0_9_3  (
    .in_1(\сравнение_границы_4_бит_4_out_3 ), .in_2(in_1), .in_3(in_2), .out_6(out_10),
    .in_5(demultiplexer_1_out3), .in_4(demultiplexer_2_out3));
  \Сравнение_границы_4_бит  \u_сравнение_границы_4_бит_4  (
    .in_1(out_11), .in_2(4'b0101), .out_3(\сравнение_границы_4_бит_4_out_3 ));
  Demultiplexer #(.select(3), .enable("false")) demultiplexer_2 (
    .out0(demultiplexer_2_out0), .out1(demultiplexer_2_out1), .out2(demultiplexer_2_out2),
    .out3(demultiplexer_2_out3), .out4(demultiplexer_2_out4), .out5(demultiplexer_2_out5), .in(in_6),
    .sel(in_4));  // open: out6, out7
  // Probe on out_11
  \Ограничитель_0_5_2_0  \u_ограничитель_0_5_2_0_2  (
    .in_1(\сравнение_границы_4_бит_5_out_3 ), .in_2(in_1), .in_3(in_2), .out_6(out_11),
    .in_4(demultiplexer_2_out4), .in_5(demultiplexer_1_out4));
  \Сравнение_границы_4_бит  \u_сравнение_границы_4_бит_5  (
    .in_1(out_12), .in_2(4'b1001), .out_3(\сравнение_границы_4_бит_5_out_3 ));
  // Probe on out_12
  \Ограничитель_0_9  \u_ограничитель_0_9_4  (
    .in_1(in_3), .in_2(in_1), .in_3(in_2), .out_6(out_12), .in_5(demultiplexer_1_out5),
    .in_4(demultiplexer_2_out5));
endmodule

module \Перевод_в_10_ричную  (
  input  _0,
  input  _1,
  input  _2,
  input  _3,
  input  _4,
  input  _5,
  input  _6,
  input  _7,
  input  _8,
  input  _9,
  output [3:0] out_11,
  output out_12
);

  or or_1 (out_12, _0, _1, _2, _3, _4, _6, _7, _8, _9, _5);
  \Бит_0  \u_бит_0_1  (.in_1({_9, _8, _7, _6, _5, _4, _3, _2, _1, _0}), .out_2(out_11[0]));
  \Бит_1  \u_бит_1_1  (.in_1({_9, _8, _7, _6, _5, _4, _3, _2, _1, _0}), .out_2(out_11[1]));
  \Бит_2  \u_бит_2_1  (.in_1({_9, _8, _7, _6, _5, _4, _3, _2, _1, _0}), .out_2(out_11[2]));
  \Бит_3  \u_бит_3_1  (.in_1({_9, _8, _7, _6, _5, _4, _3, _2, _1, _0}), .out_2(out_11[3]));
  // Probe on out_11
endmodule

module \Бит_3  (
  input  [9:0] in_1,
  output out_2
);

  wire and_1_out, and_2_out;

  and and_1 (and_1_out, ~in_1[0], ~in_1[1], ~in_1[2], ~in_1[3], ~in_1[4], ~in_1[5], ~in_1[6], ~in_1[7], ~in_1[8], in_1[9]);  // AND_Gate
  and and_2 (and_2_out, ~in_1[0], ~in_1[1], ~in_1[2], ~in_1[3], ~in_1[4], ~in_1[5], ~in_1[6], ~in_1[7], in_1[8], ~in_1[9]);  // AND_Gate
  or or_1 (out_2, and_1_out, and_2_out);
endmodule

module \Бит_2  (
  input  [9:0] in_1,
  output out_2
);

  wire and_1_out, and_2_out, and_3_out, and_4_out;

  and and_1 (and_1_out, ~in_1[0], ~in_1[1], ~in_1[2], ~in_1[3], ~in_1[4], ~in_1[5], ~in_1[6], in_1[7], ~in_1[8], ~in_1[9]);  // AND_Gate
  and and_2 (and_2_out, ~in_1[0], ~in_1[1], ~in_1[2], ~in_1[3], ~in_1[4], ~in_1[5], in_1[6], ~in_1[7], ~in_1[8], ~in_1[9]);  // AND_Gate
  and and_3 (and_3_out, ~in_1[0], ~in_1[1], ~in_1[2], ~in_1[3], ~in_1[4], in_1[5], ~in_1[6], ~in_1[7], ~in_1[8], ~in_1[9]);  // AND_Gate
  and and_4 (and_4_out, ~in_1[0], ~in_1[1], ~in_1[2], ~in_1[3], in_1[4], ~in_1[5], ~in_1[6], ~in_1[7], ~in_1[8], ~in_1[9]);  // AND_Gate
  or or_1 (out_2, and_1_out, and_2_out, and_3_out, and_4_out);
endmodule

module \Бит_1  (
  input  [9:0] in_1,
  output out_2
);

  wire and_1_out, and_2_out, and_3_out, and_4_out;

  and and_1 (and_1_out, ~in_1[0], ~in_1[1], ~in_1[2], ~in_1[3], ~in_1[4], ~in_1[5], ~in_1[6], in_1[7], ~in_1[8], ~in_1[9]);  // AND_Gate
  and and_2 (and_2_out, ~in_1[0], ~in_1[1], ~in_1[2], ~in_1[3], ~in_1[4], ~in_1[5], in_1[6], ~in_1[7], ~in_1[8], ~in_1[9]);  // AND_Gate
  and and_3 (and_3_out, ~in_1[0], ~in_1[1], ~in_1[2], in_1[3], ~in_1[4], ~in_1[5], ~in_1[6], ~in_1[7], ~in_1[8], ~in_1[9]);  // AND_Gate
  and and_4 (and_4_out, ~in_1[0], ~in_1[1], in_1[2], ~in_1[3], ~in_1[4], ~in_1[5], ~in_1[6], ~in_1[7], ~in_1[8], ~in_1[9]);  // AND_Gate
  or or_1 (out_2, and_1_out, and_2_out, and_3_out, and_4_out);
endmodule

module \Бит_0  (
  input  [9:0] in_1,
  output out_2
);

  wire and_1_out, and_2_out, and_3_out, and_4_out, and_5_out;

  and and_1 (and_1_out, ~in_1[0], ~in_1[1], ~in_1[2], ~in_1[3], ~in_1[4], ~in_1[5], ~in_1[6], ~in_1[7], ~in_1[8], in_1[9]);  // AND_Gate
  and and_2 (and_2_out, ~in_1[0], ~in_1[1], ~in_1[2], ~in_1[3], ~in_1[4], ~in_1[5], ~in_1[6], in_1[7], ~in_1[8], ~in_1[9]);  // AND_Gate
  and and_3 (and_3_out, ~in_1[0], ~in_1[1], ~in_1[2], ~in_1[3], ~in_1[4], in_1[5], ~in_1[6], ~in_1[7], ~in_1[8], ~in_1[9]);  // AND_Gate
  and and_4 (and_4_out, ~in_1[0], ~in_1[1], ~in_1[2], in_1[3], ~in_1[4], ~in_1[5], ~in_1[6], ~in_1[7], ~in_1[8], ~in_1[9]);  // AND_Gate
  and and_5 (and_5_out, ~in_1[0], in_1[1], ~in_1[2], ~in_1[3], ~in_1[4], ~in_1[5], ~in_1[6], ~in_1[7], ~in_1[8], ~in_1[9]);  // AND_Gate
  or or_1 (out_2, and_1_out, and_2_out, and_3_out, and_4_out, and_5_out);
endmodule

module \_10____7_сег  (
  input  [3:0] in_1,
  output [7:0] out_2
);

  wire and_1_out, and_2_out, and_3_out, and_4_out, and_5_out, and_6_out, and_7_out, and_8_out, and_9_out,
       and_10_out, and_11_out, and_12_out, and_13_out, and_14_out, and_15_out, and_16_out, and_17_out,
       and_18_out, and_19_out, and_20_out, and_21_out, and_22_out, and_23_out, and_24_out, and_25_out,
       and_26_out, not_1_out, not_2_out, not_3_out, not_4_out, not_5_out, not_6_out, not_7_out, not_8_out,
       not_9_out, not_10_out, not_11_out, not_12_out, not_13_out, not_14_out, not_15_out, not_16_out,
       not_17_out, not_18_out, not_19_out, not_20_out, not_21_out, not_22_out, not_23_out, not_24_out,
       not_25_out, not_26_out, not_27_out, not_28_out, not_29_out, not_30_out, not_31_out, not_32_out,
       not_33_out, not_34_out, not_35_out, not_36_out, not_37_out, not_38_out, not_39_out, not_40_out,
       not_41_out, not_42_out, not_43_out, not_44_out, not_45_out, not_46_out, not_47_out, not_48_out,
       not_49_out, not_50_out, not_51_out, not_52_out;

  not not_1 (not_1_out, in_1[2]);
  not not_2 (not_2_out, in_1[1]);
  not not_3 (not_3_out, in_1[0]);
  not not_4 (not_4_out, in_1[3]);
  not not_5 (not_5_out, in_1[0]);
  not not_6 (not_6_out, in_1[3]);
  not not_7 (not_7_out, in_1[2]);
  not not_8 (not_8_out, in_1[0]);
  not not_9 (not_9_out, in_1[3]);
  not not_10 (not_10_out, in_1[2]);
  not not_11 (not_11_out, in_1[3]);
  not not_12 (not_12_out, in_1[0]);
  not not_13 (not_13_out, in_1[3]);
  not not_14 (not_14_out, in_1[1]);
  not not_15 (not_15_out, in_1[2]);
  not not_16 (not_16_out, in_1[1]);
  not not_17 (not_17_out, in_1[2]);
  not not_18 (not_18_out, in_1[1]);
  not not_19 (not_19_out, in_1[3]);
  not not_20 (not_20_out, in_1[3]);
  not not_21 (not_21_out, in_1[3]);
  not not_22 (not_22_out, in_1[2]);
  not not_23 (not_23_out, in_1[3]);
  not not_24 (not_24_out, in_1[1]);
  not not_25 (not_25_out, in_1[3]);
  not not_26 (not_26_out, in_1[0]);
  not not_27 (not_27_out, in_1[2]);
  not not_28 (not_28_out, in_1[1]);
  not not_29 (not_29_out, in_1[3]);
  not not_30 (not_30_out, in_1[1]);
  not not_31 (not_31_out, in_1[0]);
  not not_32 (not_32_out, in_1[3]);
  not not_33 (not_33_out, in_1[1]);
  not not_34 (not_34_out, in_1[3]);
  not not_35 (not_35_out, in_1[0]);
  not not_36 (not_36_out, in_1[2]);
  not not_37 (not_37_out, in_1[1]);
  not not_38 (not_38_out, in_1[3]);
  not not_39 (not_39_out, in_1[2]);
  not not_40 (not_40_out, in_1[0]);
  not not_41 (not_41_out, in_1[3]);
  not not_42 (not_42_out, in_1[3]);
  not not_43 (not_43_out, in_1[2]);
  not not_44 (not_44_out, in_1[1]);
  not not_45 (not_45_out, in_1[3]);
  not not_46 (not_46_out, in_1[2]);
  not not_47 (not_47_out, in_1[3]);
  not not_48 (not_48_out, in_1[1]);
  not not_49 (not_49_out, in_1[0]);
  not not_50 (not_50_out, in_1[2]);
  not not_51 (not_51_out, in_1[1]);
  not not_52 (not_52_out, in_1[3]);
  and and_1 (and_1_out, not_1_out, not_2_out, not_3_out);
  and and_2 (and_2_out, not_4_out, in_1[1], not_5_out);
  and and_3 (and_3_out, not_6_out, not_7_out, not_8_out);
  and and_4 (and_4_out, not_9_out, not_10_out, in_1[1]);
  and and_5 (and_5_out, not_11_out, in_1[1], not_12_out);
  and and_6 (and_6_out, not_13_out, in_1[2], not_14_out, in_1[0]);
  and and_7 (and_7_out, in_1[3], not_15_out, not_16_out);
  and and_8 (and_8_out, not_17_out, not_18_out);
  and and_9 (and_9_out, not_19_out, in_1[0]);
  and and_10 (and_10_out, not_20_out, in_1[2]);
  and and_11 (and_11_out, not_21_out, not_22_out, in_1[1]);
  and and_12 (and_12_out, not_23_out, in_1[2], not_24_out);
  and and_13 (and_13_out, not_25_out, in_1[2], not_26_out);
  and and_14 (and_14_out, in_1[3], not_27_out, not_28_out);
  and and_15 (and_15_out, not_29_out, not_30_out, not_31_out);
  and and_16 (and_16_out, not_32_out, in_1[2], not_33_out);
  and and_17 (and_17_out, not_34_out, in_1[2], not_35_out);
  and and_18 (and_18_out, in_1[3], not_36_out, not_37_out);
  and and_19 (and_19_out, not_38_out, not_39_out, not_40_out);
  and and_20 (and_20_out, not_41_out, in_1[1]);
  and and_21 (and_21_out, not_42_out, in_1[2], in_1[0]);
  and and_22 (and_22_out, in_1[3], not_43_out, not_44_out);
  and and_23 (and_23_out, not_45_out, not_46_out);
  and and_24 (and_24_out, not_47_out, not_48_out, not_49_out);
  and and_25 (and_25_out, not_50_out, not_51_out);
  and and_26 (and_26_out, not_52_out, in_1[1], in_1[0]);
  or or_1 (out_2[7], and_1_out, and_2_out);
  or or_2 (out_2[6], and_3_out, and_4_out, and_5_out, and_6_out, and_7_out);
  or or_3 (out_2[5], and_8_out, and_9_out, and_10_out);
  or or_4 (out_2[3], and_11_out, and_12_out, and_13_out, and_14_out);
  or or_5 (out_2[2], and_15_out, and_16_out, and_17_out, and_18_out);
  or or_6 (out_2[1], and_19_out, and_20_out, and_21_out, and_22_out);
  or or_7 (out_2[0], and_23_out, and_24_out, and_25_out, and_26_out);

  assign out_2[4] = 1'b0;
endmodule

module \_10____7_сег_2  (
  input  [3:0] in_1,
  output [7:0] out_2
);

  wire and_1_out, and_2_out, and_3_out, and_4_out, and_5_out, and_6_out, and_7_out, and_8_out, and_9_out,
       and_10_out, and_11_out, and_12_out, and_13_out, and_14_out, and_15_out, and_16_out, and_17_out,
       and_18_out, and_19_out, and_20_out, and_21_out, and_22_out, and_23_out, and_24_out, and_25_out,
       and_26_out, and_27_out, and_28_out, not_1_out, not_2_out, not_3_out, not_4_out, not_5_out, not_6_out,
       not_7_out, not_8_out, not_9_out, not_10_out, not_11_out, not_12_out, not_13_out, not_14_out,
       not_15_out, not_16_out, not_17_out, not_18_out, not_19_out, not_20_out, not_21_out, not_22_out,
       not_23_out, not_24_out, not_25_out, not_26_out, not_27_out, not_28_out, not_29_out, not_30_out,
       not_31_out, not_32_out, not_33_out, not_34_out, not_35_out, not_36_out, not_37_out, not_38_out,
       not_39_out, not_40_out, not_41_out, not_42_out, not_43_out, not_44_out, not_45_out, not_46_out,
       not_47_out, not_48_out, not_49_out, not_50_out, not_51_out, not_52_out, not_53_out, not_54_out,
       not_55_out, not_56_out, not_57_out, not_58_out;

  not not_1 (not_1_out, in_1[3]);
  not not_2 (not_2_out, in_1[2]);
  not not_3 (not_3_out, in_1[0]);
  not not_4 (not_4_out, in_1[2]);
  not not_5 (not_5_out, in_1[1]);
  not not_6 (not_6_out, in_1[0]);
  not not_7 (not_7_out, in_1[3]);
  not not_8 (not_8_out, in_1[0]);
  not not_9 (not_9_out, in_1[3]);
  not not_10 (not_10_out, in_1[1]);
  not not_11 (not_11_out, in_1[2]);
  not not_12 (not_12_out, in_1[1]);
  not not_13 (not_13_out, in_1[3]);
  not not_14 (not_14_out, in_1[3]);
  not not_15 (not_15_out, in_1[2]);
  not not_16 (not_16_out, in_1[1]);
  not not_17 (not_17_out, in_1[3]);
  not not_18 (not_18_out, in_1[2]);
  not not_19 (not_19_out, in_1[3]);
  not not_20 (not_20_out, in_1[1]);
  not not_21 (not_21_out, in_1[3]);
  not not_22 (not_22_out, in_1[0]);
  not not_23 (not_23_out, in_1[2]);
  not not_24 (not_24_out, in_1[1]);
  not not_25 (not_25_out, in_1[3]);
  not not_26 (not_26_out, in_1[1]);
  not not_27 (not_27_out, in_1[0]);
  not not_28 (not_28_out, in_1[3]);
  not not_29 (not_29_out, in_1[1]);
  not not_30 (not_30_out, in_1[3]);
  not not_31 (not_31_out, in_1[0]);
  not not_32 (not_32_out, in_1[2]);
  not not_33 (not_33_out, in_1[1]);
  not not_34 (not_34_out, in_1[3]);
  not not_35 (not_35_out, in_1[2]);
  not not_36 (not_36_out, in_1[0]);
  not not_37 (not_37_out, in_1[3]);
  not not_38 (not_38_out, in_1[3]);
  not not_39 (not_39_out, in_1[2]);
  not not_40 (not_40_out, in_1[1]);
  not not_41 (not_41_out, in_1[3]);
  not not_42 (not_42_out, in_1[2]);
  not not_43 (not_43_out, in_1[3]);
  not not_44 (not_44_out, in_1[1]);
  not not_45 (not_45_out, in_1[0]);
  not not_46 (not_46_out, in_1[2]);
  not not_47 (not_47_out, in_1[1]);
  not not_48 (not_48_out, in_1[3]);
  and and_1 (and_1_out, not_1_out, not_2_out, not_3_out);
  and and_2 (and_2_out, not_4_out, not_5_out, not_6_out);
  and and_3 (and_3_out, not_7_out, in_1[1], not_8_out);
  not not_49 (not_49_out, in_1[3]);
  and and_4 (and_4_out, not_49_out, not_50_out, not_51_out);
  not not_50 (not_50_out, in_1[2]);
  not not_51 (not_51_out, in_1[0]);
  not not_52 (not_52_out, in_1[3]);
  not not_53 (not_53_out, in_1[2]);
  and and_5 (and_5_out, not_52_out, not_53_out, in_1[1]);
  not not_54 (not_54_out, in_1[3]);
  and and_6 (and_6_out, not_54_out, in_1[1], not_55_out);
  not not_55 (not_55_out, in_1[0]);
  and and_7 (and_7_out, not_9_out, in_1[2], not_10_out, in_1[0]);
  and and_8 (and_8_out, in_1[3], not_56_out, not_57_out);
  not not_56 (not_56_out, in_1[2]);
  not not_57 (not_57_out, in_1[1]);
  and and_9 (and_9_out, not_11_out, not_12_out);
  and and_10 (and_10_out, not_13_out, in_1[0]);
  and and_11 (and_11_out, not_14_out, in_1[2]);
  not not_58 (not_58_out, in_1[3]);
  and and_12 (and_12_out, not_15_out, not_16_out);
  and and_13 (and_13_out, not_17_out, not_18_out, in_1[1]);
  and and_14 (and_14_out, not_19_out, in_1[2], not_20_out);
  and and_15 (and_15_out, not_21_out, in_1[2], not_22_out);
  and and_16 (and_16_out, in_1[3], not_23_out, not_24_out);
  and and_17 (and_17_out, not_25_out, not_26_out, not_27_out);
  and and_18 (and_18_out, not_28_out, in_1[2], not_29_out);
  and and_19 (and_19_out, not_30_out, in_1[2], not_31_out);
  and and_20 (and_20_out, in_1[3], not_32_out, not_33_out);
  and and_21 (and_21_out, not_34_out, not_35_out, not_36_out);
  and and_22 (and_22_out, not_37_out, in_1[1]);
  and and_23 (and_23_out, not_38_out, in_1[2], in_1[0]);
  and and_24 (and_24_out, in_1[3], not_39_out, not_40_out);
  and and_25 (and_25_out, not_41_out, not_42_out);
  and and_26 (and_26_out, not_43_out, not_44_out, not_45_out);
  and and_27 (and_27_out, not_46_out, not_47_out);
  and and_28 (and_28_out, not_48_out, in_1[1], in_1[0]);
  or or_1 (out_2[7], and_1_out, and_2_out, and_3_out);
  or or_2 (out_2[6], and_4_out, and_5_out, and_6_out, and_7_out, and_8_out);
  or or_3 (out_2[5], and_9_out, and_10_out, and_11_out);
  or or_4 (out_2[4], not_58_out, and_12_out);
  or or_5 (out_2[3], and_13_out, and_14_out, and_15_out, and_16_out);
  or or_6 (out_2[2], and_17_out, and_18_out, and_19_out, and_20_out);
  or or_7 (out_2[1], and_21_out, and_22_out, and_23_out, and_24_out);
  or or_8 (out_2[0], and_25_out, and_26_out, and_27_out, and_28_out);
endmodule

module _10____7 (
  input  [3:0] in_1,
  output [7:0] out_2
);

  wire demultiplexer_1_out0, demultiplexer_1_out1, demultiplexer_1_out2, demultiplexer_1_out3,
       demultiplexer_1_out4, demultiplexer_1_out5, demultiplexer_1_out6, demultiplexer_1_out7,
       demultiplexer_1_out8, demultiplexer_1_out9;
  wire [3:0] \перевод_в_10_ричную_1_out_11 ;

  Demultiplexer #(.select(4), .enable("false")) demultiplexer_1 (
    .out0(demultiplexer_1_out0), .out1(demultiplexer_1_out1), .out2(demultiplexer_1_out2),
    .out3(demultiplexer_1_out3), .out4(demultiplexer_1_out4), .out5(demultiplexer_1_out5),
    .out6(demultiplexer_1_out6), .out7(demultiplexer_1_out7), .out8(demultiplexer_1_out8),
    .out9(demultiplexer_1_out9), .in(1'b1), .sel(in_1));  // open: out10, out11, out12, out13, out14, out15
  // Probe on \перевод_в_10_ричную_1_out_11 
  // Probe on \перевод_в_10_ричную_1_out_11 
  \Перевод_в_10_ричную  \u_перевод_в_10_ричную_1  (
    ._0(demultiplexer_1_out0), ._1(demultiplexer_1_out1), ._2(demultiplexer_1_out2),
    ._3(demultiplexer_1_out3), ._4(demultiplexer_1_out4), ._5(demultiplexer_1_out5),
    ._6(demultiplexer_1_out6), ._7(demultiplexer_1_out7), ._8(demultiplexer_1_out8),
    ._9(demultiplexer_1_out9), .out_11(\перевод_в_10_ричную_1_out_11 ));  // open: out_12
  \_10____7_сег  \u_10_7_сег_1  (.in_1(\перевод_в_10_ричную_1_out_11 ), .out_2(out_2));
endmodule

module \Выбор  (
  input  in_1,
  input  in_2,
  output [2:0] out_3
);

  wire or_1_out, s_r_ff_1_q;

  or or_1 (or_1_out, in_1, in_2);
  S_R_Flip_Flop s_r_ff_1 (.Q(s_r_ff_1_q), .preset(in_2), .reset(in_1));  // open: S, clk, R, Qn, en
  \Работа_2_кнопок_выбора  \u_работа_2_кнопок_выбора_1  (.in_1(or_1_out), .in_2(s_r_ff_1_q), .out_3(out_3));
endmodule

module \Работа_2_кнопок_выбора  (
  input  in_1,
  input  in_2,
  output [2:0] out_3
);

  wire demultiplexer_1_out0, demultiplexer_1_out1;
  wire [2:0] \правая_кнопка_1_out_4 ;

  Demultiplexer #(.enable("false")) demultiplexer_1 (
    .out0(demultiplexer_1_out0), .out1(demultiplexer_1_out1), .in(in_1), .sel(in_2));
  \Левая_кнопка  \u_левая_кнопка_1  (
    .out_4(out_3), .in_1(demultiplexer_1_out0), .in_2(demultiplexer_1_out1), .in_3(\правая_кнопка_1_out_4 ));
  \Правая_кнопка  \u_правая_кнопка_1  (
    .in_1(demultiplexer_1_out1), .out_4(\правая_кнопка_1_out_4 ), .in_3(out_3), .in_2(demultiplexer_1_out0));
  // Probe on out_3
  // Probe on \правая_кнопка_1_out_4 
endmodule

module \Правая_кнопка  (
  input  in_1,
  input  in_2,
  input  [2:0] in_3,
  output [2:0] out_4
);

  wire and_1_out, or_1_out, \сравнение_границы_3_бит_1_out_3 ;
  wire [2:0] multiplexer_1_out;

  and and_1 (and_1_out, in_1, \сравнение_границы_3_бит_1_out_3 );
  or or_1 (or_1_out, and_1_out, in_2);
  \Улучшенный_счетчик_3_бит  \u_улучшенный_счетчик_3_бит_1  (
    .\Счет_вверх_вниз (1'b1), .Clock(in_1), .Enable(1'b1), .\Сброс (1'b0), .\Запись (or_1_out),
    .out_7(out_4), .in_6(multiplexer_1_out));
  Multiplexer #(.width(3), .enable("false")) multiplexer_1 (
    .in0(3'b000), .in1(in_3), .out(multiplexer_1_out), .sel(in_2));
  \Сравнение_границы_3_бит  \u_сравнение_границы_3_бит_1  (
    .in_1(out_4), .out_3(\сравнение_границы_3_бит_1_out_3 ), .in_2(3'b110));
endmodule

module \Левая_кнопка  (
  input  in_1,
  input  in_2,
  input  [2:0] in_3,
  output [2:0] out_4
);

  wire and_1_out, or_1_out, \сравнение_границы_3_бит_1_out_3 ;
  wire [2:0] multiplexer_1_out;

  and and_1 (and_1_out, in_1, \сравнение_границы_3_бит_1_out_3 );
  or or_1 (or_1_out, and_1_out, in_2);
  \Улучшенный_счетчик_3_бит  \u_улучшенный_счетчик_3_бит_1  (
    .\Счет_вверх_вниз (1'b0), .Clock(in_1), .Enable(1'b1), .\Сброс (1'b0), .\Запись (or_1_out),
    .out_7(out_4), .in_6(multiplexer_1_out));
  Multiplexer #(.width(3), .enable("false")) multiplexer_1 (
    .in0(3'b101), .in1(in_3), .out(multiplexer_1_out), .sel(in_2));
  \Сравнение_границы_3_бит  \u_сравнение_границы_3_бит_1  (
    .in_1(out_4), .out_3(\сравнение_границы_3_бит_1_out_3 ), .in_2(3'b111));
endmodule
